// Logisim project cpu21-riscv.circ as structural Verilog: 24 circuits, main circuit ◇单周期RISC-V
module \单周期RISC_V  (
  input  IR1,
  input  IR2,
  input  IR3,
  output RegWrite,
  output MemWrite,
  output [31:0] PC,
  output [31:0] IR,
  output [31:0] RDin,
  output [31:0] MDin,
  output [31:0] LedData,
  output [31:0] out_11
);

  wire ALUequal, ALUless, AluSrcBS, and_1_out, and_2_out, and_3_out, and_4_out, and_5_out, BEQS, BES, BLTUS,
       BNES, CLK, clock_1_out, comparator_1_eq, comparator_2_eq, comparator_2_lt, d_ff_1_q, ecall, Go, halt,
       IR1_t, IR2_t, IR3_t, IRA, IRB, IRC, JALRS, JALS, LBUS, MemToRegS, nand_1_out, not_1_out, not_2_out,
       not_3_out, not_4_out, or_5_out, RST, Stype, URETS, W1, W2, W3;
  wire [3:0] AluOPS;
  wire [4:0] multiplexer_1_out, multiplexer_2_out;
  wire [7:0] multiplexer_6_out;
  wire [11:0] multiplexer_3_out;
  wire [12:0] CNT_num;
  wire [15:0] \总周期数 ;
  wire [31:0] ALURet, BEADDR, bit_extender_1_out, bit_extender_2_out, bit_extender_3_out, bit_extender_4_out,
       JALADDR, multiplexer_4_out, multiplexer_5_out, multiplexer_7_out, multiplexer_10_out,
       multiplexer_11_out, PCP4, R1, ram_1_data, shifter_1_out, shifter_2_out;

  Button \u_继续运行  (.out(Go));
  Button _1 (.out(IRA));
  Button _2 (.out(IRB));
  Button _3 (.out(IRC));
  LED #(.active("true")) led_1 (.in(W1));
  LED #(.active("true")) led_2 (.in(W2));
  LED #(.active("true")) led_3 (.in(W3));
  Hex_Digit_Display hex_digit_display_1 (.value(LedData[31:28]));  // open: dp
  Register #(.width(32), .trigger("rising"), .Select("low")) u_PC (
    .D(out_11), .en(not_1_out), .Q(PC), .clk(CLK), .clr(RST));
  not not_1 (not_1_out, halt);
  not not_2 (not_2_out, ecall);
  Hex_Digit_Display hex_digit_display_2 (.value(LedData[27:24]));  // open: dp
  Hex_Digit_Display hex_digit_display_3 (.value(LedData[23:20]));  // open: dp
  Counter #(.width(16), .max('hffff), .ongoal("wrap"), .trigger("rising"), .behavior("new")) counter_1 (
    .D({16{1'b0}}), .count(not_2_out), .Q(\总周期数 ), .clk(CLK));  // open: load, carry, clr, preset, down
  Hex_Digit_Display hex_digit_display_4 (.value(LedData[19:16]));  // open: dp
  Hex_Digit_Display hex_digit_display_5 (.value(LedData[15:12]));  // open: dp
  Adder #(.width(32)) adder_1 (.a(PC), .b(32'h4), .out(PCP4));  // open: cin, cout
  Hex_Digit_Display hex_digit_display_6 (.value(LedData[11:8]));  // open: dp
  Hex_Digit_Display hex_digit_display_7 (.value(LedData[7:4]));  // open: dp
  // Probe on \总周期数 
  // RiscV_Probe riscv_probe_1: pin names not known; wires that end beside it: IR
  ROM #(.addrWidth(10), .dataWidth(32), .Select("high")) rom_1 (.addr(PC[11:2]), .data(IR));
  Hex_Digit_Display hex_digit_display_8 (.value(LedData[3:0]));  // open: dp
  \单周期硬布线控制器  \u_单周期硬布线控制器_1  (
    .Funct({IR[30], IR[25], IR[14:12]}), .OP(IR[6:2]), .ALU_OP(AluOPS), .MemToReg(MemToRegS),
    .MemWrite(MemWrite), .ALU_SRC(AluSrcBS), .ecall(ecall), .S_type(Stype), .Jalr(JALRS), .Beq(BEQS),
    .JAL(JALS), .Bne(BNES), .in_3(IR[21]), .uret(URETS), .LBU(LBUS), .BLTU(BLTUS), .RegWrite(RegWrite));  // open: RSread, RTread, CSC
  Multiplexer #(.select(1), .width(5), .disabled("Z"), .enable("false")) multiplexer_1 (
    .in0(IR[19:15]), .in1(5'b10001), .out(multiplexer_1_out), .sel(ecall));
  Multiplexer #(.select(1), .width(5), .disabled("Z"), .enable("false")) multiplexer_2 (
    .in0(IR[24:20]), .in1(5'b01010), .out(multiplexer_2_out), .sel(ecall));
  Multiplexer #(.select(1), .width(12), .disabled("Z"), .enable("false")) multiplexer_3 (
    .in0(IR[31:20]), .in1({IR[31:25], IR[11:7]}), .out(multiplexer_3_out), .sel(Stype));
  or or_1 (IR1_t, IR1, IRA);
  or or_2 (IR2_t, IR2, IRB);
  assign bit_extender_1_out = {{20{multiplexer_3_out[11]}}, multiplexer_3_out};  // Bit_Extender bit_extender_1
  assign bit_extender_2_out = {{20{IR[31]}}, {IR[31], IR[7], IR[30:25], IR[11:8]}};  // Bit_Extender bit_extender_2
  assign bit_extender_3_out = {{12{IR[31]}}, {IR[31], IR[19:12], IR[20], IR[30:21]}};  // Bit_Extender bit_extender_3
  Regifile regifile_1 (
    .Din(RDin), .Clk(CLK), .R1(R1), .R2(MDin), .WE(RegWrite), .W_num(IR[11:7]), .R1_num(multiplexer_1_out),
    .R2_num(multiplexer_2_out));
  Shifter #(.width(32), .shift("ll")) shifter_1 (.in(bit_extender_2_out), .\dist (5'b00001), .out(shifter_1_out));
  Shifter #(.width(32), .shift("ll")) shifter_2 (.in(bit_extender_3_out), .\dist (5'b00001), .out(shifter_2_out));
  or or_3 (IR3_t, IR3, IRC);
  Adder #(.width(32)) adder_2 (.a(shifter_1_out), .b(PC), .out(BEADDR), .cin(1'b0));  // open: cout
  Adder #(.width(32)) adder_3 (.a(shifter_2_out), .b(PC), .out(JALADDR), .cin(1'b0));  // open: cout
  Multiplexer #(.select(1), .width(32), .disabled("Z"), .enable("false")) multiplexer_4 (
    .in0(MDin), .in1(bit_extender_1_out), .out(multiplexer_4_out), .sel(AluSrcBS));
  and and_1 (and_1_out, ALUequal, BEQS);
  not not_3 (not_3_out, ALUequal);
  and and_2 (and_2_out, not_3_out, BNES);
  and and_3 (and_3_out, ALUless, BLTUS);
  ALU alu_1 (
    .X(R1), .Y(multiplexer_4_out), .AluOP(AluOPS), .Equal(ALUequal), .Result(ALURet), .out_6(ALUless));  // open: Result_2, out_4
  or or_4 (BES, and_1_out, and_2_out, and_3_out);
  Comparator #(.width(32), .mode("twosComplement")) comparator_1 (
    .a(R1), .b(32'h22), .eq(comparator_1_eq));  // open: gt, lt
  RAM #(.addrWidth(10), .dataWidth(32), .bus("separate"), .Select("high")) ram_1 (
    .addr(ALURet[11:2]), .din(MDin), .data(ram_1_data), .str(MemWrite), .clk(CLK));  // open: sel, ld, clr
  Multiplexer #(.select(1), .width(32), .disabled("Z"), .enable("false")) multiplexer_5 (
    .in0(PCP4), .in1(BEADDR), .out(multiplexer_5_out), .sel(BES));
  not not_4 (not_4_out, comparator_1_eq);
  and and_4 (and_4_out, comparator_1_eq, ecall);
  D_Flip_Flop #(.trigger("high"), .Pre_Clr_Positions("LEGACY"), .NegatePresetClear("false"), .enable("true"), .NewFFLayout("false")) d_ff_1 (.Q(d_ff_1_q));  // open: clk, D, Qn, preset, en, reset
  // Probe on 13'h29a
  Multiplexer #(.select(2), .width(8), .disabled("Z"), .enable("false")) multiplexer_6 (
    .in0(ram_1_data[7:0]), .in1(ram_1_data[15:8]), .in2(ram_1_data[23:16]), .in3(ram_1_data[31:24]),
    .out(multiplexer_6_out), .sel(ALURet[1:0]));
  Multiplexer #(.select(1), .width(32), .disabled("Z"), .enable("false")) multiplexer_7 (
    .in0(multiplexer_5_out), .in1(JALADDR), .out(multiplexer_7_out), .sel(JALS));
  and and_5 (and_5_out, not_4_out, ecall);
  Multiplexer #(.select(1), .width(1), .disabled("Z"), .enable("false")) multiplexer_8 (
    .in0(and_5_out), .in1(1'b0), .out(halt), .sel(Go));
  Register #(.width(32), .trigger("rising"), .Select("low")) register_1 (
    .D(MDin), .en(and_4_out), .Q(LedData), .clk(CLK));  // open: clr
  Comparator #(.width(13), .mode("twosComplement")) comparator_2 (
    .a(CNT_num), .b(13'h29a), .eq(comparator_2_eq), .lt(comparator_2_lt));  // open: gt
  Clock #(.highDuration(1), .lowDuration(1)) clock_1 (.out(clock_1_out));
  assign bit_extender_4_out = {{24{1'b0}}, multiplexer_6_out};  // Bit_Extender bit_extender_4
  Multiplexer #(.select(1), .width(32), .disabled("Z"), .enable("false")) multiplexer_9 (
    .in0(multiplexer_7_out), .in1(ALURet), .out(out_11), .sel(JALRS));
  Counter #(.width(13), .max('h1fff), .ongoal("stay"), .trigger("rising"), .behavior("old")) counter_2 (
    .count(comparator_2_lt), .Q(CNT_num), .clk(clock_1_out));  // open: load, D, carry, clr, preset
  nand nand_1 (nand_1_out, d_ff_1_q, comparator_2_eq);
  Multiplexer #(.select(1), .width(32), .disabled("Z"), .enable("false")) multiplexer_10 (
    .in0(ram_1_data), .in1(bit_extender_4_out), .out(multiplexer_10_out), .sel(LBUS));
  assign CLK = nand_1_out ? clock_1_out : 1'bz;  // Controlled_Buffer controlled_buffer_1
  Pull_Resistor #(.pull(1)) pull_resistor_1 (.node(CLK));
  Multiplexer #(.select(1), .width(32), .disabled("Z"), .enable("false")) multiplexer_11 (
    .in0(ALURet), .in1(multiplexer_10_out), .out(multiplexer_11_out), .sel(MemToRegS));
  or or_5 (or_5_out, JALS, JALRS);
  Multiplexer #(.select(1), .width(32), .disabled("Z"), .enable("false")) multiplexer_12 (
    .in0(multiplexer_11_out), .in1(PCP4), .out(RDin), .sel(or_5_out));

  // Other names for the same wires on the sheet: PCADDR[31:0] = out_11; R2[31:0] = MDin

  // Notes on the sheet:
  //   中断源
  //   中断等待指示
  //   数码管输出应该用寄存器锁存，否则显示数据只能一闪而过
  //   数码管输出
  //   指令探针
  //   指令存储器
  //   contents of rom_1 (hex, n*v repeats v):
  //   ff100493 900533 2200893 73 148493 fe9068e3 900533 2200893 73 a00893 73
  //   指令字
  //   JAL
  //   JALR
  //   URET
  //   Beq
  //   Bne
  //   AluOP
  //   AluSrcB
  //   RegWrite
  //   MemToReg
  //   MemWrite
  //   为方便自动评测，需要输出PC，IR，寄存器堆写如数据RDin
  //   RAM写使能MemWrite、RAM写入数据MDin等信号
  //   控制位
  //   暂停节拍，不能为0
  //   戳工具置1进入计数暂停模式，ctrl+k时钟自动运行到对应节拍暂停
  //   ctrl+k关闭时钟连续运行，将控制位置零，进入单步调试模式调试
  //   用这个时钟源需要去掉电路中的其他时钟源
  //   可计数暂停的时钟源
endmodule

// 单周期硬布线控制器
module \单周期硬布线控制器  (
  input  [4:0] OP,
  input  [4:0] Funct,
  input  in_3,
  output [3:0] ALU_OP,
  output uret,
  output MemToReg,
  output CSC,
  output BLTU,
  output MemWrite,
  output ecall,
  output ALU_SRC,
  output LBU,
  output RSread,
  output RegWrite,
  output RTread,
  output S_type,
  output Beq,
  output Bne,
  output Jalr,
  output JAL
);

  wire \控制信号自动生成_1_ecall ;

  \运算控制器自动生成  \u_运算控制器自动生成_1  (
    .OP2(OP[0]), .OP3(OP[1]), .OP4(OP[2]), .OP5(OP[3]), .OP6(OP[4]), .F12(Funct[0]), .F13(Funct[1]),
    .F14(Funct[2]), .F25(Funct[3]), .F30(Funct[4]), .S0(ALU_OP[0]), .S1(ALU_OP[1]), .S2(ALU_OP[2]),
    .S3(ALU_OP[3]));
  \控制信号自动生成  \u_控制信号自动生成_1  (
    .OP2(OP[0]), .OP3(OP[1]), .OP4(OP[2]), .OP5(OP[3]), .OP6(OP[4]), .MemToReg(MemToReg), .F12(Funct[0]),
    .F13(Funct[1]), .F14(Funct[2]), .F25(Funct[3]), .F30(Funct[4]), .BLTU(BLTU), .MemWrite(MemWrite),
    .ALU_SRC(ALU_SRC), .LBU(LBU), .CSC(CSC), .RSread(RSread), .RegWrite(RegWrite), .RTread(RTread),
    .ecall(\控制信号自动生成_1_ecall ), .S_Type(S_type), .BEQ(Beq), .BNE(Bne), .JALR(Jalr), .JAL(JAL));
  and and_1 (uret, in_3, \控制信号自动生成_1_ecall );
  and and_2 (ecall, ~in_3, \控制信号自动生成_1_ecall );  // AND_Gate

  // Other names for the same wires on the sheet: IR21 = in_3; OP_CODE[4:0] = OP

  // Notes on the sheet:
  //   运算器控制器，根据指令生成运算器功能选择信号
  //   控制信号生成，产生数据通路需要的其他控制信号
endmodule

// 运算器控制器
module \运算控制器自动生成  (
  input  OP2,
  input  OP3,
  input  OP4,
  input  OP5,
  input  OP6,
  input  F12,
  input  F13,
  input  F14,
  input  F25,
  input  F30,
  output S0,
  output S1,
  output S2,
  output S3
);

  wire and_1_out, and_2_out, and_3_out, and_4_out, and_5_out, and_6_out, and_7_out, and_8_out, and_9_out,
       and_10_out, and_11_out, and_12_out, and_13_out, and_14_out, and_15_out, and_16_out, and_17_out,
       and_18_out, and_19_out, and_20_out, and_21_out, and_22_out, and_23_out, and_24_out, and_25_out,
       and_26_out, and_27_out, and_28_out, and_29_out, and_30_out, and_31_out, and_32_out, and_33_out,
       and_34_out, and_35_out, and_36_out, and_37_out, and_38_out, not_1_out, not_2_out, not_3_out,
       not_4_out, not_5_out, not_6_out, not_7_out, not_8_out, not_9_out, not_10_out, not_11_out, not_12_out,
       not_13_out, not_14_out, not_15_out, not_16_out, not_17_out, not_18_out, not_19_out, not_20_out,
       not_21_out, not_22_out, not_23_out, not_24_out, not_25_out, not_26_out, not_27_out, not_28_out,
       not_29_out, not_30_out, not_31_out, not_32_out, not_33_out, not_34_out, not_35_out, not_36_out,
       not_37_out, not_38_out, not_39_out, not_40_out, not_41_out, not_42_out, not_43_out, not_44_out,
       not_45_out, not_46_out, not_47_out, not_48_out, not_49_out, not_50_out, not_51_out, not_52_out,
       not_53_out, not_54_out, not_55_out, not_56_out, not_57_out, not_58_out, not_59_out, not_60_out,
       not_61_out, not_62_out, not_63_out, not_64_out, not_65_out, not_66_out, not_67_out, not_68_out,
       not_69_out, not_70_out, not_71_out, not_72_out, not_73_out, not_74_out, not_75_out, not_76_out,
       not_77_out, not_78_out, not_79_out, not_80_out, not_81_out, not_82_out, not_83_out, not_84_out,
       not_85_out, not_86_out, not_87_out, not_88_out, not_89_out, not_90_out, not_91_out, not_92_out,
       not_93_out, not_94_out, not_95_out, not_96_out, not_97_out, not_98_out, not_99_out, not_100_out,
       not_101_out, not_102_out, not_103_out, not_104_out, not_105_out, not_106_out, not_107_out,
       not_108_out, not_109_out, not_110_out, not_111_out, not_112_out, not_113_out, not_114_out,
       not_115_out, not_116_out, not_117_out, not_118_out, not_119_out, not_120_out, not_121_out,
       not_122_out, not_123_out, not_124_out, not_125_out, not_126_out, not_127_out, not_128_out,
       not_129_out, not_130_out, not_131_out, not_132_out, not_133_out, not_134_out, not_135_out,
       not_136_out, not_137_out, not_138_out, not_139_out, not_140_out, not_141_out, not_142_out,
       not_143_out, not_144_out, not_145_out, not_146_out, not_147_out, not_148_out, not_149_out,
       not_150_out, not_151_out, not_152_out, not_153_out, not_154_out, not_155_out, not_156_out,
       not_157_out, not_158_out, not_159_out, not_160_out, not_161_out, not_162_out, not_163_out,
       not_164_out, not_165_out, not_166_out, not_167_out, not_168_out, not_169_out, not_170_out,
       not_171_out, not_172_out, not_173_out, not_174_out, not_175_out, not_176_out, not_177_out,
       not_178_out, not_179_out, not_180_out, not_181_out, not_182_out, not_183_out, not_184_out,
       not_185_out, not_186_out, not_187_out, not_188_out, not_189_out, not_190_out, not_191_out,
       not_192_out, not_193_out, not_194_out, not_195_out, not_196_out, not_197_out, not_198_out,
       not_199_out, not_200_out, not_201_out, not_202_out, not_203_out, not_204_out, not_205_out,
       not_206_out, not_207_out, not_208_out, not_209_out, not_210_out, not_211_out, not_212_out,
       not_213_out, not_214_out, not_215_out, not_216_out, not_217_out, not_218_out, not_219_out,
       not_220_out, not_221_out, not_222_out, not_223_out, not_224_out, not_225_out, not_226_out;

  not not_1 (not_1_out, F30);
  not not_2 (not_2_out, F25);
  not not_3 (not_3_out, F14);
  not not_4 (not_4_out, F13);
  not not_5 (not_5_out, F12);
  not not_6 (not_6_out, OP6);
  not not_7 (not_7_out, OP3);
  not not_8 (not_8_out, OP2);
  not not_9 (not_9_out, F30);
  not not_10 (not_10_out, F25);
  not not_11 (not_11_out, OP6);
  not not_12 (not_12_out, OP3);
  not not_13 (not_13_out, OP2);
  not not_14 (not_14_out, F30);
  not not_15 (not_15_out, F25);
  not not_16 (not_16_out, F14);
  not not_17 (not_17_out, F12);
  not not_18 (not_18_out, OP6);
  not not_19 (not_19_out, OP3);
  not not_20 (not_20_out, OP2);
  not not_21 (not_21_out, F14);
  not not_22 (not_22_out, F13);
  not not_23 (not_23_out, F12);
  not not_24 (not_24_out, OP6);
  not not_25 (not_25_out, OP5);
  not not_26 (not_26_out, OP3);
  not not_27 (not_27_out, OP2);
  not not_28 (not_28_out, OP6);
  not not_29 (not_29_out, OP5);
  not not_30 (not_30_out, OP3);
  not not_31 (not_31_out, OP2);
  not not_32 (not_32_out, F13);
  not not_33 (not_33_out, F12);
  not not_34 (not_34_out, OP6);
  not not_35 (not_35_out, OP5);
  not not_36 (not_36_out, OP3);
  not not_37 (not_37_out, OP2);
  not not_38 (not_38_out, F14);
  not not_39 (not_39_out, F12);
  not not_40 (not_40_out, OP6);
  not not_41 (not_41_out, OP5);
  not not_42 (not_42_out, OP3);
  not not_43 (not_43_out, OP2);
  not not_44 (not_44_out, F25);
  not not_45 (not_45_out, F13);
  not not_46 (not_46_out, OP6);
  not not_47 (not_47_out, OP5);
  not not_48 (not_48_out, OP3);
  not not_49 (not_49_out, OP2);
  not not_50 (not_50_out, F14);
  not not_51 (not_51_out, F12);
  not not_52 (not_52_out, OP6);
  not not_53 (not_53_out, OP5);
  not not_54 (not_54_out, OP4);
  not not_55 (not_55_out, OP3);
  not not_56 (not_56_out, OP2);
  not not_57 (not_57_out, F14);
  not not_58 (not_58_out, F12);
  not not_59 (not_59_out, OP6);
  not not_60 (not_60_out, OP4);
  not not_61 (not_61_out, OP3);
  not not_62 (not_62_out, OP2);
  not not_63 (not_63_out, F14);
  not not_64 (not_64_out, F13);
  not not_65 (not_65_out, F12);
  not not_66 (not_66_out, OP4);
  not not_67 (not_67_out, OP3);
  not not_68 (not_68_out, F13);
  not not_69 (not_69_out, F12);
  not not_70 (not_70_out, OP6);
  not not_71 (not_71_out, OP5);
  not not_72 (not_72_out, OP4);
  not not_73 (not_73_out, OP3);
  not not_74 (not_74_out, OP2);
  not not_75 (not_75_out, F25);
  not not_76 (not_76_out, F14);
  not not_77 (not_77_out, F13);
  not not_78 (not_78_out, F12);
  not not_79 (not_79_out, OP6);
  not not_80 (not_80_out, OP3);
  not not_81 (not_81_out, OP2);
  not not_82 (not_82_out, F30);
  not not_83 (not_83_out, F25);
  not not_84 (not_84_out, OP6);
  not not_85 (not_85_out, OP3);
  not not_86 (not_86_out, OP2);
  not not_87 (not_87_out, F30);
  not not_88 (not_88_out, F25);
  not not_89 (not_89_out, F14);
  not not_90 (not_90_out, F12);
  not not_91 (not_91_out, OP6);
  not not_92 (not_92_out, OP3);
  not not_93 (not_93_out, OP2);
  not not_94 (not_94_out, OP6);
  not not_95 (not_95_out, OP5);
  not not_96 (not_96_out, OP3);
  not not_97 (not_97_out, OP2);
  not not_98 (not_98_out, F14);
  not not_99 (not_99_out, F12);
  not not_100 (not_100_out, OP6);
  not not_101 (not_101_out, OP5);
  not not_102 (not_102_out, OP3);
  not not_103 (not_103_out, OP2);
  not not_104 (not_104_out, F30);
  not not_105 (not_105_out, F25);
  not not_106 (not_106_out, F13);
  not not_107 (not_107_out, OP6);
  not not_108 (not_108_out, OP5);
  not not_109 (not_109_out, OP3);
  not not_110 (not_110_out, OP2);
  not not_111 (not_111_out, F30);
  not not_112 (not_112_out, F25);
  not not_113 (not_113_out, F14);
  not not_114 (not_114_out, F13);
  not not_115 (not_115_out, F12);
  not not_116 (not_116_out, OP6);
  not not_117 (not_117_out, OP3);
  not not_118 (not_118_out, OP2);
  not not_119 (not_119_out, F25);
  not not_120 (not_120_out, F14);
  not not_121 (not_121_out, F13);
  not not_122 (not_122_out, F12);
  not not_123 (not_123_out, OP6);
  not not_124 (not_124_out, OP3);
  not not_125 (not_125_out, OP2);
  not not_126 (not_126_out, F30);
  not not_127 (not_127_out, F25);
  not not_128 (not_128_out, OP6);
  not not_129 (not_129_out, OP3);
  not not_130 (not_130_out, OP2);
  not not_131 (not_131_out, F30);
  not not_132 (not_132_out, F25);
  not not_133 (not_133_out, F14);
  not not_134 (not_134_out, OP6);
  not not_135 (not_135_out, OP3);
  not not_136 (not_136_out, OP2);
  not not_137 (not_137_out, F14);
  not not_138 (not_138_out, F13);
  not not_139 (not_139_out, F12);
  not not_140 (not_140_out, OP6);
  not not_141 (not_141_out, OP5);
  not not_142 (not_142_out, OP3);
  not not_143 (not_143_out, OP2);
  not not_144 (not_144_out, OP6);
  not not_145 (not_145_out, OP5);
  not not_146 (not_146_out, OP3);
  not not_147 (not_147_out, OP2);
  not not_148 (not_148_out, F14);
  not not_149 (not_149_out, F12);
  not not_150 (not_150_out, OP6);
  not not_151 (not_151_out, OP5);
  not not_152 (not_152_out, OP4);
  not not_153 (not_153_out, OP3);
  not not_154 (not_154_out, OP2);
  not not_155 (not_155_out, F14);
  not not_156 (not_156_out, F12);
  not not_157 (not_157_out, OP6);
  not not_158 (not_158_out, OP4);
  not not_159 (not_159_out, OP3);
  not not_160 (not_160_out, OP2);
  not not_161 (not_161_out, F14);
  not not_162 (not_162_out, F13);
  not not_163 (not_163_out, F12);
  not not_164 (not_164_out, OP4);
  not not_165 (not_165_out, OP3);
  not not_166 (not_166_out, F14);
  not not_167 (not_167_out, OP6);
  not not_168 (not_168_out, OP5);
  not not_169 (not_169_out, OP3);
  not not_170 (not_170_out, OP2);
  not not_171 (not_171_out, F13);
  not not_172 (not_172_out, F12);
  not not_173 (not_173_out, OP6);
  not not_174 (not_174_out, OP5);
  not not_175 (not_175_out, OP4);
  not not_176 (not_176_out, OP3);
  not not_177 (not_177_out, OP2);
  not not_178 (not_178_out, F12);
  not not_179 (not_179_out, OP4);
  not not_180 (not_180_out, OP3);
  not not_181 (not_181_out, OP2);
  not not_182 (not_182_out, F30);
  not not_183 (not_183_out, F25);
  not not_184 (not_184_out, F12);
  not not_185 (not_185_out, OP6);
  not not_186 (not_186_out, OP3);
  not not_187 (not_187_out, OP2);
  not not_188 (not_188_out, F30);
  not not_189 (not_189_out, F25);
  not not_190 (not_190_out, F14);
  not not_191 (not_191_out, F12);
  not not_192 (not_192_out, OP6);
  not not_193 (not_193_out, OP3);
  not not_194 (not_194_out, OP2);
  not not_195 (not_195_out, F30);
  not not_196 (not_196_out, F25);
  not not_197 (not_197_out, F14);
  not not_198 (not_198_out, OP6);
  not not_199 (not_199_out, OP3);
  not not_200 (not_200_out, OP2);
  not not_201 (not_201_out, F12);
  not not_202 (not_202_out, OP6);
  not not_203 (not_203_out, OP5);
  not not_204 (not_204_out, OP3);
  not not_205 (not_205_out, OP2);
  not not_206 (not_206_out, F13);
  not not_207 (not_207_out, F12);
  not not_208 (not_208_out, OP6);
  not not_209 (not_209_out, OP5);
  not not_210 (not_210_out, OP3);
  not not_211 (not_211_out, OP2);
  not not_212 (not_212_out, F14);
  not not_213 (not_213_out, F12);
  not not_214 (not_214_out, OP6);
  not not_215 (not_215_out, OP5);
  not not_216 (not_216_out, OP3);
  not not_217 (not_217_out, OP2);
  not not_218 (not_218_out, F14);
  not not_219 (not_219_out, OP6);
  not not_220 (not_220_out, OP5);
  not not_221 (not_221_out, OP3);
  not not_222 (not_222_out, OP2);
  not not_223 (not_223_out, F12);
  not not_224 (not_224_out, OP4);
  not not_225 (not_225_out, OP3);
  not not_226 (not_226_out, OP2);
  and and_1 (and_1_out, not_1_out, not_2_out, not_3_out, not_4_out, not_5_out, not_6_out, OP5, OP4, not_7_out, not_8_out);
  and and_2 (and_2_out, not_9_out, not_10_out, F14, F13, F12, not_11_out, OP5, OP4, not_12_out, not_13_out);
  and and_3 (and_3_out, not_14_out, not_15_out, not_16_out, F13, not_17_out, not_18_out, OP5, OP4, not_19_out, not_20_out);
  and and_4 (and_4_out, not_21_out, not_22_out, not_23_out, not_24_out, not_25_out, OP4, not_26_out, not_27_out);
  and and_5 (and_5_out, F14, F13, F12, not_28_out, not_29_out, OP4, not_30_out, not_31_out);
  and and_6 (and_6_out, F14, not_32_out, not_33_out, not_34_out, not_35_out, OP4, not_36_out, not_37_out);
  and and_7 (and_7_out, not_38_out, F13, not_39_out, not_40_out, not_41_out, OP4, not_42_out, not_43_out);
  and and_8 (and_8_out, F30, not_44_out, F14, not_45_out, F12, not_46_out, not_47_out, OP4, not_48_out, not_49_out);
  and and_9 (and_9_out, not_50_out, F13, not_51_out, not_52_out, not_53_out, not_54_out, not_55_out, not_56_out);
  and and_10 (and_10_out, not_57_out, F13, not_58_out, not_59_out, OP5, not_60_out, not_61_out, not_62_out);
  and and_11 (and_11_out, not_63_out, not_64_out, not_65_out, OP6, OP5, not_66_out, not_67_out, OP2);
  and and_12 (and_12_out, F14, not_68_out, not_69_out, not_70_out, not_71_out, not_72_out, not_73_out, not_74_out);
  and and_13 (and_13_out, F30, not_75_out, not_76_out, not_77_out, not_78_out, not_79_out, OP5, OP4, not_80_out, not_81_out);
  and and_14 (and_14_out, not_82_out, not_83_out, F14, F13, F12, not_84_out, OP5, OP4, not_85_out, not_86_out);
  and and_15 (and_15_out, not_87_out, not_88_out, not_89_out, F13, not_90_out, not_91_out, OP5, OP4, not_92_out, not_93_out);
  and and_16 (and_16_out, F14, F13, F12, not_94_out, not_95_out, OP4, not_96_out, not_97_out);
  and and_17 (and_17_out, not_98_out, F13, not_99_out, not_100_out, not_101_out, OP4, not_102_out, not_103_out);
  and and_18 (and_18_out, not_104_out, not_105_out, F14, not_106_out, F12, not_107_out, not_108_out, OP4, not_109_out, not_110_out);
  and and_19 (and_19_out, not_111_out, not_112_out, not_113_out, not_114_out, not_115_out, not_116_out, OP5, OP4, not_117_out, not_118_out);
  and and_20 (and_20_out, F30, not_119_out, not_120_out, not_121_out, not_122_out, not_123_out, OP5, OP4, not_124_out, not_125_out);
  and and_21 (and_21_out, not_126_out, not_127_out, F14, F13, F12, not_128_out, OP5, OP4, not_129_out, not_130_out);
  and and_22 (and_22_out, not_131_out, not_132_out, not_133_out, F13, F12, not_134_out, OP5, OP4, not_135_out, not_136_out);
  and and_23 (and_23_out, not_137_out, not_138_out, not_139_out, not_140_out, not_141_out, OP4, not_142_out, not_143_out);
  and and_24 (and_24_out, F14, F13, F12, not_144_out, not_145_out, OP4, not_146_out, not_147_out);
  and and_25 (and_25_out, not_148_out, F13, not_149_out, not_150_out, not_151_out, not_152_out, not_153_out, not_154_out);
  and and_26 (and_26_out, not_155_out, F13, not_156_out, not_157_out, OP5, not_158_out, not_159_out, not_160_out);
  and and_27 (and_27_out, not_161_out, not_162_out, not_163_out, OP6, OP5, not_164_out, not_165_out, OP2);
  and and_28 (and_28_out, not_166_out, F13, F12, not_167_out, not_168_out, OP4, not_169_out, not_170_out);
  and and_29 (and_29_out, F14, not_171_out, not_172_out, not_173_out, not_174_out, not_175_out, not_176_out, not_177_out);
  and and_30 (and_30_out, F14, F13, not_178_out, OP6, OP5, not_179_out, not_180_out, not_181_out);
  and and_31 (and_31_out, not_182_out, not_183_out, F14, F13, not_184_out, not_185_out, OP5, OP4, not_186_out, not_187_out);
  and and_32 (and_32_out, not_188_out, not_189_out, not_190_out, F13, not_191_out, not_192_out, OP5, OP4, not_193_out, not_194_out);
  and and_33 (and_33_out, not_195_out, not_196_out, not_197_out, F13, F12, not_198_out, OP5, OP4, not_199_out, not_200_out);
  and and_34 (and_34_out, F14, F13, not_201_out, not_202_out, not_203_out, OP4, not_204_out, not_205_out);
  and and_35 (and_35_out, F14, not_206_out, not_207_out, not_208_out, not_209_out, OP4, not_210_out, not_211_out);
  and and_36 (and_36_out, not_212_out, F13, not_213_out, not_214_out, not_215_out, OP4, not_216_out, not_217_out);
  and and_37 (and_37_out, not_218_out, F13, F12, not_219_out, not_220_out, OP4, not_221_out, not_222_out);
  and and_38 (and_38_out, F14, F13, not_223_out, OP6, OP5, not_224_out, not_225_out, not_226_out);
  or or_1 (S0, and_1_out, and_2_out, and_3_out, and_4_out, and_5_out, and_6_out, and_7_out, and_8_out, and_9_out, and_10_out, and_11_out, and_12_out);
  or or_2 (S1, and_13_out, and_14_out, and_15_out, and_16_out, and_17_out, and_18_out);
  or or_3 (S2, and_19_out, and_20_out, and_21_out, and_22_out, and_23_out, and_24_out, and_25_out, and_26_out, and_27_out, and_28_out, and_29_out, and_30_out);
  or or_4 (S3, and_31_out, and_32_out, and_33_out, and_34_out, and_35_out, and_36_out, and_37_out, and_38_out);
endmodule

// 控制信号生成
module \控制信号自动生成  (
  input  OP2,
  input  OP3,
  input  OP4,
  input  OP5,
  input  OP6,
  input  F12,
  input  F13,
  input  F14,
  input  F25,
  input  F30,
  output MemToReg,
  output BLTU,
  output MemWrite,
  output ALU_SRC,
  output LBU,
  output CSC,
  output RSread,
  output RegWrite,
  output RTread,
  output ecall,
  output S_Type,
  output BEQ,
  output BNE,
  output JALR,
  output JAL
);

  wire and_1_out, and_2_out, and_5_out, and_6_out, and_7_out, and_8_out, and_9_out, and_10_out, and_11_out,
       and_13_out, and_14_out, and_15_out, and_16_out, and_17_out, and_18_out, and_19_out, and_20_out,
       and_21_out, and_22_out, and_23_out, and_24_out, and_25_out, and_26_out, and_27_out, and_28_out,
       and_29_out, and_30_out, and_31_out, and_32_out, and_33_out, and_34_out, and_35_out, and_36_out,
       and_37_out, and_38_out, and_39_out, and_40_out, and_41_out, and_42_out, and_43_out, and_44_out,
       not_1_out, not_2_out, not_3_out, not_4_out, not_5_out, not_6_out, not_7_out, not_8_out, not_9_out,
       not_10_out, not_11_out, not_12_out, not_13_out, not_14_out, not_15_out, not_16_out, not_17_out,
       not_18_out, not_19_out, not_20_out, not_21_out, not_22_out, not_23_out, not_24_out, not_25_out,
       not_26_out, not_27_out, not_28_out, not_29_out, not_30_out, not_31_out, not_32_out, not_33_out,
       not_34_out, not_35_out, not_36_out, not_37_out, not_38_out, not_39_out, not_40_out, not_41_out,
       not_42_out, not_43_out, not_44_out, not_45_out, not_46_out, not_47_out, not_48_out, not_49_out,
       not_50_out, not_51_out, not_52_out, not_53_out, not_54_out, not_55_out, not_56_out, not_57_out,
       not_58_out, not_59_out, not_60_out, not_61_out, not_62_out, not_63_out, not_64_out, not_65_out,
       not_66_out, not_67_out, not_68_out, not_69_out, not_70_out, not_71_out, not_72_out, not_73_out,
       not_74_out, not_75_out, not_76_out, not_77_out, not_78_out, not_79_out, not_80_out, not_81_out,
       not_82_out, not_83_out, not_84_out, not_85_out, not_86_out, not_87_out, not_88_out, not_89_out,
       not_90_out, not_91_out, not_92_out, not_93_out, not_94_out, not_95_out, not_96_out, not_97_out,
       not_98_out, not_99_out, not_100_out, not_101_out, not_102_out, not_103_out, not_104_out, not_105_out,
       not_106_out, not_107_out, not_108_out, not_109_out, not_110_out, not_111_out, not_112_out,
       not_113_out, not_114_out, not_115_out, not_116_out, not_117_out, not_118_out, not_119_out,
       not_120_out, not_121_out, not_122_out, not_123_out, not_124_out, not_125_out, not_126_out,
       not_127_out, not_128_out, not_129_out, not_130_out, not_131_out, not_132_out, not_133_out,
       not_134_out, not_135_out, not_136_out, not_137_out, not_138_out, not_139_out, not_140_out,
       not_141_out, not_142_out, not_143_out, not_144_out, not_145_out, not_146_out, not_147_out,
       not_148_out, not_149_out, not_150_out, not_151_out, not_152_out, not_153_out, not_154_out,
       not_155_out, not_156_out, not_157_out, not_158_out, not_159_out, not_160_out, not_161_out,
       not_162_out, not_163_out, not_164_out, not_165_out, not_166_out, not_167_out, not_168_out,
       not_169_out, not_170_out, not_171_out, not_172_out, not_173_out, not_174_out, not_175_out,
       not_176_out, not_177_out, not_178_out, not_179_out, not_180_out, not_181_out, not_182_out,
       not_183_out, not_184_out, not_185_out, not_186_out, not_187_out, not_188_out, not_189_out,
       not_190_out, not_191_out, not_192_out, not_193_out, not_194_out, not_195_out, not_196_out,
       not_197_out, not_198_out, not_199_out, not_200_out, not_201_out, not_202_out, not_203_out,
       not_204_out, not_205_out, not_206_out, not_207_out, not_208_out, not_209_out, not_210_out,
       not_211_out, not_212_out, not_213_out, not_214_out, not_215_out, not_216_out, not_217_out,
       not_218_out, not_219_out, not_220_out, not_221_out, not_222_out, not_223_out, not_224_out,
       not_225_out, not_226_out, not_227_out, not_228_out, not_229_out, not_230_out, not_231_out,
       not_232_out, not_233_out, not_234_out, not_235_out, not_236_out, not_237_out, not_238_out,
       not_239_out, not_240_out, not_241_out, not_242_out, not_243_out, not_244_out, not_245_out,
       not_246_out, not_247_out, not_248_out, not_249_out, not_250_out, not_251_out, not_252_out,
       not_253_out, not_254_out, not_255_out, not_256_out, not_257_out, not_258_out;

  not not_1 (not_1_out, OP2);
  not not_2 (not_2_out, OP3);
  not not_3 (not_3_out, OP4);
  not not_4 (not_4_out, OP5);
  not not_5 (not_5_out, OP6);
  not not_6 (not_6_out, F12);
  not not_7 (not_7_out, F13);
  not not_8 (not_8_out, OP2);
  not not_9 (not_9_out, OP3);
  not not_10 (not_10_out, OP4);
  not not_11 (not_11_out, OP5);
  not not_12 (not_12_out, OP6);
  not not_13 (not_13_out, F12);
  not not_14 (not_14_out, F14);
  not not_15 (not_15_out, OP2);
  not not_16 (not_16_out, OP3);
  not not_17 (not_17_out, OP4);
  not not_18 (not_18_out, F12);
  not not_19 (not_19_out, OP2);
  not not_20 (not_20_out, OP3);
  not not_21 (not_21_out, OP4);
  not not_22 (not_22_out, OP6);
  not not_23 (not_23_out, F12);
  not not_24 (not_24_out, F14);
  not not_25 (not_25_out, OP2);
  not not_26 (not_26_out, OP3);
  not not_27 (not_27_out, OP5);
  not not_28 (not_28_out, OP6);
  not not_29 (not_29_out, F12);
  not not_30 (not_30_out, F13);
  not not_31 (not_31_out, OP2);
  not not_32 (not_32_out, OP3);
  not not_33 (not_33_out, OP4);
  not not_34 (not_34_out, OP6);
  not not_35 (not_35_out, F12);
  not not_36 (not_36_out, F14);
  not not_37 (not_37_out, OP2);
  not not_38 (not_38_out, OP3);
  not not_39 (not_39_out, OP5);
  not not_40 (not_40_out, OP6);
  not not_41 (not_41_out, F12);
  not not_42 (not_42_out, OP2);
  not not_43 (not_43_out, OP3);
  not not_44 (not_44_out, OP5);
  not not_45 (not_45_out, OP6);
  not not_46 (not_46_out, F25);
  not not_47 (not_47_out, F30);
  not not_48 (not_48_out, OP2);
  not not_49 (not_49_out, OP3);
  not not_50 (not_50_out, OP5);
  not not_51 (not_51_out, OP6);
  not not_52 (not_52_out, F25);
  not not_53 (not_53_out, OP2);
  not not_54 (not_54_out, OP3);
  not not_55 (not_55_out, OP5);
  not not_56 (not_56_out, OP6);
  not not_57 (not_57_out, OP3);
  not not_58 (not_58_out, OP4);
  not not_59 (not_59_out, F12);
  not not_60 (not_60_out, F13);
  not not_61 (not_61_out, F14);
  not not_62 (not_62_out, OP2);
  not not_63 (not_63_out, OP3);
  not not_64 (not_64_out, OP4);
  not not_65 (not_65_out, OP5);
  not not_66 (not_66_out, OP6);
  not not_67 (not_67_out, F12);
  not not_68 (not_68_out, F13);
  not not_69 (not_69_out, F12);
  not not_70 (not_70_out, OP3);
  not not_71 (not_71_out, OP2);
  not not_72 (not_72_out, OP3);
  not not_73 (not_73_out, OP2);
  not not_74 (not_74_out, OP2);
  not not_75 (not_75_out, OP3);
  not not_76 (not_76_out, OP5);
  not not_77 (not_77_out, OP6);
  not not_78 (not_78_out, F12);
  not not_79 (not_79_out, F13);
  not not_80 (not_80_out, OP2);
  not not_81 (not_81_out, OP3);
  not not_82 (not_82_out, OP4);
  not not_83 (not_83_out, OP6);
  not not_84 (not_84_out, F12);
  not not_85 (not_85_out, F14);
  not not_86 (not_86_out, OP2);
  not not_87 (not_87_out, OP3);
  not not_88 (not_88_out, OP4);
  not not_89 (not_89_out, F13);
  not not_90 (not_90_out, F14);
  not not_91 (not_91_out, OP3);
  not not_92 (not_92_out, OP4);
  not not_93 (not_93_out, F12);
  not not_94 (not_94_out, F13);
  not not_95 (not_95_out, F14);
  not not_96 (not_96_out, OP2);
  not not_97 (not_97_out, OP3);
  not not_98 (not_98_out, F12);
  not not_99 (not_99_out, OP2);
  not not_100 (not_100_out, OP3);
  not not_101 (not_101_out, OP5);
  not not_102 (not_102_out, OP6);
  not not_103 (not_103_out, F12);
  not not_104 (not_104_out, OP2);
  not not_105 (not_105_out, OP3);
  not not_106 (not_106_out, OP6);
  not not_107 (not_107_out, F12);
  not not_108 (not_108_out, F13);
  not not_109 (not_109_out, F14);
  not not_110 (not_110_out, F25);
  not not_111 (not_111_out, OP2);
  not not_112 (not_112_out, OP3);
  not not_113 (not_113_out, OP6);
  not not_114 (not_114_out, F14);
  not not_115 (not_115_out, F25);
  not not_116 (not_116_out, F30);
  not not_117 (not_117_out, OP2);
  not not_118 (not_118_out, OP3);
  not not_119 (not_119_out, OP5);
  not not_120 (not_120_out, OP6);
  not not_121 (not_121_out, F25);
  not not_122 (not_122_out, OP2);
  not not_123 (not_123_out, OP3);
  not not_124 (not_124_out, OP5);
  not not_125 (not_125_out, OP6);
  not not_126 (not_126_out, OP2);
  not not_127 (not_127_out, OP3);
  not not_128 (not_128_out, OP6);
  not not_129 (not_129_out, F25);
  not not_130 (not_130_out, F30);
  not not_131 (not_131_out, OP2);
  not not_132 (not_132_out, OP3);
  not not_133 (not_133_out, F12);
  not not_134 (not_134_out, F13);
  not not_135 (not_135_out, F14);
  not not_136 (not_136_out, F25);
  not not_137 (not_137_out, F30);
  not not_138 (not_138_out, OP2);
  not not_139 (not_139_out, OP3);
  not not_140 (not_140_out, OP2);
  not not_141 (not_141_out, OP3);
  not not_142 (not_142_out, OP5);
  not not_143 (not_143_out, OP6);
  not not_144 (not_144_out, F12);
  not not_145 (not_145_out, F13);
  not not_146 (not_146_out, OP2);
  not not_147 (not_147_out, OP3);
  not not_148 (not_148_out, OP5);
  not not_149 (not_149_out, OP6);
  not not_150 (not_150_out, F12);
  not not_151 (not_151_out, F14);
  not not_152 (not_152_out, OP2);
  not not_153 (not_153_out, OP3);
  not not_154 (not_154_out, OP5);
  not not_155 (not_155_out, OP6);
  not not_156 (not_156_out, F12);
  not not_157 (not_157_out, OP2);
  not not_158 (not_158_out, OP3);
  not not_159 (not_159_out, OP6);
  not not_160 (not_160_out, F12);
  not not_161 (not_161_out, F13);
  not not_162 (not_162_out, F14);
  not not_163 (not_163_out, F25);
  not not_164 (not_164_out, OP2);
  not not_165 (not_165_out, OP3);
  not not_166 (not_166_out, OP6);
  not not_167 (not_167_out, F14);
  not not_168 (not_168_out, F25);
  not not_169 (not_169_out, F30);
  not not_170 (not_170_out, OP2);
  not not_171 (not_171_out, OP3);
  not not_172 (not_172_out, OP5);
  not not_173 (not_173_out, OP6);
  not not_174 (not_174_out, F25);
  not not_175 (not_175_out, OP2);
  not not_176 (not_176_out, OP3);
  not not_177 (not_177_out, OP5);
  not not_178 (not_178_out, OP6);
  not not_179 (not_179_out, OP2);
  not not_180 (not_180_out, OP3);
  not not_181 (not_181_out, OP6);
  not not_182 (not_182_out, F25);
  not not_183 (not_183_out, F30);
  not not_184 (not_184_out, OP4);
  not not_185 (not_185_out, F12);
  not not_186 (not_186_out, F13);
  not not_187 (not_187_out, F14);
  not not_188 (not_188_out, OP4);
  not not_189 (not_189_out, OP2);
  not not_190 (not_190_out, OP3);
  not not_191 (not_191_out, OP4);
  not not_192 (not_192_out, OP6);
  not not_193 (not_193_out, F12);
  not not_194 (not_194_out, F14);
  not not_195 (not_195_out, OP2);
  not not_196 (not_196_out, OP3);
  not not_197 (not_197_out, OP4);
  not not_198 (not_198_out, F13);
  not not_199 (not_199_out, F14);
  not not_200 (not_200_out, OP2);
  not not_201 (not_201_out, OP3);
  not not_202 (not_202_out, OP4);
  not not_203 (not_203_out, F12);
  not not_204 (not_204_out, OP2);
  not not_205 (not_205_out, OP3);
  not not_206 (not_206_out, OP6);
  not not_207 (not_207_out, F12);
  not not_208 (not_208_out, F13);
  not not_209 (not_209_out, F14);
  not not_210 (not_210_out, F25);
  not not_211 (not_211_out, OP2);
  not not_212 (not_212_out, OP3);
  not not_213 (not_213_out, OP6);
  not not_214 (not_214_out, F14);
  not not_215 (not_215_out, F25);
  not not_216 (not_216_out, F30);
  not not_217 (not_217_out, OP2);
  not not_218 (not_218_out, OP3);
  not not_219 (not_219_out, F12);
  not not_220 (not_220_out, F13);
  not not_221 (not_221_out, F14);
  not not_222 (not_222_out, F25);
  not not_223 (not_223_out, F30);
  not not_224 (not_224_out, OP2);
  not not_225 (not_225_out, OP3);
  not not_226 (not_226_out, OP6);
  not not_227 (not_227_out, F25);
  not not_228 (not_228_out, F30);
  not not_229 (not_229_out, OP2);
  not not_230 (not_230_out, OP3);
  not not_231 (not_231_out, F12);
  not not_232 (not_232_out, F13);
  not not_233 (not_233_out, F14);
  not not_234 (not_234_out, F25);
  not not_235 (not_235_out, F30);
  not not_236 (not_236_out, OP2);
  not not_237 (not_237_out, OP3);
  not not_238 (not_238_out, OP4);
  not not_239 (not_239_out, OP6);
  not not_240 (not_240_out, F12);
  not not_241 (not_241_out, F14);
  not not_242 (not_242_out, OP2);
  not not_243 (not_243_out, OP3);
  not not_244 (not_244_out, OP4);
  not not_245 (not_245_out, F12);
  not not_246 (not_246_out, F13);
  not not_247 (not_247_out, F14);
  not not_248 (not_248_out, OP2);
  not not_249 (not_249_out, OP3);
  not not_250 (not_250_out, OP4);
  not not_251 (not_251_out, F13);
  not not_252 (not_252_out, F14);
  not not_253 (not_253_out, OP3);
  not not_254 (not_254_out, OP4);
  not not_255 (not_255_out, F12);
  not not_256 (not_256_out, F13);
  not not_257 (not_257_out, F14);
  not not_258 (not_258_out, OP4);
  and and_1 (and_1_out, not_1_out, not_2_out, not_3_out, not_4_out, not_5_out, not_6_out, not_7_out, F14);
  and and_2 (and_2_out, not_8_out, not_9_out, not_10_out, not_11_out, not_12_out, not_13_out, F13, not_14_out);
  and and_3 (BLTU, not_15_out, not_16_out, not_17_out, OP5, OP6, not_18_out, F13, F14);
  and and_4 (MemWrite, not_19_out, not_20_out, not_21_out, OP5, not_22_out, not_23_out, F13, not_24_out);
  and and_5 (and_5_out, not_25_out, not_26_out, not_27_out, not_28_out, not_29_out, not_30_out, F14);
  and and_6 (and_6_out, not_31_out, not_32_out, not_33_out, not_34_out, not_35_out, F13, not_36_out);
  and and_7 (and_7_out, not_37_out, not_38_out, OP4, not_39_out, not_40_out, not_41_out);
  and and_8 (and_8_out, not_42_out, not_43_out, OP4, not_44_out, not_45_out, not_46_out, not_47_out);
  and and_9 (and_9_out, not_48_out, not_49_out, OP4, not_50_out, not_51_out, F14, not_52_out);
  and and_10 (and_10_out, not_53_out, not_54_out, OP4, not_55_out, not_56_out, F13);
  and and_11 (and_11_out, OP2, not_57_out, not_58_out, OP5, OP6, not_59_out, not_60_out, not_61_out);
  and and_12 (LBU, not_62_out, not_63_out, not_64_out, not_65_out, not_66_out, not_67_out, not_68_out, F14);
  and and_13 (and_13_out, F14, F13, not_69_out, OP6, OP5, OP4, not_70_out, not_71_out);
  and and_14 (and_14_out, F14, F13, F12, OP6, OP5, OP4, not_72_out, not_73_out);
  and and_15 (and_15_out, not_74_out, not_75_out, not_76_out, not_77_out, not_78_out, not_79_out, F14);
  and and_16 (and_16_out, not_80_out, not_81_out, not_82_out, not_83_out, not_84_out, F13, not_85_out);
  and and_17 (and_17_out, not_86_out, not_87_out, not_88_out, OP5, OP6, not_89_out, not_90_out);
  and and_18 (and_18_out, not_91_out, not_92_out, OP5, OP6, not_93_out, not_94_out, not_95_out);
  and and_19 (and_19_out, not_96_out, not_97_out, OP5, OP6, not_98_out, F13, F14);
  and and_20 (and_20_out, not_99_out, not_100_out, OP4, not_101_out, not_102_out, not_103_out);
  and and_21 (and_21_out, not_104_out, not_105_out, OP4, not_106_out, not_107_out, not_108_out, not_109_out, not_110_out);
  and and_22 (and_22_out, not_111_out, not_112_out, OP4, not_113_out, not_114_out, not_115_out, not_116_out);
  and and_23 (and_23_out, not_117_out, not_118_out, OP4, not_119_out, not_120_out, F14, not_121_out);
  and and_24 (and_24_out, not_122_out, not_123_out, OP4, not_124_out, not_125_out, F13);
  and and_25 (and_25_out, not_126_out, not_127_out, OP4, not_128_out, F13, not_129_out, not_130_out);
  and and_26 (and_26_out, not_131_out, not_132_out, OP4, OP5, not_133_out, not_134_out, not_135_out, not_136_out, not_137_out);
  and and_27 (and_27_out, not_138_out, not_139_out, OP4, OP5, OP6, F13, F14);
  and and_28 (and_28_out, not_140_out, not_141_out, not_142_out, not_143_out, not_144_out, not_145_out, F14);
  and and_29 (and_29_out, not_146_out, not_147_out, not_148_out, not_149_out, not_150_out, F13, not_151_out);
  and and_30 (and_30_out, not_152_out, not_153_out, OP4, not_154_out, not_155_out, not_156_out);
  and and_31 (and_31_out, not_157_out, not_158_out, OP4, not_159_out, not_160_out, not_161_out, not_162_out, not_163_out);
  and and_32 (and_32_out, not_164_out, not_165_out, OP4, not_166_out, not_167_out, not_168_out, not_169_out);
  and and_33 (and_33_out, not_170_out, not_171_out, OP4, not_172_out, not_173_out, F14, not_174_out);
  and and_34 (and_34_out, not_175_out, not_176_out, OP4, not_177_out, not_178_out, F13);
  and and_35 (and_35_out, not_179_out, not_180_out, OP4, not_181_out, F13, not_182_out, not_183_out);
  and and_36 (and_36_out, OP2, not_184_out, OP5, OP6, not_185_out, not_186_out, not_187_out);
  and and_37 (and_37_out, OP2, OP3, not_188_out, OP5, OP6);
  and and_38 (and_38_out, not_189_out, not_190_out, not_191_out, OP5, not_192_out, not_193_out, F13, not_194_out);
  and and_39 (and_39_out, not_195_out, not_196_out, not_197_out, OP5, OP6, not_198_out, not_199_out);
  and and_40 (and_40_out, not_200_out, not_201_out, not_202_out, OP5, OP6, not_203_out, F13, F14);
  and and_41 (and_41_out, not_204_out, not_205_out, OP4, OP5, not_206_out, not_207_out, not_208_out, not_209_out, not_210_out);
  and and_42 (and_42_out, not_211_out, not_212_out, OP4, OP5, not_213_out, not_214_out, not_215_out, not_216_out);
  and and_43 (and_43_out, not_217_out, not_218_out, OP4, OP5, not_219_out, not_220_out, not_221_out, not_222_out, not_223_out);
  and and_44 (and_44_out, not_224_out, not_225_out, OP4, OP5, not_226_out, F13, not_227_out, not_228_out);
  and and_45 (ecall, not_229_out, not_230_out, OP4, OP5, OP6, not_231_out, not_232_out, not_233_out, not_234_out, not_235_out);
  and and_46 (S_Type, not_236_out, not_237_out, not_238_out, OP5, not_239_out, not_240_out, F13, not_241_out);
  and and_47 (BEQ, not_242_out, not_243_out, not_244_out, OP5, OP6, not_245_out, not_246_out, not_247_out);
  and and_48 (BNE, not_248_out, not_249_out, not_250_out, OP5, OP6, F12, not_251_out, not_252_out);
  and and_49 (JALR, OP2, not_253_out, not_254_out, OP5, OP6, not_255_out, not_256_out, not_257_out);
  and and_50 (JAL, OP2, OP3, not_258_out, OP5, OP6);
  or or_1 (MemToReg, and_1_out, and_2_out);
  or or_2 (ALU_SRC, and_5_out, and_6_out, and_7_out, and_8_out, and_9_out, and_10_out, and_11_out);
  or or_3 (CSC, and_13_out, and_14_out);
  or or_4 (RTread, and_38_out, and_39_out, and_40_out, and_41_out, and_42_out, and_43_out, and_44_out);
  or or_5 (RSread, and_15_out, and_16_out, and_17_out, and_18_out, and_19_out, and_20_out, and_21_out, and_22_out, and_23_out, and_24_out, and_25_out, and_26_out, and_27_out);
  or or_6 (RegWrite, and_28_out, and_29_out, and_30_out, and_31_out, and_32_out, and_33_out, and_34_out, and_35_out, and_36_out, and_37_out);
endmodule

// ALU
module ALU (
  input  [31:0] X,
  input  [31:0] Y,
  input  [3:0] AluOP,
  output out_4,
  output Equal,
  output out_6,
  output [31:0] Result,
  output [31:0] Result_2
);

  wire [0:0] comparator_1_lt, comparator_2_lt;
  wire [31:0] adder_1_out, AND_out, divider_1_out, divider_1_rem, multiplier_1_cout, multiplier_1_out,
       NOR_out, OR_out, shifter_1_out, shifter_2_out, shifter_3_out, subtractor_1_out, XOR_out;

  assign AND_out = X & Y;  // AND_Gate AND, 32 bits wide
  assign OR_out = X | Y;  // OR_Gate OR, 32 bits wide
  Shifter #(.width(32), .shift("ll")) shifter_1 (.in(X), .\dist (Y[4:0]), .out(shifter_1_out));
  Shifter #(.width(32), .shift("ar")) shifter_2 (.in(X), .\dist (Y[4:0]), .out(shifter_2_out));
  Shifter #(.width(32), .shift("lr")) shifter_3 (.in(X), .\dist (Y[4:0]), .out(shifter_3_out));
  Multiplier #(.width(32)) multiplier_1 (.a(X), .b(Y), .out(multiplier_1_out), .cout(multiplier_1_cout));  // open: cin
  Divider #(.width(32)) divider_1 (.a(X), .b(Y), .out(divider_1_out), .rem(divider_1_rem));  // open: upper
  Adder #(.width(32)) adder_1 (.a(X), .b(Y), .out(adder_1_out));  // open: cin, cout
  Subtractor #(.width(32)) subtractor_1 (.a(X), .b(Y), .out(subtractor_1_out));  // open: bin, bout
  assign XOR_out = X ^ Y;  // XOR_Gate XOR, 32 bits wide
  assign NOR_out = ~(X | Y);  // NOR_Gate NOR, 32 bits wide
  Comparator #(.width(32), .mode("twosComplement")) comparator_1 (
    .a(X), .b(Y), .eq(Equal), .lt(comparator_1_lt[0]));  // open: gt
  Comparator #(.width(32), .mode("unsigned")) comparator_2 (.a(X), .b(Y), .lt(comparator_2_lt[0]));  // open: gt, eq
  Multiplexer #(.select(4), .width(32), .disabled("Z"), .enable("false")) multiplexer_1 (
    .in0(shifter_1_out), .in1(shifter_2_out), .in2(shifter_3_out), .in3(multiplier_1_out),
    .in4(divider_1_out), .in5(adder_1_out), .in6(subtractor_1_out), .in7(AND_out), .in8(OR_out),
    .in9(XOR_out), .in10(NOR_out), .in11({{31{1'b0}}, comparator_1_lt[0]}),
    .in12({{31{1'b0}}, comparator_2_lt[0]}), .in13({32{1'b0}}), .in14({32{1'b0}}), .in15({32{1'b0}}),
    .out(Result), .sel(AluOP));
  Multiplexer #(.select(4), .width(32), .disabled("Z"), .enable("false")) multiplexer_2 (
    .in0({32{1'b0}}), .in1({32{1'b0}}), .in2({32{1'b0}}), .in3(multiplier_1_cout), .in4(divider_1_rem),
    .in5({32{1'b0}}), .in6({32{1'b0}}), .in7({32{1'b0}}), .in8({32{1'b0}}), .in9({32{1'b0}}),
    .in10({32{1'b0}}), .in11({32{1'b0}}), .in12({32{1'b0}}), .in13({32{1'b0}}), .in14({32{1'b0}}),
    .in15({32{1'b0}}), .out(Result_2), .sel(AluOP));
  Multiplexer #(.select(4), .width(1), .disabled("Z"), .enable("false")) multiplexer_3 (
    .in0(1'b0), .in1(1'b0), .in2(1'b0), .in3(1'b0), .in4(1'b0), .in5(1'b0), .in6(1'b0), .in7(1'b0),
    .in8(1'b0), .in9(1'b0), .in10(1'b0), .in11(comparator_1_lt[0]), .in12(comparator_2_lt[0]), .in13(1'b0),
    .in14(1'b0), .in15(1'b0), .out(out_6), .sel(AluOP));
  not not_1 (out_4, out_6);

  // Other names for the same wires on the sheet: Result2[31:0] = Result_2; S[3:0] = AluOP; tunnel = out_6;
  //   tunnel_t = out_4

  // Notes on the sheet:
  //   不要改变此引脚区域内容，也不要改变ALU封装形式
  //   输入引脚
  //   输出引脚
endmodule

module Regifile (
  input  [31:0] Din,
  input  Clk,
  input  WE,
  input  [4:0] R1_num,
  input  [4:0] W_num,
  input  [4:0] R2_num,
  output [31:0] R1,
  output [31:0] R2
);

  // RegisterFile registerfile_1: pin names not known; wires that end beside it: Din, Clk, WE, W_num, R1_num, R2_num, R1, R2
endmodule

module \理想流水线  (
  output RegWrite,
  output MemWrite,
  output [31:0] IF_PC,
  output [31:0] ID_PC,
  output [31:0] EX_PC,
  output [31:0] M_PC,
  output [31:0] WB_PC,
  output [31:0] RDin,
  output [31:0] MDin,
  output [31:0] LedData
);

  wire and_2_out, and_3_out, and_4_out, and_5_out, CLK, clock_1_out, comparator_1_eq, comparator_2_eq,
       comparator_2_lt, d_ff_1_q, ENS, EX_ALUequal, EX_ALUless, EX_AluSrcB, EX_BE, EX_BEQ, EX_BLTU, EX_BNE,
       EX_ecall, EX_JAL, EX_JALR, EX_LBU, EX_MemToReg, EX_MemWrite, EX_RegWrite, EX_Stype, Go, halt,
       ID_AluSrcB, ID_BEQ, ID_BLTU, ID_BNE, ID_ecall, ID_JAL, ID_JALR, ID_LBU, ID_MemToReg, ID_MemWrite,
       ID_RegWrite, ID_Stype, ID_URET, IR1, IR2, IR3, MEM_AluSrcB, MEM_BE, MEM_BEQ, MEM_BLTU, MEM_BNE,
       MEM_ecall, MEM_JAL, MEM_JALR, MEM_LBU, MEM_MemToReg, MEM_RegWrite, MEM_Stype, nand_1_out, not_2_out,
       not_3_out, not_4_out, not_5_out, or_2_out, RST, W1, W2, W3, WB_AluSrcB, WB_BE, WB_BEQ, WB_BLTU,
       WB_BNE, WB_ecall, WB_JAL, WB_JALR, WB_LBU, WB_MemToReg, WB_MemWrite, WB_Stype;
  wire [3:0] EX_AluOP, ID_AluOP, MEM_AluOP, WB_AluOP;
  wire [4:0] EX_W_num, MEM_W_num, multiplexer_1_out, multiplexer_2_out, WB_W_num;
  wire [7:0] multiplexer_5_out;
  wire [11:0] multiplexer_3_out;
  wire [12:0] CNT_num;
  wire [15:0] \LoadUse次数 , \总周期数 , \插入气泡数 , \无条件分支数 , \条件分支成功数 ;
  wire [31:0] bit_extender_2_out, bit_extender_3_out, bit_extender_4_out, EX_BEADDR, EX_IMM, EX_IR,
       EX_JALADDR, EX_PCP4, EX_R1, EX_R2, EX_Result, ID_BEADDR, ID_IMM, ID_IR, ID_JALADDR, ID_PCP4, ID_R1,
       ID_R2, IF_IR, IF_PCP4, MEM_ALUOUT, MEM_BEADDR, MEM_IMM, MEM_IR, MEM_JALADDR, MEM_PCP4, MEM_R1,
       mem_wb_1_aluresultout, mem_wb_1_memout, multiplexer_4_out, multiplexer_6_out, multiplexer_7_out,
       ram_1_data, shifter_1_out, shifter_2_out, WB_BEADDR, WB_IR, WB_JALADDR, WB_PCP4;

  Button \u_总复位  (.out(RST));
  Button _1 (.out(IR1));
  Button _2 (.out(IR2));
  Button _3 (.out(IR3));
  // Probe on \总周期数 
  // Probe on \总周期数 
  Button \u_继续运行  (.out(Go));
  LED #(.active("true")) led_1 (.in(W1));
  LED #(.active("true")) led_2 (.in(W2));
  LED #(.active("true")) led_3 (.in(W3));
  not not_1 (ENS, halt);
  Hex_Digit_Display hex_digit_display_1 (.value(LedData[31:28]));  // open: dp
  // Probe on IF_PC[19:0]
  // RiscV_Probe riscv_probe_1: pin names not known; wires that end beside it: IF_IR
  Register #(.width(32), .trigger("rising"), .Select("low")) PC (
    .D(IF_PCP4), .en(not_2_out), .Q(IF_PC), .clk(CLK), .clr(RST));
  not not_2 (not_2_out, halt);
  Hex_Digit_Display hex_digit_display_2 (.value(LedData[23:20]));  // open: dp
  Hex_Digit_Display hex_digit_display_3 (.value(LedData[27:24]));  // open: dp
  // Probe on ID_PC[19:0]
  // RiscV_Probe riscv_probe_2: pin names not known; wires that end beside it: ID_IR
  Adder #(.width(32)) adder_1 (.a(IF_PC), .b(32'h4), .out(IF_PCP4));  // open: cin, cout
  Hex_Digit_Display hex_digit_display_4 (.value(LedData[15:12]));  // open: dp
  Hex_Digit_Display hex_digit_display_5 (.value(LedData[19:16]));  // open: dp
  Hex_Digit_Display hex_digit_display_6 (.value(LedData[7:4]));  // open: dp
  Hex_Digit_Display hex_digit_display_7 (.value(LedData[11:8]));  // open: dp
  // Probe on EX_PC[19:0]
  // RiscV_Probe riscv_probe_3: pin names not known; wires that end beside it: EX_IR
  ROM #(.addrWidth(10), .dataWidth(32), .Select("high")) rom_1 (.addr(IF_PC[11:2]), .data(IF_IR));
  Hex_Digit_Display hex_digit_display_8 (.value(LedData[3:0]));  // open: dp
  // RiscV_Probe riscv_probe_4: pin names not known; wires that end beside it: IF_IR
  // Probe on \总周期数 
  // Probe on M_PC[19:0]
  // RiscV_Probe riscv_probe_5: pin names not known; wires that end beside it: MEM_IR
  IF_ID if_id_1 (
    .CLK(CLK), .IRin(IF_IR), .IRout(ID_IR), .PCP4in(IF_PCP4), .PCP4out(ID_PCP4), .EN(ENS), .RESET(1'b0),
    .PCin(IF_PC), .PCout(ID_PC));
  not not_3 (not_3_out, WB_ecall);
  // Probe on \总周期数 
  // Probe on \无条件分支数 
  // Probe on \条件分支成功数 
  // Probe on \插入气泡数 
  // Probe on \LoadUse次数 
  // RiscV_Probe riscv_probe_6: pin names not known; wires that end beside it: ID_IR
  Comparator #(.width(32), .mode("twosComplement")) comparator_1 (
    .a(ID_R1), .b(32'h22), .eq(comparator_1_eq));  // open: gt, lt
  Counter #(.width(16), .max('hffff), .ongoal("wrap"), .trigger("rising"), .behavior("new")) counter_1 (
    .D({16{1'b0}}), .count(not_3_out), .Q(\总周期数 ), .clk(CLK));  // open: load, carry, clr, preset, down
  // Probe on IF_PC[11:0]
  // Probe on WB_PC[19:0]
  // RiscV_Probe riscv_probe_7: pin names not known; wires that end beside it: WB_IR
  not not_4 (not_4_out, comparator_1_eq);
  // Probe on EX_PC[11:0]
  // Probe on ID_PC[11:0]
  and and_1 (halt, not_4_out, WB_ecall);
  and and_2 (and_2_out, comparator_1_eq, WB_ecall);
  // Probe on M_PC[11:0]
  D_Flip_Flop #(.trigger("high"), .Pre_Clr_Positions("LEGACY"), .NegatePresetClear("false"), .enable("true"), .NewFFLayout("false")) d_ff_1 (.Q(d_ff_1_q));  // open: clk, D, Qn, preset, en, reset
  // Probe on 13'h2
  // Probe on WB_PC[11:0]
  Comparator #(.width(13), .mode("twosComplement")) comparator_2 (
    .a(CNT_num), .b(13'h2), .eq(comparator_2_eq), .lt(comparator_2_lt));  // open: gt
  Clock #(.highDuration(1), .lowDuration(1)) clock_1 (.out(clock_1_out));
  Register #(.width(32), .trigger("rising"), .Select("low")) register_1 (
    .D(ID_R2), .en(and_2_out), .Q(LedData), .clk(CLK));  // open: clr
  nand nand_1 (nand_1_out, d_ff_1_q, comparator_2_eq);
  Counter #(.width(13), .max('h1fff), .ongoal("stay"), .trigger("rising"), .behavior("old")) counter_2 (
    .count(comparator_2_lt), .Q(CNT_num), .clk(clock_1_out));  // open: load, D, carry, clr, preset
  \单周期硬布线控制器  \u_单周期硬布线控制器_1  (
    .Funct({ID_IR[30], ID_IR[25], ID_IR[14:12]}), .OP(ID_IR[6:2]), .ALU_OP(ID_AluOP), .MemToReg(ID_MemToReg),
    .MemWrite(ID_MemWrite), .ALU_SRC(ID_AluSrcB), .ecall(ID_ecall), .S_type(ID_Stype), .Jalr(ID_JALR),
    .Beq(ID_BEQ), .JAL(ID_JAL), .Bne(ID_BNE), .in_3(ID_IR[21]), .uret(ID_URET), .LBU(ID_LBU), .BLTU(ID_BLTU),
    .RegWrite(ID_RegWrite));  // open: RSread, RTread, CSC
  Multiplexer #(.select(1), .width(5), .disabled("Z"), .enable("false")) multiplexer_1 (
    .in0(ID_IR[19:15]), .in1(5'b10001), .out(multiplexer_1_out), .sel(ID_ecall));
  Multiplexer #(.select(1), .width(5), .disabled("Z"), .enable("false")) multiplexer_2 (
    .in0(ID_IR[24:20]), .in1(5'b01010), .out(multiplexer_2_out), .sel(ID_ecall));
  Multiplexer #(.select(1), .width(12), .disabled("Z"), .enable("false")) multiplexer_3 (
    .in0(ID_IR[31:20]), .in1({ID_IR[31:25], ID_IR[11:7]}), .out(multiplexer_3_out), .sel(ID_Stype));
  assign CLK = nand_1_out ? clock_1_out : 1'bz;  // Controlled_Buffer controlled_buffer_1
  assign ID_IMM = {{20{multiplexer_3_out[11]}}, multiplexer_3_out};  // Bit_Extender bit_extender_1
  assign bit_extender_2_out = {{20{ID_IR[31]}}, {ID_IR[31], ID_IR[7], ID_IR[30:25], ID_IR[11:8]}};  // Bit_Extender bit_extender_2
  assign bit_extender_3_out = {{12{ID_IR[31]}}, {ID_IR[31], ID_IR[19:12], ID_IR[20], ID_IR[30:21]}};  // Bit_Extender bit_extender_3
  Pull_Resistor #(.pull(1)) pull_resistor_1 (.node(CLK));
  Shifter #(.width(32), .shift("ll")) shifter_1 (.in(bit_extender_2_out), .\dist (5'b00001), .out(shifter_1_out));
  Shifter #(.width(32), .shift("ll")) shifter_2 (.in(bit_extender_3_out), .\dist (5'b00001), .out(shifter_2_out));
  Regifile regifile_1 (
    .Din(RDin), .Clk(CLK), .R1(ID_R1), .R2(ID_R2), .WE(RegWrite), .W_num(WB_W_num),
    .R1_num(multiplexer_1_out), .R2_num(multiplexer_2_out));
  Adder #(.width(32)) adder_2 (.a(shifter_1_out), .b(ID_PC), .out(ID_BEADDR), .cin(1'b0));  // open: cout
  Adder #(.width(32)) adder_3 (.a(shifter_2_out), .b(ID_PC), .out(ID_JALADDR), .cin(1'b0));  // open: cout
  ID_EX id_ex_1 (
    .CLK(CLK), .EN(ENS), .RESET(1'b0), .RegWritein(ID_RegWrite), .MemToRegin(ID_MemToReg),
    .MemWritein(ID_MemWrite), .ALUOPin(ID_AluOP), .ALUSrcin(ID_AluSrcB), .ecallin(ID_ecall),
    .Stypein(ID_Stype), .BEQin(ID_BEQ), .BNEin(ID_BNE), .JALRin(ID_JALR), .BLTUin(ID_BLTU), .JALin(ID_JAL),
    .RegWriteout(EX_RegWrite), .MemToRegout(EX_MemToReg), .MemWriteout(EX_MemWrite), .ALUOPout(EX_AluOP),
    .ALUSrcout(EX_AluSrcB), .ecallout(EX_ecall), .Stypeout(EX_Stype), .BEQout(EX_BEQ), .BNEout(EX_BNE),
    .JALout(EX_JAL), .JALRout(EX_JALR), .LBUin(ID_LBU), .LBUout(EX_LBU), .BLTUout(EX_BLTU), .R1in(ID_R1),
    .R1out(EX_R1), .R2in(ID_R2), .R2out(EX_R2), .W_in(ID_IR[11:7]), .W_out(EX_W_num), .Immin(ID_IMM),
    .Immout(EX_IMM), .BEADDRin(ID_BEADDR), .BEADDRout(EX_BEADDR), .PCin(ID_PC), .PCout(EX_PC),
    .PCP4in(ID_PCP4), .PCP4out(EX_PCP4), .JALADDrin(ID_JALADDR), .JALADDRout(EX_JALADDR), .IRin(ID_IR),
    .IRout(EX_IR));  // open: RSGOin, RSGOout, RTGOin, RTGOout
  Multiplexer #(.select(1), .width(32), .disabled("Z"), .enable("false")) multiplexer_4 (
    .in0(EX_R2), .in1(EX_IMM), .out(multiplexer_4_out), .sel(EX_AluSrcB));
  ALU alu_1 (
    .X(EX_R1), .Y(multiplexer_4_out), .AluOP(EX_AluOP), .Equal(EX_ALUequal), .Result(EX_Result),
    .out_6(EX_ALUless));  // open: Result_2, out_4
  and and_3 (and_3_out, EX_ALUequal, EX_BEQ);
  not not_5 (not_5_out, EX_ALUequal);
  and and_4 (and_4_out, not_5_out, EX_BNE);
  and and_5 (and_5_out, EX_ALUless, EX_BLTU);
  or or_1 (EX_BE, and_3_out, and_4_out, and_5_out);
  EX_MEM ex_mem_1 (
    .CLK(CLK), .EN(ENS), .RESET(1'b0), .RegWritein(EX_RegWrite), .MemToRegin(EX_MemToReg),
    .MemWritein(EX_MemWrite), .ALUOPin(EX_AluOP), .ALUSrcin(EX_AluSrcB), .ecallin(EX_ecall),
    .Stypein(EX_Stype), .BEQin(EX_BEQ), .BNEin(EX_BNE), .JALin(EX_JAL), .JALRin(EX_JALR), .LBUin(EX_LBU),
    .BLTUin(EX_BLTU), .W_in(EX_W_num), .Immin(EX_IMM), .BEADDRin(EX_BEADDR), .PCin(EX_PC), .PCP4in(EX_PCP4),
    .JALADDrin(EX_JALADDR), .RegWriteout(MEM_RegWrite), .MemToRegout(MEM_MemToReg), .MemWriteout(MemWrite),
    .ALUOPout(MEM_AluOP), .ALUSrcout(MEM_AluSrcB), .ecallout(MEM_ecall), .Stypeout(MEM_Stype),
    .BEQout(MEM_BEQ), .BNEout(MEM_BNE), .JALout(MEM_JAL), .JALRout(MEM_JALR), .LBUout(MEM_LBU),
    .BLTUout(MEM_BLTU), .W_out(MEM_W_num), .Immout(MEM_IMM), .BEADDRout(MEM_BEADDR), .PCout(M_PC),
    .PCP4out(MEM_PCP4), .JALADDRout(MEM_JALADDR), .BEin(EX_BE), .BEout(MEM_BE), .ALUResultin(EX_Result),
    .ALUResultout(MEM_ALUOUT), .R1in(EX_R1), .R1out(MEM_R1), .R2in(EX_R2), .R2out(MDin), .IRin(EX_IR),
    .IRout(MEM_IR));
  RAM #(.addrWidth(10), .dataWidth(32), .bus("separate"), .Select("high")) ram_1 (
    .addr(MEM_ALUOUT[11:2]), .din(MDin), .data(ram_1_data), .str(MemWrite), .clk(CLK));  // open: sel, ld, clr
  Multiplexer #(.select(2), .width(8), .disabled("Z"), .enable("false")) multiplexer_5 (
    .in0(ram_1_data[7:0]), .in1(ram_1_data[15:8]), .in2(ram_1_data[23:16]), .in3(ram_1_data[31:24]),
    .out(multiplexer_5_out), .sel(MEM_ALUOUT[1:0]));
  assign bit_extender_4_out = {{24{1'b0}}, multiplexer_5_out};  // Bit_Extender bit_extender_4
  Multiplexer #(.select(1), .width(32), .disabled("Z"), .enable("false")) multiplexer_6 (
    .in0(ram_1_data), .in1(bit_extender_4_out), .out(multiplexer_6_out), .sel(MEM_LBU));
  MEM_WB mem_wb_1 (
    .CLK(CLK), .EN(ENS), .RESET(1'b0), .RegWritein(MEM_RegWrite), .RegWriteout(RegWrite),
    .MemToRegin(MEM_MemToReg), .MemToRegout(WB_MemToReg), .MemWritein(MemWrite), .MemWriteout(WB_MemWrite),
    .ALUOPin(MEM_AluOP), .ALUOPout(WB_AluOP), .ALUSrcin(MEM_AluSrcB), .ALUSrcout(WB_AluSrcB),
    .ecallin(MEM_ecall), .ecallout(WB_ecall), .Stypein(MEM_Stype), .Stypeout(WB_Stype), .BEQin(MEM_BEQ),
    .BEQout(WB_BEQ), .BNEin(MEM_BNE), .BNEout(WB_BNE), .JALin(MEM_JAL), .JALout(WB_JAL), .JALRin(MEM_JALR),
    .JALRout(WB_JALR), .LBUin(MEM_LBU), .LBUout(WB_LBU), .BLTUin(MEM_BLTU), .BLTUout(WB_BLTU),
    .W_in(MEM_W_num), .W_out(WB_W_num), .Memin(multiplexer_6_out), .Memout(mem_wb_1_memout),
    .BEADDRin(MEM_BEADDR), .BEADDRout(WB_BEADDR), .PCin(M_PC), .PCout(WB_PC), .PCP4in(MEM_PCP4),
    .PCP4out(WB_PCP4), .JALADDrin(MEM_JALADDR), .JALADDRout(WB_JALADDR), .BEin(MEM_BE), .BEout(WB_BE),
    .ALUResultin(MEM_ALUOUT), .ALUResultout(mem_wb_1_aluresultout), .IRin(MEM_IR), .IRout(WB_IR));  // open: R1in, R1out, R2in, R2out
  Multiplexer #(.select(1), .width(32), .disabled("Z"), .enable("false")) multiplexer_7 (
    .in0(mem_wb_1_aluresultout), .in1(mem_wb_1_memout), .out(multiplexer_7_out), .sel(WB_MemToReg));
  or or_2 (or_2_out, WB_JAL, WB_JALR);
  Multiplexer #(.select(1), .width(32), .disabled("Z"), .enable("false")) multiplexer_8 (
    .in0(multiplexer_7_out), .in1(WB_PCP4), .out(RDin), .sel(or_2_out));

  // Other names for the same wires on the sheet: ID_W_num[4:0] = ID_IR[11:7]; MEM_MemWrite = MemWrite;
  //   MEM_PC[31:0] = M_PC; MEM_R2[31:0] = MDin; WB_RegWrite = RegWrite

  // Notes on the sheet:
  //   中断源
  //   时空图监测，可删除
  //   中断等待指示
  //   数码管输出
  //   IF
  //   指令存储器
  //   contents of rom_1 (hex, n*v repeats v):
  //   100493 100006f 100493 200913 300993 100006f 100493 200913 300993 100006f 100493 200913 300993
  //   100006f 100493 200913 300993 29c000ef 100413 100493 1f49493 900533 2200893 73 24d493 48463 fedff06f
  //   900533 2200893 73 100493 249493 900533 2200893 73 48463 fedff06f 100493 1f49493 900533 2200893 73
  //   4034d493 900533 2200893 73 4044d493 900533 2200893 73 4044d493 900533 2200893 73 4044d493 900533
  //   2200893 73 4044d493 900533 2200893 73 4044d493 900533 2200893 73 4044d493 900533 2200893 73 4044d493
  //   900533 2200893 73 100413 1f41993 41f9d993 433 c00913 300b13 140413 f47413 800293 100313 499993
  //   89e9b3 1300533 2200893 73 406282b3 fe0294e3 140413 f00f93 1f47433 1c41413 800293 100313 49d993
  //   89e9b3 1300533 2200893 73 406282b3 fe0294e3 1c45413 406b0b33 b0463 f95ff06f 2b3 fff2c293 829293
  //   ff2e293 500533 2200893 73 fff00413 493 84a023 140413 448493 84a023 140413 448493 84a023 140413
  //   448493 84a023 140413 448493 84a023 140413 448493 84a023 140413 448493 84a023 140413 448493 84a023
  //   140413 448493 84a023 140413 448493 84a023 140413 448493 84a023 140413 448493 84a023 140413 448493
  //   84a023 140413 448493 84a023 140413 448493 84a023 140413 448493 84a023 140413 448493 140413 433
  //   3c00493 42983 4aa03 149a2b3 28663 134a023 1442023 ffc48493 fe9412e3 800533 2200893 73 440413 3c00493
  //   fc9416e3 a00893 73 413 140413 800533 2200893 73 240413 800533 2200893 73 340413 800533 2200893 73
  //   440413 800533 2200893 73 540413 800533 2200893 73 640413 800533 2200893 73 740413 800533 2200893 73
  //   840413 800533 2200893 2200893 73 8067 f00493 100913 409909b3 900533 2200893 73 fff48493 ff29f6e3
  //   a00893 73 200293 1100493 849493 1148493 900533 2200893 73 2000e13 25484b3 900533 2200893 73 fffe0e13
  //   fe0e16e3 a00893 73 8800493 849493 4848493 8700913 891913 5490913 2997933 1091913 11096913 1200533
  //   2200893 73 a00893 73 313 2000e13 493 100913 930023 900533 2200893 73 12484b3 130313 fffe0e13
  //   fe0e12e3 800e13 313 32483 900533 2200893 73 430313 fffe0e13 fe0e14e3 a00893 73
  //   IR
  //   PC
  //   PC+4
  //   ID
  //   控制位
  //   流水调试日志用
  //   暂停节拍，不能为0
  //   戳工具置1进入计数暂停模式，ctrl+k时钟自动运行到对应节拍暂停
  //   ctrl+k关闭时钟连续运行，将控制位置零，进入单步调试模式调试
  //   用这个时钟源需要去掉电路中的其他时钟源
  //   JAL
  //   JALR
  //   URET
  //   Beq
  //   Bne
  //   MemToReg
  //   MemWrite
  //   AluOP
  //   AluSrcB
  //   RegWrite
  //   可计数暂停的时钟源
  //   为方便自动评测，需要输出流水线各段保存的PC值，注意是PC不是PC+4，另外ID段寄存器写入信息，Mem段内存写入信息也要输出
endmodule

module \重定向流水线  (
  output RegWrite,
  output MemWrite,
  output [31:0] IF_PC,
  output [31:0] ID_PC,
  output [31:0] EX_PC,
  output [31:0] M_PC,
  output [31:0] WB_PC,
  output [31:0] RDin,
  output [31:0] MDin,
  output [31:0] LedData
);

  wire and_1_out, and_2_out, and_3_out, and_5_out, and_6_out, and_7_out, CLK, clock_1_out, comparator_1_eq,
       comparator_1_lt, comparator_2_eq, d_ff_1_q, ENS, EX_ALUequal, EX_ALUless, EX_AluSrcB, EX_BE, EX_BEQ,
       EX_BLTU, EX_BNE, EX_branch, EX_ecall, EX_JAL, EX_JALR, EX_JUMP, EX_LBU, EX_MemToReg, EX_MemWrite,
       EX_RegWrite, EX_Stype, Go, halt, ID_AluSrcB, ID_BEQ, ID_BLTU, ID_BNE, ID_ecall, ID_JAL, ID_JALR,
       ID_LBU, ID_MemToReg, ID_MemWrite, ID_RegWrite, ID_Stype, ID_URET, IR1, IR2, IR3, load, MEM_AluSrcB,
       MEM_BE, MEM_BEQ, MEM_BLTU, MEM_BNE, MEM_ecall, MEM_JAL, MEM_JALR, MEM_LBU, MEM_MemToReg, MEM_RegWrite,
       MEM_Stype, nand_1_out, nor_1_out, not_2_out, not_3_out, not_4_out, not_5_out, not_6_out, or_1_out,
       or_2_out, or_6_out, RST, W1, W2, W3, WB_AluSrcB, WB_BE, WB_BEQ, WB_BLTU, WB_BNE, WB_ecall, WB_JAL,
       WB_JALR, WB_LBU, WB_MemToReg, WB_MemWrite, WB_Stype, \单周期硬布线控制器_1_rsread , \单周期硬布线控制器_1_rtread ;
  wire [1:0] EX_RSGO, EX_RTGO, ID_RSGO, ID_RTGO;
  wire [3:0] EX_AluOP, ID_AluOP, MEM_AluOP, WB_AluOP;
  wire [4:0] EX_W_num, MEM_W_num, RS_id, RT_id, WB_W_num;
  wire [7:0] multiplexer_10_out;
  wire [11:0] multiplexer_3_out;
  wire [12:0] CNT_num;
  wire [15:0] \LoadUse次数 , \总周期数 , \插入气泡数 , \无条件分支数 , \条件分支成功数 ;
  wire [31:0] bit_extender_2_out, bit_extender_3_out, bit_extender_4_out, EX_BEADDR, EX_IMM, EX_IR,
       EX_JALADDR, EX_PCP4, EX_R1, EX_R2, EX_Result, ID_BEADDR, id_ex_1_r1out, id_ex_1_r2out, ID_IMM, ID_IR,
       ID_JALADDR, ID_PCP4, ID_R1, ID_R2, IF_IR, IF_PCP4, MEM_ALUOUT, MEM_BEADDR, MEM_IMM, MEM_IR,
       MEM_JALADDR, MEM_PCP4, MEM_R1, mem_wb_1_aluresultout, mem_wb_1_memout, multiplexer_6_out,
       multiplexer_7_out, multiplexer_8_out, multiplexer_11_out, multiplexer_12_out, PCnext, ram_1_data,
       shifter_1_out, shifter_2_out, WB_BEADDR, WB_IR, WB_JALADDR, WB_PCP4, WB_R1, WB_R2;

  Button \u_总复位  (.out(RST));
  Button _1 (.out(IR1));
  Button _2 (.out(IR2));
  Button _3 (.out(IR3));
  // Probe on \总周期数 
  // Probe on \总周期数 
  Button \u_继续运行  (.out(Go));
  LED #(.active("true")) led_1 (.in(W1));
  LED #(.active("true")) led_2 (.in(W2));
  LED #(.active("true")) led_3 (.in(W3));
  Hex_Digit_Display hex_digit_display_1 (.value(LedData[31:28]));  // open: dp
  // Probe on IF_PC[19:0]
  // RiscV_Probe riscv_probe_1: pin names not known; wires that end beside it: IF_IR
  not not_1 (ENS, halt);
  Hex_Digit_Display hex_digit_display_2 (.value(LedData[27:24]));  // open: dp
  Hex_Digit_Display hex_digit_display_3 (.value(LedData[23:20]));  // open: dp
  // Probe on ID_PC[19:0]
  // RiscV_Probe riscv_probe_2: pin names not known; wires that end beside it: ID_IR
  Register #(.width(32), .trigger("rising"), .Select("low")) PC (
    .D(PCnext), .en(not_2_out), .Q(IF_PC), .clk(CLK), .clr(RST));
  not not_2 (not_2_out, or_1_out);
  or or_1 (or_1_out, load, halt);
  Hex_Digit_Display hex_digit_display_4 (.value(LedData[15:12]));  // open: dp
  Hex_Digit_Display hex_digit_display_5 (.value(LedData[19:16]));  // open: dp
  Adder #(.width(32)) adder_1 (.a(IF_PC), .b(32'h4), .out(IF_PCP4));  // open: cin, cout
  Hex_Digit_Display hex_digit_display_6 (.value(LedData[7:4]));  // open: dp
  Hex_Digit_Display hex_digit_display_7 (.value(LedData[11:8]));  // open: dp
  // Probe on EX_PC[19:0]
  // RiscV_Probe riscv_probe_3: pin names not known; wires that end beside it: EX_IR
  Hex_Digit_Display hex_digit_display_8 (.value(LedData[3:0]));  // open: dp
  ROM #(.addrWidth(10), .dataWidth(32), .Select("high")) rom_1 (.addr(IF_PC[11:2]), .data(IF_IR));
  // Probe on \总周期数 
  // Probe on M_PC[19:0]
  // RiscV_Probe riscv_probe_4: pin names not known; wires that end beside it: MEM_IR
  // RiscV_Probe riscv_probe_5: pin names not known; wires that end beside it: IF_IR
  // Probe on \总周期数 
  // Probe on \无条件分支数 
  // Probe on \条件分支成功数 
  // Probe on \插入气泡数 
  // Probe on \LoadUse次数 
  IF_ID if_id_1 (
    .CLK(CLK), .IRin(IF_IR), .IRout(ID_IR), .PCP4in(IF_PCP4), .PCP4out(ID_PCP4), .EN(nor_1_out),
    .RESET(EX_branch), .PCin(IF_PC), .PCout(ID_PC));
  nor nor_1 (nor_1_out, halt, load);
  // Probe on IF_PC[11:0]
  // Probe on WB_PC[19:0]
  // RiscV_Probe riscv_probe_6: pin names not known; wires that end beside it: WB_IR
  // RiscV_Probe riscv_probe_7: pin names not known; wires that end beside it: ID_IR
  // Probe on ID_PC[11:0]
  // Probe on EX_PC[11:0]
  // Probe on M_PC[11:0]
  D_Flip_Flop #(.trigger("high"), .Pre_Clr_Positions("LEGACY"), .NegatePresetClear("false"), .enable("true"), .NewFFLayout("false")) d_ff_1 (.Q(d_ff_1_q));  // open: clk, D, Qn, preset, en, reset
  // Probe on 13'hc
  // Probe on WB_PC[11:0]
  Comparator #(.width(13), .mode("twosComplement")) comparator_1 (
    .a(CNT_num), .b(13'hc), .eq(comparator_1_eq), .lt(comparator_1_lt));  // open: gt
  Clock #(.highDuration(1), .lowDuration(1)) clock_1 (.out(clock_1_out));
  and and_1 (and_1_out, not_3_out, CLK);
  not not_3 (not_3_out, WB_ecall);
  nand nand_1 (nand_1_out, d_ff_1_q, comparator_1_eq);
  Counter #(.width(13), .max('h1fff), .ongoal("stay"), .trigger("rising"), .behavior("old")) counter_1 (
    .count(comparator_1_lt), .Q(CNT_num), .clk(clock_1_out));  // open: load, D, carry, clr, preset
  Comparator #(.width(32), .mode("twosComplement")) comparator_2 (
    .a(WB_R1), .b(32'h22), .eq(comparator_2_eq));  // open: gt, lt
  Counter #(.width(16), .max('hffff), .ongoal("wrap"), .trigger("rising"), .behavior("new")) counter_2 (
    .D({16{1'b0}}), .Q(\总周期数 ), .clk(and_1_out));  // open: load, count, carry, clr, preset, down
  assign CLK = nand_1_out ? clock_1_out : 1'bz;  // Controlled_Buffer controlled_buffer_1
  \重定向判决  \u_重定向判决_1  (
    .RSU(\单周期硬布线控制器_1_rsread ), .RTU(\单周期硬布线控制器_1_rtread ), .RSid(RS_id), .RTid(RT_id),
    .EX_reg_write(EX_RegWrite), .MEM_reg_write(MEM_RegWrite), .EX_Wid(EX_W_num), .MEM_Wid(MEM_W_num),
    .EX_memtoreg(EX_MemToReg), .RSGO(ID_RSGO), .RTGO(ID_RTGO), .load(load));
  \单周期硬布线控制器  \u_单周期硬布线控制器_1  (
    .Funct({ID_IR[30], ID_IR[25], ID_IR[14:12]}), .OP(ID_IR[6:2]), .ALU_OP(ID_AluOP), .MemToReg(ID_MemToReg),
    .MemWrite(ID_MemWrite), .ALU_SRC(ID_AluSrcB), .ecall(ID_ecall), .S_type(ID_Stype), .Jalr(ID_JALR),
    .Beq(ID_BEQ), .JAL(ID_JAL), .Bne(ID_BNE), .in_3(ID_IR[21]), .uret(ID_URET), .LBU(ID_LBU), .BLTU(ID_BLTU),
    .RSread(\单周期硬布线控制器_1_rsread ), .RTread(\单周期硬布线控制器_1_rtread ), .RegWrite(ID_RegWrite));  // open: CSC
  Multiplexer #(.select(1), .width(5), .disabled("Z"), .enable("false")) multiplexer_1 (
    .in0(ID_IR[19:15]), .in1(5'b10001), .out(RS_id), .sel(ID_ecall));
  Multiplexer #(.select(1), .width(5), .disabled("Z"), .enable("false")) multiplexer_2 (
    .in0(ID_IR[24:20]), .in1(5'b01010), .out(RT_id), .sel(ID_ecall));
  Multiplexer #(.select(1), .width(12), .disabled("Z"), .enable("false")) multiplexer_3 (
    .in0(ID_IR[31:20]), .in1({ID_IR[31:25], ID_IR[11:7]}), .out(multiplexer_3_out), .sel(ID_Stype));
  not not_4 (not_4_out, comparator_2_eq);
  Pull_Resistor #(.pull(1)) pull_resistor_1 (.node(CLK));
  assign ID_IMM = {{20{multiplexer_3_out[11]}}, multiplexer_3_out};  // Bit_Extender bit_extender_1
  assign bit_extender_2_out = {{20{ID_IR[31]}}, {ID_IR[31], ID_IR[7], ID_IR[30:25], ID_IR[11:8]}};  // Bit_Extender bit_extender_2
  assign bit_extender_3_out = {{12{ID_IR[31]}}, {ID_IR[31], ID_IR[19:12], ID_IR[20], ID_IR[30:21]}};  // Bit_Extender bit_extender_3
  and and_2 (and_2_out, not_4_out, WB_ecall);
  and and_3 (and_3_out, comparator_2_eq, WB_ecall);
  Shifter #(.width(32), .shift("ll")) shifter_1 (.in(bit_extender_2_out), .\dist (5'b00001), .out(shifter_1_out));
  Shifter #(.width(32), .shift("ll")) shifter_2 (.in(bit_extender_3_out), .\dist (5'b00001), .out(shifter_2_out));
  not not_5 (not_5_out, Go);
  and and_4 (halt, not_5_out, and_2_out);
  Regifile regifile_1 (
    .Din(RDin), .Clk(CLK), .R1(ID_R1), .R2(ID_R2), .WE(RegWrite), .W_num(WB_W_num), .R1_num(RS_id),
    .R2_num(RT_id));
  Adder #(.width(32)) adder_2 (.a(shifter_1_out), .b(ID_PC), .out(ID_BEADDR), .cin(1'b0));  // open: cout
  Adder #(.width(32)) adder_3 (.a(shifter_2_out), .b(ID_PC), .out(ID_JALADDR), .cin(1'b0));  // open: cout
  Register #(.width(32), .trigger("rising"), .Select("low")) register_1 (
    .D(WB_R2), .en(and_3_out), .Q(LedData), .clk(CLK));  // open: clr
  ID_EX id_ex_1 (
    .CLK(CLK), .EN(ENS), .RESET(or_2_out), .RegWritein(ID_RegWrite), .MemToRegin(ID_MemToReg),
    .MemWritein(ID_MemWrite), .ALUOPin(ID_AluOP), .ALUSrcin(ID_AluSrcB), .ecallin(ID_ecall),
    .Stypein(ID_Stype), .BEQin(ID_BEQ), .BNEin(ID_BNE), .JALRin(ID_JALR), .BLTUin(ID_BLTU), .JALin(ID_JAL),
    .RegWriteout(EX_RegWrite), .MemToRegout(EX_MemToReg), .MemWriteout(EX_MemWrite), .ALUOPout(EX_AluOP),
    .ALUSrcout(EX_AluSrcB), .ecallout(EX_ecall), .Stypeout(EX_Stype), .BEQout(EX_BEQ), .BNEout(EX_BNE),
    .JALout(EX_JAL), .JALRout(EX_JALR), .LBUin(ID_LBU), .LBUout(EX_LBU), .BLTUout(EX_BLTU), .R1in(ID_R1),
    .R1out(id_ex_1_r1out), .R2in(ID_R2), .R2out(id_ex_1_r2out), .W_in(ID_IR[11:7]), .W_out(EX_W_num),
    .Immin(ID_IMM), .Immout(EX_IMM), .BEADDRin(ID_BEADDR), .BEADDRout(EX_BEADDR), .PCin(ID_PC),
    .PCout(EX_PC), .PCP4in(ID_PCP4), .PCP4out(EX_PCP4), .JALADDrin(ID_JALADDR), .JALADDRout(EX_JALADDR),
    .IRin(ID_IR), .IRout(EX_IR), .RSGOin(ID_RSGO), .RSGOout(EX_RSGO), .RTGOin(ID_RTGO), .RTGOout(EX_RTGO));
  or or_2 (or_2_out, EX_branch, load);
  Multiplexer #(.select(2), .width(32), .disabled("Z"), .enable("false")) multiplexer_4 (
    .in0(id_ex_1_r1out), .in1(RDin), .in2(MEM_ALUOUT), .out(EX_R1), .sel(EX_RSGO));  // open: in3
  Multiplexer #(.select(2), .width(32), .disabled("Z"), .enable("false")) multiplexer_5 (
    .in0(id_ex_1_r2out), .in1(RDin), .in2(MEM_ALUOUT), .out(EX_R2), .sel(EX_RTGO));  // open: in3
  Multiplexer #(.select(1), .width(32), .disabled("Z"), .enable("false")) multiplexer_6 (
    .in0(IF_PCP4), .in1(EX_BEADDR), .out(multiplexer_6_out), .sel(EX_BE));
  Multiplexer #(.select(1), .width(32), .disabled("Z"), .enable("false")) multiplexer_7 (
    .in0(multiplexer_6_out), .in1(EX_JALADDR), .out(multiplexer_7_out), .sel(EX_JAL));
  Multiplexer #(.select(1), .width(32), .disabled("Z"), .enable("false")) multiplexer_8 (
    .in0(EX_R2), .in1(EX_IMM), .out(multiplexer_8_out), .sel(EX_AluSrcB));
  and and_5 (and_5_out, EX_ALUequal, EX_BEQ);
  not not_6 (not_6_out, EX_ALUequal);
  and and_6 (and_6_out, not_6_out, EX_BNE);
  and and_7 (and_7_out, EX_ALUless, EX_BLTU);
  or or_3 (EX_JUMP, EX_JAL, EX_JALR);
  Multiplexer #(.select(1), .width(32), .disabled("Z"), .enable("false")) multiplexer_9 (
    .in0(multiplexer_7_out), .in1(EX_Result), .out(PCnext), .sel(EX_JALR));
  or or_4 (EX_BE, and_5_out, and_6_out, and_7_out);
  ALU alu_1 (
    .X(EX_R1), .Y(multiplexer_8_out), .AluOP(EX_AluOP), .Equal(EX_ALUequal), .Result(EX_Result),
    .out_6(EX_ALUless));  // open: Result_2, out_4
  or or_5 (EX_branch, EX_BE, EX_JUMP);
  EX_MEM ex_mem_1 (
    .CLK(CLK), .EN(ENS), .RESET(1'b0), .RegWritein(EX_RegWrite), .MemToRegin(EX_MemToReg),
    .MemWritein(EX_MemWrite), .ALUOPin(EX_AluOP), .ALUSrcin(EX_AluSrcB), .ecallin(EX_ecall),
    .Stypein(EX_Stype), .BEQin(EX_BEQ), .BNEin(EX_BNE), .JALin(EX_JAL), .JALRin(EX_JALR), .LBUin(EX_LBU),
    .BLTUin(EX_BLTU), .W_in(EX_W_num), .Immin(EX_IMM), .BEADDRin(EX_BEADDR), .PCin(EX_PC), .PCP4in(EX_PCP4),
    .JALADDrin(EX_JALADDR), .RegWriteout(MEM_RegWrite), .MemToRegout(MEM_MemToReg), .MemWriteout(MemWrite),
    .ALUOPout(MEM_AluOP), .ALUSrcout(MEM_AluSrcB), .ecallout(MEM_ecall), .Stypeout(MEM_Stype),
    .BEQout(MEM_BEQ), .BNEout(MEM_BNE), .JALout(MEM_JAL), .JALRout(MEM_JALR), .LBUout(MEM_LBU),
    .BLTUout(MEM_BLTU), .W_out(MEM_W_num), .Immout(MEM_IMM), .BEADDRout(MEM_BEADDR), .PCout(M_PC),
    .PCP4out(MEM_PCP4), .JALADDRout(MEM_JALADDR), .BEin(EX_BE), .BEout(MEM_BE), .ALUResultin(EX_Result),
    .ALUResultout(MEM_ALUOUT), .R1in(EX_R1), .R1out(MEM_R1), .R2in(EX_R2), .R2out(MDin), .IRin(EX_IR),
    .IRout(MEM_IR));
  RAM #(.addrWidth(10), .dataWidth(32), .bus("separate"), .Select("high")) ram_1 (
    .addr(MEM_ALUOUT[11:2]), .din(MDin), .data(ram_1_data), .str(MemWrite), .clk(CLK));  // open: sel, ld, clr
  Multiplexer #(.select(2), .width(8), .disabled("Z"), .enable("false")) multiplexer_10 (
    .in0(ram_1_data[7:0]), .in1(ram_1_data[15:8]), .in2(ram_1_data[23:16]), .in3(ram_1_data[31:24]),
    .out(multiplexer_10_out), .sel(MEM_ALUOUT[1:0]));
  assign bit_extender_4_out = {{24{1'b0}}, multiplexer_10_out};  // Bit_Extender bit_extender_4
  Multiplexer #(.select(1), .width(32), .disabled("Z"), .enable("false")) multiplexer_11 (
    .in0(ram_1_data), .in1(bit_extender_4_out), .out(multiplexer_11_out), .sel(MEM_LBU));
  MEM_WB mem_wb_1 (
    .CLK(CLK), .EN(ENS), .RESET(1'b0), .RegWritein(MEM_RegWrite), .RegWriteout(RegWrite),
    .MemToRegin(MEM_MemToReg), .MemToRegout(WB_MemToReg), .MemWritein(MemWrite), .MemWriteout(WB_MemWrite),
    .ALUOPin(MEM_AluOP), .ALUOPout(WB_AluOP), .ALUSrcin(MEM_AluSrcB), .ALUSrcout(WB_AluSrcB),
    .ecallin(MEM_ecall), .ecallout(WB_ecall), .Stypein(MEM_Stype), .Stypeout(WB_Stype), .BEQin(MEM_BEQ),
    .BEQout(WB_BEQ), .BNEin(MEM_BNE), .BNEout(WB_BNE), .JALin(MEM_JAL), .JALout(WB_JAL), .JALRin(MEM_JALR),
    .JALRout(WB_JALR), .LBUin(MEM_LBU), .LBUout(WB_LBU), .BLTUin(MEM_BLTU), .BLTUout(WB_BLTU),
    .W_in(MEM_W_num), .W_out(WB_W_num), .Memin(multiplexer_11_out), .Memout(mem_wb_1_memout),
    .BEADDRin(MEM_BEADDR), .BEADDRout(WB_BEADDR), .PCin(M_PC), .PCout(WB_PC), .PCP4in(MEM_PCP4),
    .PCP4out(WB_PCP4), .JALADDrin(MEM_JALADDR), .JALADDRout(WB_JALADDR), .BEin(MEM_BE), .BEout(WB_BE),
    .ALUResultin(MEM_ALUOUT), .ALUResultout(mem_wb_1_aluresultout), .IRin(MEM_IR), .IRout(WB_IR),
    .R1in(MEM_R1), .R1out(WB_R1), .R2in(MDin), .R2out(WB_R2));
  Multiplexer #(.select(1), .width(32), .disabled("Z"), .enable("false")) multiplexer_12 (
    .in0(mem_wb_1_aluresultout), .in1(mem_wb_1_memout), .out(multiplexer_12_out), .sel(WB_MemToReg));
  or or_6 (or_6_out, WB_JAL, WB_JALR);
  Multiplexer #(.select(1), .width(32), .disabled("Z"), .enable("false")) multiplexer_13 (
    .in0(multiplexer_12_out), .in1(WB_PCP4), .out(RDin), .sel(or_6_out));

  // Other names for the same wires on the sheet: ID_W_num[4:0] = ID_IR[11:7]; MEM_MemWrite = MemWrite;
  //   MEM_PC[31:0] = M_PC; MEM_R2[31:0] = MDin; WB_RegWrite = RegWrite

  // Notes on the sheet:
  //   中断源
  //   时空图监测，可删除
  //   中断等待指示
  //   数码管输出
  //   IF
  //   指令存储器
  //   contents of rom_1 (hex, n*v repeats v):
  //   100493 100006f 100493 200913 300993 100006f 100493 200913 300993 100006f 100493 200913 300993
  //   100006f 100493 200913 300993 29c000ef 100413 100493 1f49493 900533 2200893 73 24d493 48463 fedff06f
  //   900533 2200893 73 100493 249493 900533 2200893 73 48463 fedff06f 100493 1f49493 900533 2200893 73
  //   4034d493 900533 2200893 73 4044d493 900533 2200893 73 4044d493 900533 2200893 73 4044d493 900533
  //   2200893 73 4044d493 900533 2200893 73 4044d493 900533 2200893 73 4044d493 900533 2200893 73 4044d493
  //   900533 2200893 73 100413 1f41993 41f9d993 433 c00913 300b13 140413 f47413 800293 100313 499993
  //   89e9b3 1300533 2200893 73 406282b3 fe0294e3 140413 f00f93 1f47433 1c41413 800293 100313 49d993
  //   89e9b3 1300533 2200893 73 406282b3 fe0294e3 1c45413 406b0b33 b0463 f95ff06f 2b3 fff2c293 829293
  //   ff2e293 500533 2200893 73 fff00413 493 84a023 140413 448493 84a023 140413 448493 84a023 140413
  //   448493 84a023 140413 448493 84a023 140413 448493 84a023 140413 448493 84a023 140413 448493 84a023
  //   140413 448493 84a023 140413 448493 84a023 140413 448493 84a023 140413 448493 84a023 140413 448493
  //   84a023 140413 448493 84a023 140413 448493 84a023 140413 448493 84a023 140413 448493 140413 433
  //   3c00493 42983 4aa03 149a2b3 28663 134a023 1442023 ffc48493 fe9412e3 800533 2200893 73 440413 3c00493
  //   fc9416e3 a00893 73 413 140413 800533 2200893 73 240413 800533 2200893 73 340413 800533 2200893 73
  //   440413 800533 2200893 73 540413 800533 2200893 73 640413 800533 2200893 73 740413 800533 2200893 73
  //   840413 800533 2200893 2200893 73 8067
  //   IR
  //   PC
  //   PC+4
  //   控制位
  //   ID
  //   流水调试日志用
  //   暂停节拍，不能为0
  //   戳工具置1进入计数暂停模式，ctrl+k时钟自动运行到对应节拍暂停
  //   ctrl+k关闭时钟连续运行，将控制位置零，进入单步调试模式调试
  //   JAL
  //   JALR
  //   URET
  //   可计数暂停的时钟源
  //   Beq
  //   Bne
  //   MemToReg
  //   MemWrite
  //   AluOP
  //   AluSrcB
  //   RegWrite
  //   为方便自动评测，需要输出流水线各段保存的PC值，注意是PC不是PC+4，另外ID段寄存器写入信息，Mem段内存写入信息也要输出
endmodule

module \气泡流水线  (
  output RegWrite,
  output MemWrite,
  output [31:0] IF_PC,
  output [31:0] ID_PC,
  output [31:0] EX_PC,
  output [31:0] M_PC,
  output [31:0] WB_PC,
  output [31:0] RDin,
  output [31:0] MDin,
  output [31:0] LedData
);

  wire and_1_out, and_2_out, and_3_out, and_5_out, and_6_out, and_7_out, bubble, CLK, clock_1_out,
       comparator_1_eq, comparator_2_eq, comparator_2_lt, d_ff_1_q, ENS, EX_ALUequal, EX_ALUless, EX_AluSrcB,
       EX_BE, EX_BEQ, EX_BLTU, EX_BNE, EX_branch, EX_ecall, EX_JAL, EX_JALR, EX_JUMP, EX_LBU, EX_MemToReg,
       EX_MemWrite, EX_RegWrite, EX_Stype, Go, halt, ID_AluSrcB, ID_BEQ, ID_BLTU, ID_BNE, ID_ecall, ID_JAL,
       ID_JALR, ID_LBU, ID_MemToReg, ID_MemWrite, ID_RegWrite, ID_Stype, ID_URET, IR1, IR2, IR3, MEM_AluSrcB,
       MEM_BE, MEM_BEQ, MEM_BLTU, MEM_BNE, MEM_ecall, MEM_JAL, MEM_JALR, MEM_LBU, MEM_MemToReg, MEM_RegWrite,
       MEM_Stype, nand_1_out, nor_1_out, not_2_out, not_3_out, not_4_out, not_5_out, not_6_out, or_1_out,
       or_2_out, or_6_out, RST, W1, W2, W3, WB_AluSrcB, WB_BE, WB_BEQ, WB_BLTU, WB_BNE, WB_ecall, WB_JAL,
       WB_JALR, WB_LBU, WB_MemToReg, WB_MemWrite, WB_Stype, \单周期硬布线控制器_1_rsread , \单周期硬布线控制器_1_rtread ;
  wire [3:0] EX_AluOP, ID_AluOP, MEM_AluOP, WB_AluOP;
  wire [4:0] EX_W_num, MEM_W_num, RS_id, RT_id, WB_W_num;
  wire [7:0] multiplexer_8_out;
  wire [11:0] multiplexer_3_out;
  wire [12:0] CNT_num;
  wire [15:0] \LoadUse次数 , \总周期数 , \插入气泡数 , \无条件分支数 , \条件分支成功数 ;
  wire [31:0] bit_extender_2_out, bit_extender_3_out, bit_extender_4_out, EX_BEADDR, EX_IMM, EX_IR,
       EX_JALADDR, EX_PCP4, EX_R1, EX_R2, EX_Result, ID_BEADDR, ID_IMM, ID_IR, ID_JALADDR, ID_PCP4, ID_R1,
       ID_R2, IF_IR, IF_PCP4, MEM_ALUOUT, MEM_BEADDR, MEM_IMM, MEM_IR, MEM_JALADDR, MEM_PCP4, MEM_R1,
       mem_wb_1_aluresultout, mem_wb_1_memout, multiplexer_4_out, multiplexer_5_out, multiplexer_6_out,
       multiplexer_9_out, multiplexer_10_out, PCnext, ram_1_data, shifter_1_out, shifter_2_out, WB_BEADDR,
       WB_IR, WB_JALADDR, WB_PCP4, WB_R1, WB_R2;

  Button \u_总复位  (.out(RST));
  Button _1 (.out(IR1));
  Button _2 (.out(IR2));
  Button _3 (.out(IR3));
  // Probe on \总周期数 
  // Probe on \总周期数 
  Button \u_继续运行  (.out(Go));
  LED #(.active("true")) led_1 (.in(W1));
  LED #(.active("true")) led_2 (.in(W2));
  LED #(.active("true")) led_3 (.in(W3));
  Hex_Digit_Display hex_digit_display_1 (.value(LedData[31:28]));  // open: dp
  // Probe on IF_PC[19:0]
  // RiscV_Probe riscv_probe_1: pin names not known; wires that end beside it: IF_IR
  not not_1 (ENS, halt);
  Hex_Digit_Display hex_digit_display_2 (.value(LedData[23:20]));  // open: dp
  Hex_Digit_Display hex_digit_display_3 (.value(LedData[27:24]));  // open: dp
  // Probe on ID_PC[19:0]
  // RiscV_Probe riscv_probe_2: pin names not known; wires that end beside it: ID_IR
  Register #(.width(32), .trigger("rising"), .Select("low")) PC (
    .D(PCnext), .en(not_2_out), .Q(IF_PC), .clk(CLK), .clr(RST));
  not not_2 (not_2_out, or_1_out);
  or or_1 (or_1_out, bubble, halt);
  Hex_Digit_Display hex_digit_display_4 (.value(LedData[19:16]));  // open: dp
  Hex_Digit_Display hex_digit_display_5 (.value(LedData[15:12]));  // open: dp
  Adder #(.width(32)) adder_1 (.a(IF_PC), .b(32'h4), .out(IF_PCP4));  // open: cin, cout
  Hex_Digit_Display hex_digit_display_6 (.value(LedData[7:4]));  // open: dp
  Hex_Digit_Display hex_digit_display_7 (.value(LedData[11:8]));  // open: dp
  // Probe on EX_PC[19:0]
  // RiscV_Probe riscv_probe_3: pin names not known; wires that end beside it: EX_IR
  Hex_Digit_Display hex_digit_display_8 (.value(LedData[3:0]));  // open: dp
  ROM #(.addrWidth(10), .dataWidth(32), .Select("high")) rom_1 (.addr(IF_PC[11:2]), .data(IF_IR));
  // Probe on \总周期数 
  // Probe on M_PC[19:0]
  // RiscV_Probe riscv_probe_4: pin names not known; wires that end beside it: MEM_IR
  // RiscV_Probe riscv_probe_5: pin names not known; wires that end beside it: IF_IR
  // Probe on \总周期数 
  // Probe on \无条件分支数 
  // Probe on \条件分支成功数 
  // Probe on \插入气泡数 
  // Probe on \LoadUse次数 
  IF_ID if_id_1 (
    .CLK(CLK), .IRin(IF_IR), .IRout(ID_IR), .PCP4in(IF_PCP4), .PCP4out(ID_PCP4), .EN(nor_1_out),
    .RESET(EX_branch), .PCin(IF_PC), .PCout(ID_PC));
  nor nor_1 (nor_1_out, halt, bubble);
  and and_1 (and_1_out, not_3_out, CLK);
  not not_3 (not_3_out, WB_ecall);
  // Probe on IF_PC[11:0]
  // Probe on WB_PC[19:0]
  // RiscV_Probe riscv_probe_6: pin names not known; wires that end beside it: WB_IR
  // RiscV_Probe riscv_probe_7: pin names not known; wires that end beside it: ID_IR
  Comparator #(.width(32), .mode("twosComplement")) comparator_1 (
    .a(WB_R1), .b(32'h22), .eq(comparator_1_eq));  // open: gt, lt
  Counter #(.width(16), .max('hffff), .ongoal("wrap"), .trigger("rising"), .behavior("new")) counter_1 (
    .D({16{1'b0}}), .Q(\总周期数 ), .clk(and_1_out));  // open: load, count, carry, clr, preset, down
  // Probe on EX_PC[11:0]
  // Probe on ID_PC[11:0]
  not not_4 (not_4_out, comparator_1_eq);
  // Probe on M_PC[11:0]
  D_Flip_Flop #(.trigger("high"), .Pre_Clr_Positions("LEGACY"), .NegatePresetClear("false"), .enable("true"), .NewFFLayout("false")) d_ff_1 (.Q(d_ff_1_q));  // open: clk, D, Qn, preset, en, reset
  // Probe on 13'h48
  and and_2 (and_2_out, not_4_out, WB_ecall);
  and and_3 (and_3_out, comparator_1_eq, WB_ecall);
  // Probe on WB_PC[11:0]
  Comparator #(.width(13), .mode("twosComplement")) comparator_2 (
    .a(CNT_num), .b(13'h48), .eq(comparator_2_eq), .lt(comparator_2_lt));  // open: gt
  Clock #(.highDuration(1), .lowDuration(1)) clock_1 (.out(clock_1_out));
  not not_5 (not_5_out, Go);
  and and_4 (halt, not_5_out, and_2_out);
  nand nand_1 (nand_1_out, d_ff_1_q, comparator_2_eq);
  Counter #(.width(13), .max('h1fff), .ongoal("stay"), .trigger("rising"), .behavior("old")) counter_2 (
    .count(comparator_2_lt), .Q(CNT_num), .clk(clock_1_out));  // open: load, D, carry, clr, preset
  Register #(.width(32), .trigger("rising"), .Select("low")) register_1 (
    .D(WB_R2), .en(and_3_out), .Q(LedData), .clk(CLK));  // open: clr
  assign CLK = nand_1_out ? clock_1_out : 1'bz;  // Controlled_Buffer controlled_buffer_1
  \单周期硬布线控制器  \u_单周期硬布线控制器_1  (
    .Funct({ID_IR[30], ID_IR[25], ID_IR[14:12]}), .OP(ID_IR[6:2]), .ALU_OP(ID_AluOP), .MemToReg(ID_MemToReg),
    .MemWrite(ID_MemWrite), .ALU_SRC(ID_AluSrcB), .ecall(ID_ecall), .S_type(ID_Stype), .Jalr(ID_JALR),
    .Beq(ID_BEQ), .JAL(ID_JAL), .Bne(ID_BNE), .in_3(ID_IR[21]), .uret(ID_URET), .LBU(ID_LBU), .BLTU(ID_BLTU),
    .RSread(\单周期硬布线控制器_1_rsread ), .RTread(\单周期硬布线控制器_1_rtread ), .RegWrite(ID_RegWrite));  // open: CSC
  Multiplexer #(.select(1), .width(5), .disabled("Z"), .enable("false")) multiplexer_1 (
    .in0(ID_IR[19:15]), .in1(5'b10001), .out(RS_id), .sel(ID_ecall));
  Multiplexer #(.select(1), .width(5), .disabled("Z"), .enable("false")) multiplexer_2 (
    .in0(ID_IR[24:20]), .in1(5'b01010), .out(RT_id), .sel(ID_ecall));
  Multiplexer #(.select(1), .width(12), .disabled("Z"), .enable("false")) multiplexer_3 (
    .in0(ID_IR[31:20]), .in1({ID_IR[31:25], ID_IR[11:7]}), .out(multiplexer_3_out), .sel(ID_Stype));
  Pull_Resistor #(.pull(1)) pull_resistor_1 (.node(CLK));
  assign ID_IMM = {{20{multiplexer_3_out[11]}}, multiplexer_3_out};  // Bit_Extender bit_extender_1
  assign bit_extender_2_out = {{20{ID_IR[31]}}, {ID_IR[31], ID_IR[7], ID_IR[30:25], ID_IR[11:8]}};  // Bit_Extender bit_extender_2
  assign bit_extender_3_out = {{12{ID_IR[31]}}, {ID_IR[31], ID_IR[19:12], ID_IR[20], ID_IR[30:21]}};  // Bit_Extender bit_extender_3
  Shifter #(.width(32), .shift("ll")) shifter_1 (.in(bit_extender_2_out), .\dist (5'b00001), .out(shifter_1_out));
  Shifter #(.width(32), .shift("ll")) shifter_2 (.in(bit_extender_3_out), .\dist (5'b00001), .out(shifter_2_out));
  Regifile regifile_1 (
    .Din(RDin), .Clk(CLK), .R1(ID_R1), .R2(ID_R2), .WE(RegWrite), .W_num(WB_W_num), .R1_num(RS_id),
    .R2_num(RT_id));
  Adder #(.width(32)) adder_2 (.a(shifter_1_out), .b(ID_PC), .out(ID_BEADDR), .cin(1'b0));  // open: cout
  Adder #(.width(32)) adder_3 (.a(shifter_2_out), .b(ID_PC), .out(ID_JALADDR), .cin(1'b0));  // open: cout
  \流水判决  \u_流水判决_1  (
    .RSU(\单周期硬布线控制器_1_rsread ), .RTU(\单周期硬布线控制器_1_rtread ), .RSid(RS_id), .RTid(RT_id),
    .EX_regwrite(EX_RegWrite), .MEM_regwrite(MEM_RegWrite), .EX_WID(EX_W_num), .MEM_WID(MEM_W_num),
    .bubble(bubble));
  ID_EX id_ex_1 (
    .CLK(CLK), .EN(ENS), .RESET(or_2_out), .RegWritein(ID_RegWrite), .MemToRegin(ID_MemToReg),
    .MemWritein(ID_MemWrite), .ALUOPin(ID_AluOP), .ALUSrcin(ID_AluSrcB), .ecallin(ID_ecall),
    .Stypein(ID_Stype), .BEQin(ID_BEQ), .BNEin(ID_BNE), .JALRin(ID_JALR), .BLTUin(ID_BLTU), .JALin(ID_JAL),
    .RegWriteout(EX_RegWrite), .MemToRegout(EX_MemToReg), .MemWriteout(EX_MemWrite), .ALUOPout(EX_AluOP),
    .ALUSrcout(EX_AluSrcB), .ecallout(EX_ecall), .Stypeout(EX_Stype), .BEQout(EX_BEQ), .BNEout(EX_BNE),
    .JALout(EX_JAL), .JALRout(EX_JALR), .LBUin(ID_LBU), .LBUout(EX_LBU), .BLTUout(EX_BLTU), .R1in(ID_R1),
    .R1out(EX_R1), .R2in(ID_R2), .R2out(EX_R2), .W_in(ID_IR[11:7]), .W_out(EX_W_num), .Immin(ID_IMM),
    .Immout(EX_IMM), .BEADDRin(ID_BEADDR), .BEADDRout(EX_BEADDR), .PCin(ID_PC), .PCout(EX_PC),
    .PCP4in(ID_PCP4), .PCP4out(EX_PCP4), .JALADDrin(ID_JALADDR), .JALADDRout(EX_JALADDR), .IRin(ID_IR),
    .IRout(EX_IR));  // open: RSGOin, RSGOout, RTGOin, RTGOout
  or or_2 (or_2_out, EX_branch, bubble);
  Multiplexer #(.select(1), .width(32), .disabled("Z"), .enable("false")) multiplexer_4 (
    .in0(EX_R2), .in1(EX_IMM), .out(multiplexer_4_out), .sel(EX_AluSrcB));
  ALU alu_1 (
    .X(EX_R1), .Y(multiplexer_4_out), .AluOP(EX_AluOP), .Equal(EX_ALUequal), .Result(EX_Result),
    .out_6(EX_ALUless));  // open: Result_2, out_4
  Multiplexer #(.select(1), .width(32), .disabled("Z"), .enable("false")) multiplexer_5 (
    .in0(IF_PCP4), .in1(EX_BEADDR), .out(multiplexer_5_out), .sel(EX_BE));
  Multiplexer #(.select(1), .width(32), .disabled("Z"), .enable("false")) multiplexer_6 (
    .in0(multiplexer_5_out), .in1(EX_JALADDR), .out(multiplexer_6_out), .sel(EX_JAL));
  and and_5 (and_5_out, EX_ALUequal, EX_BEQ);
  not not_6 (not_6_out, EX_ALUequal);
  and and_6 (and_6_out, not_6_out, EX_BNE);
  and and_7 (and_7_out, EX_ALUless, EX_BLTU);
  or or_3 (EX_JUMP, EX_JAL, EX_JALR);
  Multiplexer #(.select(1), .width(32), .disabled("Z"), .enable("false")) multiplexer_7 (
    .in0(multiplexer_6_out), .in1(EX_Result), .out(PCnext), .sel(EX_JALR));
  or or_4 (EX_BE, and_5_out, and_6_out, and_7_out);
  or or_5 (EX_branch, EX_BE, EX_JUMP);
  EX_MEM ex_mem_1 (
    .CLK(CLK), .EN(ENS), .RESET(1'b0), .RegWritein(EX_RegWrite), .MemToRegin(EX_MemToReg),
    .MemWritein(EX_MemWrite), .ALUOPin(EX_AluOP), .ALUSrcin(EX_AluSrcB), .ecallin(EX_ecall),
    .Stypein(EX_Stype), .BEQin(EX_BEQ), .BNEin(EX_BNE), .JALin(EX_JAL), .JALRin(EX_JALR), .LBUin(EX_LBU),
    .BLTUin(EX_BLTU), .W_in(EX_W_num), .Immin(EX_IMM), .BEADDRin(EX_BEADDR), .PCin(EX_PC), .PCP4in(EX_PCP4),
    .JALADDrin(EX_JALADDR), .RegWriteout(MEM_RegWrite), .MemToRegout(MEM_MemToReg), .MemWriteout(MemWrite),
    .ALUOPout(MEM_AluOP), .ALUSrcout(MEM_AluSrcB), .ecallout(MEM_ecall), .Stypeout(MEM_Stype),
    .BEQout(MEM_BEQ), .BNEout(MEM_BNE), .JALout(MEM_JAL), .JALRout(MEM_JALR), .LBUout(MEM_LBU),
    .BLTUout(MEM_BLTU), .W_out(MEM_W_num), .Immout(MEM_IMM), .BEADDRout(MEM_BEADDR), .PCout(M_PC),
    .PCP4out(MEM_PCP4), .JALADDRout(MEM_JALADDR), .BEin(EX_BE), .BEout(MEM_BE), .ALUResultin(EX_Result),
    .ALUResultout(MEM_ALUOUT), .R1in(EX_R1), .R1out(MEM_R1), .R2in(EX_R2), .R2out(MDin), .IRin(EX_IR),
    .IRout(MEM_IR));
  RAM #(.addrWidth(10), .dataWidth(32), .bus("separate"), .Select("high")) ram_1 (
    .addr(MEM_ALUOUT[11:2]), .din(MDin), .data(ram_1_data), .str(MemWrite), .clk(CLK));  // open: sel, ld, clr
  Multiplexer #(.select(2), .width(8), .disabled("Z"), .enable("false")) multiplexer_8 (
    .in0(ram_1_data[7:0]), .in1(ram_1_data[15:8]), .in2(ram_1_data[23:16]), .in3(ram_1_data[31:24]),
    .out(multiplexer_8_out), .sel(MEM_ALUOUT[1:0]));
  assign bit_extender_4_out = {{24{1'b0}}, multiplexer_8_out};  // Bit_Extender bit_extender_4
  Multiplexer #(.select(1), .width(32), .disabled("Z"), .enable("false")) multiplexer_9 (
    .in0(ram_1_data), .in1(bit_extender_4_out), .out(multiplexer_9_out), .sel(MEM_LBU));
  MEM_WB mem_wb_1 (
    .CLK(CLK), .EN(ENS), .RESET(1'b0), .RegWritein(MEM_RegWrite), .RegWriteout(RegWrite),
    .MemToRegin(MEM_MemToReg), .MemToRegout(WB_MemToReg), .MemWritein(MemWrite), .MemWriteout(WB_MemWrite),
    .ALUOPin(MEM_AluOP), .ALUOPout(WB_AluOP), .ALUSrcin(MEM_AluSrcB), .ALUSrcout(WB_AluSrcB),
    .ecallin(MEM_ecall), .ecallout(WB_ecall), .Stypein(MEM_Stype), .Stypeout(WB_Stype), .BEQin(MEM_BEQ),
    .BEQout(WB_BEQ), .BNEin(MEM_BNE), .BNEout(WB_BNE), .JALin(MEM_JAL), .JALout(WB_JAL), .JALRin(MEM_JALR),
    .JALRout(WB_JALR), .LBUin(MEM_LBU), .LBUout(WB_LBU), .BLTUin(MEM_BLTU), .BLTUout(WB_BLTU),
    .W_in(MEM_W_num), .W_out(WB_W_num), .Memin(multiplexer_9_out), .Memout(mem_wb_1_memout),
    .BEADDRin(MEM_BEADDR), .BEADDRout(WB_BEADDR), .PCin(M_PC), .PCout(WB_PC), .PCP4in(MEM_PCP4),
    .PCP4out(WB_PCP4), .JALADDrin(MEM_JALADDR), .JALADDRout(WB_JALADDR), .BEin(MEM_BE), .BEout(WB_BE),
    .ALUResultin(MEM_ALUOUT), .ALUResultout(mem_wb_1_aluresultout), .IRin(MEM_IR), .IRout(WB_IR),
    .R1in(MEM_R1), .R1out(WB_R1), .R2in(MDin), .R2out(WB_R2));
  Multiplexer #(.select(1), .width(32), .disabled("Z"), .enable("false")) multiplexer_10 (
    .in0(mem_wb_1_aluresultout), .in1(mem_wb_1_memout), .out(multiplexer_10_out), .sel(WB_MemToReg));
  or or_6 (or_6_out, WB_JAL, WB_JALR);
  Multiplexer #(.select(1), .width(32), .disabled("Z"), .enable("false")) multiplexer_11 (
    .in0(multiplexer_10_out), .in1(WB_PCP4), .out(RDin), .sel(or_6_out));

  // Other names for the same wires on the sheet: ID_W_num[4:0] = ID_IR[11:7]; MEM_MemWrite = MemWrite;
  //   MEM_PC[31:0] = M_PC; MEM_R2[31:0] = MDin; WB_RegWrite = RegWrite

  // Notes on the sheet:
  //   中断源
  //   时空图监测，可删除
  //   中断等待指示
  //   数码管输出
  //   IF
  //   指令存储器
  //   contents of rom_1 (hex, n*v repeats v):
  //   100493 100006f 100493 200913 300993 100006f 100493 200913 300993 100006f 100493 200913 300993
  //   100006f 100493 200913 300993 29c000ef 100413 100493 1f49493 900533 2200893 73 24d493 48463 fedff06f
  //   900533 2200893 73 100493 249493 900533 2200893 73 48463 fedff06f 100493 1f49493 900533 2200893 73
  //   4034d493 900533 2200893 73 4044d493 900533 2200893 73 4044d493 900533 2200893 73 4044d493 900533
  //   2200893 73 4044d493 900533 2200893 73 4044d493 900533 2200893 73 4044d493 900533 2200893 73 4044d493
  //   900533 2200893 73 100413 1f41993 41f9d993 433 c00913 300b13 140413 f47413 800293 100313 499993
  //   89e9b3 1300533 2200893 73 406282b3 fe0294e3 140413 f00f93 1f47433 1c41413 800293 100313 49d993
  //   89e9b3 1300533 2200893 73 406282b3 fe0294e3 1c45413 406b0b33 b0463 f95ff06f 2b3 fff2c293 829293
  //   ff2e293 500533 2200893 73 fff00413 493 84a023 140413 448493 84a023 140413 448493 84a023 140413
  //   448493 84a023 140413 448493 84a023 140413 448493 84a023 140413 448493 84a023 140413 448493 84a023
  //   140413 448493 84a023 140413 448493 84a023 140413 448493 84a023 140413 448493 84a023 140413 448493
  //   84a023 140413 448493 84a023 140413 448493 84a023 140413 448493 84a023 140413 448493 140413 433
  //   3c00493 42983 4aa03 149a2b3 28663 134a023 1442023 ffc48493 fe9412e3 800533 2200893 73 440413 3c00493
  //   fc9416e3 a00893 73 413 140413 800533 2200893 73 240413 800533 2200893 73 340413 800533 2200893 73
  //   440413 800533 2200893 73 540413 800533 2200893 73 640413 800533 2200893 73 740413 800533 2200893 73
  //   840413 800533 2200893 2200893 73 8067
  //   IR
  //   PC
  //   PC+4
  //   控制位
  //   ID
  //   流水调试日志用
  //   暂停节拍，不能为0
  //   戳工具置1进入计数暂停模式，ctrl+k时钟自动运行到对应节拍暂停
  //   ctrl+k关闭时钟连续运行，将控制位置零，进入单步调试模式调试
  //   JAL
  //   JALR
  //   URET
  //   可计数暂停的时钟源
  //   Beq
  //   Bne
  //   MemToReg
  //   MemWrite
  //   AluOP
  //   AluSrcB
  //   RegWrite
  //   为方便自动评测，需要输出流水线各段保存的PC值，注意是PC不是PC+4，另外ID段寄存器写入信息，Mem段内存写入信息也要输出
endmodule

module \中断按键参考电路  (
  input  \同步清零信号 ,
  output \与中断屏蔽位与 
);

  wire \_1号中断_out , and_1_out, clock_1_out, d_ff_1_q, or_1_out, or_2_out;

  Clock #(.highDuration(1), .lowDuration(1)) clock_1 (.out(clock_1_out));
  Button \_1号中断  (.out(\_1号中断_out ));
  or or_1 (or_1_out, \与中断屏蔽位与 , d_ff_1_q);
  LED #(.active("true")) \_1号中断等待指示灯  (.in(or_1_out));
  D_Flip_Flop #(.trigger("rising"), .Pre_Clr_Positions("LEGACY"), .NegatePresetClear("false"), .enable("true"), .NewFFLayout("false")) d_ff_1 (
    .clk(\_1号中断_out ), .D(1'b1), .Q(d_ff_1_q), .reset(\与中断屏蔽位与 ));  // open: Qn, preset, en
  or or_2 (or_2_out, d_ff_1_q, \与中断屏蔽位与 );
  and and_1 (and_1_out, or_2_out, ~\同步清零信号 );  // AND_Gate
  D_Flip_Flop #(.trigger("rising"), .Pre_Clr_Positions("LEGACY"), .NegatePresetClear("false"), .enable("true"), .NewFFLayout("false")) IR1 (
    .clk(clock_1_out), .D(and_1_out), .Q(\与中断屏蔽位与 ));  // open: Qn, preset, en, reset

  // Notes on the sheet:
  //   中断信号采样参考电路
  //   Reset 
endmodule
module \单周期_单级中断  (
  input  IR1,
  input  IR2,
  input  IR3,
  output RegWrite,
  output MemWrite,
  output [31:0] PC,
  output [31:0] IR,
  output [31:0] RDin,
  output [31:0] MDin,
  output [31:0] LedData
);

  wire ALUequal, ALUless, AluSrcBS, and_1_out, and_2_out, and_3_out, and_5_out, and_6_out, and_7_out,
       and_8_out, and_9_out, BEQS, BES, BLTUS, BNES, CLK, clock_1_out, clock_2_out, clock_3_out, clock_4_out,
       comparator_1_eq, comparator_2_eq, comparator_3_eq, comparator_4_eq, comparator_5_eq, comparator_6_eq,
       comparator_6_lt, comparator_7_eq, d_ff_1_q, d_ff_2_q, d_ff_3_q, d_ff_4_q, d_ff_5_q, d_ff_6_q,
       d_ff_7_q, ecall, Go, halt, IE, interrupt, IR1_reset, IR1_t, IR2_reset, IR2_t, IR3_reset, IR3_t, IRA,
       IRB, IRC, JALRS, JALS, LBUS, MemToRegS, nand_1_out, not_1_out, not_2_out, not_3_out, not_4_out,
       not_5_out, not_6_out, not_7_out, or_1_out, or_5_out, or_6_out, or_7_out, or_8_out, or_13_out,
       priority_encoder_1_gs, RST, Stype, URETS, W1, W2, W3;
  wire [1:0] InterruptId, register_2_q;
  wire [3:0] AluOPS;
  wire [4:0] multiplexer_3_out, multiplexer_4_out;
  wire [7:0] multiplexer_10_out;
  wire [11:0] multiplexer_5_out;
  wire [12:0] CNT_num;
  wire [31:0] ALURet, BEADDR, bit_extender_1_out, bit_extender_2_out, bit_extender_3_out, bit_extender_4_out,
       EPC, JALADDR, multiplexer_1_out, multiplexer_2_out, multiplexer_7_out, multiplexer_8_out,
       multiplexer_9_out, multiplexer_13_out, multiplexer_14_out, PCADDR, PCnextnew, PCP4, R1, ram_1_data,
       shifter_1_out, shifter_2_out;

  Button \u_继续运行  (.out(Go));
  Button _1 ();  // open: out
  Button _2 ();  // open: out
  Button _3 ();  // open: out
  LED #(.active("true")) led_1 (.in(W1));
  LED #(.active("true")) led_2 (.in(W2));
  LED #(.active("true")) led_3 (.in(W3));
  Hex_Digit_Display hex_digit_display_1 (.value(LedData[31:28]));  // open: dp
  Comparator #(.width(16), .mode("twosComplement")) comparator_1 (
    .a(16'h23b), .b({3'b000, CNT_num}), .eq(comparator_1_eq));  // open: gt, lt
  Comparator #(.width(16), .mode("twosComplement")) comparator_2 (
    .a({3'b000, CNT_num}), .b(16'h1), .eq(comparator_2_eq));  // open: gt, lt
  Comparator #(.width(16), .mode("twosComplement")) comparator_3 (
    .a({3'b000, CNT_num}), .b(16'h4), .eq(comparator_3_eq));  // open: gt, lt
  Comparator #(.width(16), .mode("twosComplement")) comparator_4 (
    .a({3'b000, CNT_num}), .b(16'h7), .eq(comparator_4_eq));  // open: gt, lt
  Hex_Digit_Display hex_digit_display_2 (.value(LedData[27:24]));  // open: dp
  Hex_Digit_Display hex_digit_display_3 (.value(LedData[23:20]));  // open: dp
  or or_1 (or_1_out, comparator_1_eq, comparator_2_eq);
  assign IRA = or_1_out ? ~CLK : 1'bz;  // Controlled_Inverter controlled_inverter_1
  assign IRB = comparator_3_eq ? ~CLK : 1'bz;  // Controlled_Inverter controlled_inverter_2
  assign IRC = comparator_4_eq ? ~CLK : 1'bz;  // Controlled_Inverter controlled_inverter_3
  Hex_Digit_Display hex_digit_display_4 (.value(LedData[15:12]));  // open: dp
  Hex_Digit_Display hex_digit_display_5 (.value(LedData[19:16]));  // open: dp
  Pull_Resistor #(.pull(0)) pull_resistor_1 (.node(IRA));
  Pull_Resistor #(.pull(0)) pull_resistor_2 (.node(IRB));
  Pull_Resistor #(.pull(0)) pull_resistor_3 (.node(IRC));
  Hex_Digit_Display hex_digit_display_6 (.value(LedData[11:8]));  // open: dp
  Hex_Digit_Display hex_digit_display_7 (.value(LedData[7:4]));  // open: dp
  // Probe on {3'b000, CNT_num}
  or or_2 (W1, d_ff_4_q, d_ff_1_q);
  or or_3 (W2, d_ff_5_q, d_ff_2_q);
  or or_4 (W3, d_ff_6_q, d_ff_3_q);
  Hex_Digit_Display hex_digit_display_8 (.value(LedData[3:0]));  // open: dp
  D_Flip_Flop #(.trigger("high"), .Pre_Clr_Positions("LEGACY"), .NegatePresetClear("false"), .enable("true"), .NewFFLayout("false")) d_ff_1 (
    .clk(IR1_t), .D(1'b1), .Q(d_ff_1_q), .reset(d_ff_4_q));  // open: Qn, preset, en
  D_Flip_Flop #(.trigger("high"), .Pre_Clr_Positions("LEGACY"), .NegatePresetClear("false"), .enable("true"), .NewFFLayout("false")) d_ff_2 (
    .clk(IR2_t), .D(1'b1), .Q(d_ff_2_q), .reset(d_ff_5_q));  // open: Qn, preset, en
  D_Flip_Flop #(.trigger("high"), .Pre_Clr_Positions("LEGACY"), .NegatePresetClear("false"), .enable("true"), .NewFFLayout("false")) d_ff_3 (
    .clk(IR3_t), .D(1'b1), .Q(d_ff_3_q), .reset(d_ff_6_q));  // open: Qn, preset, en
  Comparator #(.width(16), .mode("twosComplement")) comparator_5 (
    .a({3'b000, CNT_num}), .b({16{1'b0}}), .eq(comparator_5_eq));  // open: gt, lt
  not not_1 (not_1_out, halt);
  or or_5 (or_5_out, d_ff_1_q, d_ff_4_q);
  not not_2 (not_2_out, IR1_reset);
  or or_6 (or_6_out, d_ff_2_q, d_ff_5_q);
  not not_3 (not_3_out, IR2_reset);
  or or_7 (or_7_out, d_ff_3_q, d_ff_6_q);
  not not_4 (not_4_out, IR3_reset);
  not not_5 (not_5_out, interrupt);
  or or_8 (or_8_out, interrupt, comparator_5_eq, URETS);
  or or_9 (IR1_t, IR1, IRA);
  Register #(.width(32), .trigger("rising"), .Select("low")) u_PC (
    .D(PCnextnew), .en(not_1_out), .Q(PC), .clk(CLK), .clr(RST));
  Clock #(.highDuration(1), .lowDuration(1)) clock_1 (.out(clock_1_out));
  and and_1 (and_1_out, or_5_out, not_2_out);
  Clock #(.highDuration(1), .lowDuration(1)) clock_2 (.out(clock_2_out));
  and and_2 (and_2_out, or_6_out, not_3_out);
  Clock #(.highDuration(1), .lowDuration(1)) clock_3 (.out(clock_3_out));
  and and_3 (and_3_out, or_7_out, not_4_out);
  Register #(.width(1), .trigger("rising"), .Select("low")) register_1 (
    .D(not_5_out), .en(or_8_out), .Q(IE), .clk(CLK), .clr(RST));
  or or_10 (IR2_t, IR2, IRB);
  Adder #(.width(32)) adder_1 (.a(PC), .b(32'h4), .out(PCP4));  // open: cin, cout
  D_Flip_Flop #(.trigger("rising"), .Pre_Clr_Positions("LEGACY"), .NegatePresetClear("false"), .enable("true"), .NewFFLayout("false")) d_ff_4 (
    .clk(clock_1_out), .D(and_1_out), .Q(d_ff_4_q));  // open: Qn, preset, en, reset
  D_Flip_Flop #(.trigger("rising"), .Pre_Clr_Positions("LEGACY"), .NegatePresetClear("false"), .enable("true"), .NewFFLayout("false")) d_ff_5 (
    .clk(clock_2_out), .D(and_2_out), .Q(d_ff_5_q));  // open: Qn, preset, en, reset
  D_Flip_Flop #(.trigger("rising"), .Pre_Clr_Positions("LEGACY"), .NegatePresetClear("false"), .enable("true"), .NewFFLayout("false")) d_ff_6 (
    .clk(clock_3_out), .D(and_3_out), .Q(d_ff_6_q));  // open: Qn, preset, en, reset
  Multiplexer #(.select(2), .width(32), .disabled("Z"), .enable("false")) multiplexer_1 (
    .in1(32'h30ac), .in2(32'h3150), .in3(32'h31f4), .out(multiplexer_1_out), .sel(InterruptId));  // open: in0
  // RiscV_Probe riscv_probe_1: pin names not known; wires that end beside it: IR
  or or_11 (IR3_t, IR3, IRC);
  ROM #(.addrWidth(10), .dataWidth(32), .Select("high")) rom_1 (.addr(PC[11:2]), .data(IR));
  Multiplexer #(.select(1), .width(32), .disabled("Z"), .enable("false")) multiplexer_2 (
    .in0(PCADDR), .in1(multiplexer_1_out), .out(multiplexer_2_out), .sel(interrupt));
  Multiplexer #(.select(1), .width(5), .disabled("Z"), .enable("false")) multiplexer_3 (
    .in0(IR[19:15]), .in1(5'b10001), .out(multiplexer_3_out), .sel(ecall));
  Multiplexer #(.select(1), .width(5), .disabled("Z"), .enable("false")) multiplexer_4 (
    .in0(IR[24:20]), .in1(5'b01010), .out(multiplexer_4_out), .sel(ecall));
  Multiplexer #(.select(1), .width(12), .disabled("Z"), .enable("false")) multiplexer_5 (
    .in0(IR[31:20]), .in1({IR[31:25], IR[11:7]}), .out(multiplexer_5_out), .sel(Stype));
  Priority_Encoder #(.select(2), .disabled("Z")) priority_encoder_1 (
    .in1(d_ff_4_q), .in2(d_ff_5_q), .in3(d_ff_6_q), .out(InterruptId), .gs(priority_encoder_1_gs));  // open: in0, en_out, en_in
  \单周期硬布线控制器  \u_单周期硬布线控制器_1  (
    .Funct({IR[30], IR[25], IR[14:12]}), .OP(IR[6:2]), .ALU_OP(AluOPS), .MemToReg(MemToRegS),
    .MemWrite(MemWrite), .ALU_SRC(AluSrcBS), .ecall(ecall), .S_type(Stype), .Jalr(JALRS), .Beq(BEQS),
    .JAL(JALS), .Bne(BNES), .in_3(IR[21]), .uret(URETS), .LBU(LBUS), .BLTU(BLTUS), .RegWrite(RegWrite));  // open: RSread, RTread, CSC
  and and_4 (interrupt, priority_encoder_1_gs, IE);
  Multiplexer #(.select(1), .width(32), .disabled("Z"), .enable("false")) multiplexer_6 (
    .in0(multiplexer_2_out), .in1(EPC), .out(PCnextnew), .sel(URETS));
  assign bit_extender_1_out = {{20{multiplexer_5_out[11]}}, multiplexer_5_out};  // Bit_Extender bit_extender_1
  assign bit_extender_2_out = {{20{IR[31]}}, {IR[31], IR[7], IR[30:25], IR[11:8]}};  // Bit_Extender bit_extender_2
  assign bit_extender_3_out = {{12{IR[31]}}, {IR[31], IR[19:12], IR[20], IR[30:21]}};  // Bit_Extender bit_extender_3
  Regifile regifile_1 (
    .Din(RDin), .Clk(CLK), .R1(R1), .R2(MDin), .WE(RegWrite), .W_num(IR[11:7]), .R1_num(multiplexer_3_out),
    .R2_num(multiplexer_4_out));
  Shifter #(.width(32), .shift("ll")) shifter_1 (.in(bit_extender_2_out), .\dist (5'b00001), .out(shifter_1_out));
  Shifter #(.width(32), .shift("ll")) shifter_2 (.in(bit_extender_3_out), .\dist (5'b00001), .out(shifter_2_out));
  Multiplexer #(.select(1), .width(32), .disabled("Z"), .enable("false")) multiplexer_7 (
    .in0(MDin), .in1(bit_extender_1_out), .out(multiplexer_7_out), .sel(AluSrcBS));
  Adder #(.width(32)) adder_2 (.a(shifter_1_out), .b(PC), .out(BEADDR), .cin(1'b0));  // open: cout
  Adder #(.width(32)) adder_3 (.a(shifter_2_out), .b(PC), .out(JALADDR), .cin(1'b0));  // open: cout
  D_Flip_Flop #(.trigger("high"), .Pre_Clr_Positions("LEGACY"), .NegatePresetClear("false"), .enable("true"), .NewFFLayout("false")) d_ff_7 (.Q(d_ff_7_q));  // open: clk, D, Qn, preset, en, reset
  // Probe on 13'hc
  not not_6 (not_6_out, ALUequal);
  ALU alu_1 (
    .X(R1), .Y(multiplexer_7_out), .AluOP(AluOPS), .Equal(ALUequal), .Result(ALURet), .out_6(ALUless));  // open: Result_2, out_4
  Register #(.width(2), .trigger("rising"), .Select("low")) register_2 (
    .D(InterruptId), .en(interrupt), .Q(register_2_q), .clk(CLK));  // open: clr
  Demultiplexer #(.select(2), .width(1), .tristate("false"), .disabled("Z"), .enable("false")) demultiplexer_1 (
    .out1(IR1_reset), .out2(IR2_reset), .out3(IR3_reset), .in(URETS), .sel(register_2_q));  // open: out0
  Register #(.width(32), .trigger("rising"), .Select("low")) register_3 (
    .D(PCADDR), .en(interrupt), .Q(EPC), .clk(CLK), .clr(RST));
  Comparator #(.width(13), .mode("twosComplement")) comparator_6 (
    .a(CNT_num), .b(13'hc), .eq(comparator_6_eq), .lt(comparator_6_lt));  // open: gt
  Clock #(.highDuration(1), .lowDuration(1)) clock_4 (.out(clock_4_out));
  and and_5 (and_5_out, ALUequal, BEQS);
  and and_6 (and_6_out, not_6_out, BNES);
  or or_12 (BES, and_5_out, and_6_out, and_7_out);
  and and_7 (and_7_out, ALUless, BLTUS);
  Counter #(.width(13), .max('h1fff), .ongoal("stay"), .trigger("rising"), .behavior("old")) counter_1 (
    .count(comparator_6_lt), .Q(CNT_num), .clk(clock_4_out));  // open: load, D, carry, clr, preset
  nand nand_1 (nand_1_out, d_ff_7_q, comparator_6_eq);
  Comparator #(.width(32), .mode("twosComplement")) comparator_7 (
    .a(R1), .b(32'h22), .eq(comparator_7_eq));  // open: gt, lt
  assign CLK = nand_1_out ? clock_4_out : 1'bz;  // Controlled_Buffer controlled_buffer_1
  Pull_Resistor #(.pull(1)) pull_resistor_4 (.node(CLK));
  Multiplexer #(.select(1), .width(32), .disabled("Z"), .enable("false")) multiplexer_8 (
    .in0(PCP4), .in1(BEADDR), .out(multiplexer_8_out), .sel(BES));
  not not_7 (not_7_out, comparator_7_eq);
  and and_8 (and_8_out, comparator_7_eq, ecall);
  RAM #(.addrWidth(10), .dataWidth(32), .bus("separate"), .Select("high")) ram_1 (
    .addr(ALURet[11:2]), .din(MDin), .data(ram_1_data), .str(MemWrite), .clk(CLK));  // open: sel, ld, clr
  Multiplexer #(.select(1), .width(32), .disabled("Z"), .enable("false")) multiplexer_9 (
    .in0(multiplexer_8_out), .in1(JALADDR), .out(multiplexer_9_out), .sel(JALS));
  and and_9 (and_9_out, not_7_out, ecall);
  Register #(.width(32), .trigger("rising"), .Select("low")) register_4 (
    .D(MDin), .en(and_8_out), .Q(LedData), .clk(CLK));  // open: clr
  Multiplexer #(.select(2), .width(8), .disabled("Z"), .enable("false")) multiplexer_10 (
    .in0(ram_1_data[7:0]), .in1(ram_1_data[15:8]), .in2(ram_1_data[23:16]), .in3(ram_1_data[31:24]),
    .out(multiplexer_10_out), .sel(ALURet[1:0]));
  Multiplexer #(.select(1), .width(32), .disabled("Z"), .enable("false")) multiplexer_11 (
    .in0(multiplexer_9_out), .in1(ALURet), .out(PCADDR), .sel(JALRS));
  Multiplexer #(.select(1), .width(1), .disabled("Z"), .enable("false")) multiplexer_12 (
    .in0(and_9_out), .in1(1'b0), .out(halt), .sel(Go));
  assign bit_extender_4_out = {{24{1'b0}}, multiplexer_10_out};  // Bit_Extender bit_extender_4
  Multiplexer #(.select(1), .width(32), .disabled("Z"), .enable("false")) multiplexer_13 (
    .in0(ram_1_data), .in1(bit_extender_4_out), .out(multiplexer_13_out), .sel(LBUS));
  Multiplexer #(.select(1), .width(32), .disabled("Z"), .enable("false")) multiplexer_14 (
    .in0(ALURet), .in1(multiplexer_13_out), .out(multiplexer_14_out), .sel(MemToRegS));
  or or_13 (or_13_out, JALS, JALRS);
  Multiplexer #(.select(1), .width(32), .disabled("Z"), .enable("false")) multiplexer_15 (
    .in0(multiplexer_14_out), .in1(PCP4), .out(RDin), .sel(or_13_out));

  // Other names for the same wires on the sheet: flag = ALURet[1]; R2[31:0] = MDin; 总周期数[12:0] = CNT_num

  // Notes on the sheet:
  //   中断源
  //   中断等待指示
  //   总复位信号应将除ROM以外所有存储组件全部清零
  //   单级中断测试信号模拟器
  //   数码管输出
  //   数码管输出应该用寄存器锁存，否则显示数据只能一闪而过
  //   指令探针
  //   指令存储器
  //   contents of rom_1 (hex, n*v repeats v):
  //   7d000113 100413 1f41993 41f9d993 433 c00913 800b13 140413 f47413 800293 100313 499993 89e9b3 1300533
  //   2200893 73 406282b3 fe0294e3 140413 f00f93 1f47433 1c41413 800293 100313 49d993 89e9b3 1300533
  //   2200893 73 406282b3 fe0294e3 1c45413 406b0b33 b0463 f95ff06f 2b3 fff2c293 1029293 fff2e293 500533
  //   2200893 73 f5dff06f 1112023 410113 a12023 410113 812023 410113 1312023 410113 1412023 410113 1512023
  //   410113 1612023 410113 100b13 300a13 100a93 1600433 441413 14469b3 1300533 2200893 73 fe0416e3
  //   415a0a33 fe0a10e3 ffc10113 12b03 ffc10113 12a83 ffc10113 12a03 ffc10113 12983 ffc10113 12403
  //   ffc10113 12503 ffc10113 12883 200073 1112023 410113 a12023 410113 812023 410113 1312023 410113
  //   1412023 410113 1512023 410113 1612023 410113 200b13 300a13 100a93 1600433 441413 14469b3 1300533
  //   2200893 73 fe0416e3 415a0a33 fe0a10e3 ffc10113 12b03 ffc10113 12a83 ffc10113 12a03 ffc10113 12983
  //   ffc10113 12403 ffc10113 12503 ffc10113 12883 200073 1112023 410113 a12023 410113 812023 410113
  //   1312023 410113 1412023 410113 1512023 410113 1612023 410113 300b13 300a13 100a93 1600433 441413
  //   14469b3 1300533 2200893 73 fe0416e3 415a0a33 fe0a10e3 ffc10113 12b03 ffc10113 12a83 ffc10113 12a03
  //   ffc10113 12983 ffc10113 12403 ffc10113 12503 ffc10113 12883 200073
  //   指令字
  //   JAL
  //   JALR
  //   URET
  //   Beq
  //   Bne
  //   MemToReg
  //   MemWrite
  //   AluOP
  //   AluSrcB
  //   RegWrite
  //   为方便自动评测，需要输出PC，IR，寄存器堆写如数据RDin
  //   RAM写使能MemWrite、RAM写入数据MDin等信号
  //   控制位
  //   暂停节拍，不能为0
  //   戳工具置1进入计数暂停模式，ctrl+k时钟自动运行到对应节拍暂停
  //   ctrl+k关闭时钟连续运行，将控制位置零，进入单步调试模式调试
  //   可计数暂停的时钟源
endmodule

module \单周期_多级中断  (
  input  IR1,
  input  IR2,
  input  IR3,
  output RegWrite,
  output MemWrite,
  output [31:0] PC,
  output [31:0] IR,
  output [31:0] RDin,
  output [31:0] MDin,
  output [31:0] LedData
);

  wire ALUequal, ALUless, AluSrcBS, and_1_out, and_2_out, and_3_out, and_5_out, and_6_out, and_7_out,
       and_8_out, and_9_out, BEQS, BES, BLTUS, BNES, CLK, clock_1_out, clock_2_out, clock_3_out, clock_4_out,
       comparator_1_eq, comparator_2_eq, comparator_3_eq, comparator_4_eq, comparator_5_eq, comparator_6_eq,
       comparator_7_eq, comparator_7_lt, comparator_8_eq, CSC, d_ff_1_q, d_ff_2_q, d_ff_3_q, d_ff_4_q,
       d_ff_5_q, d_ff_6_q, d_ff_7_q, demultiplexer_1_out1, demultiplexer_1_out2, demultiplexer_1_out3,
       demultiplexer_3_out1, demultiplexer_3_out2, demultiplexer_3_out3, ecall, Go, halt, IE, interrupt,
       IR1_begin, IR1_reset, IR1_t, IR2_begin, IR2_reset, IR2_t, IR3_begin, IR3_reset, IR3_t, IRA, IRB, IRC,
       JALRS, JALS, LBUS, MemToRegS, multiplexer_1_out, nand_1_out, not_1_out, not_2_out, not_3_out,
       not_4_out, not_5_out, not_6_out, not_7_out, not_8_out, not_9_out, or_1_out, or_2_out, or_6_out,
       or_7_out, or_8_out, or_12_out, or_14_out, priority_encoder_1_gs, RST, Stype, URETS, W1, W2, W3;
  wire [1:0] InterruptId, InterruptProcessing;
  wire [3:0] AluOPS;
  wire [4:0] multiplexer_2_out, multiplexer_3_out;
  wire [7:0] multiplexer_8_out;
  wire [11:0] multiplexer_4_out;
  wire [12:0] CNT_num;
  wire [15:0] \总周期数 ;
  wire [31:0] ALURet, BEADDR, bit_extender_1_out, bit_extender_2_out, bit_extender_3_out, bit_extender_4_out,
       EPC, JALADDR, multiplexer_5_out, multiplexer_6_out, multiplexer_7_out, multiplexer_12_out,
       multiplexer_13_out, multiplexer_14_out, multiplexer_15_out, PCADDR, PCnextnew, PCP4, R1, ram_1_data,
       register_5_q, register_6_q, register_7_q, shifter_1_out, shifter_2_out;

  Button \u_继续运行  (.out(Go));
  Button _1 ();  // open: out
  Button _2 ();  // open: out
  Button _3 ();  // open: out
  LED #(.active("true")) led_1 (.in(W1));
  LED #(.active("true")) led_2 (.in(W2));
  LED #(.active("true")) led_3 (.in(W3));
  Hex_Digit_Display hex_digit_display_1 (.value(LedData[31:28]));  // open: dp
  Comparator #(.width(16), .mode("twosComplement")) comparator_1 (
    .a(16'h258), .b(\总周期数 ), .eq(comparator_1_eq));  // open: gt, lt
  Comparator #(.width(16), .mode("twosComplement")) comparator_2 (
    .a(\总周期数 ), .b(16'h1), .eq(comparator_2_eq));  // open: gt, lt
  Comparator #(.width(16), .mode("twosComplement")) comparator_3 (
    .a(\总周期数 ), .b(16'h4), .eq(comparator_3_eq));  // open: gt, lt
  Comparator #(.width(16), .mode("twosComplement")) comparator_4 (
    .a(\总周期数 ), .b(16'h7), .eq(comparator_4_eq));  // open: gt, lt
  Comparator #(.width(16), .mode("twosComplement")) comparator_5 (
    .a(\总周期数 ), .b(16'h241), .eq(comparator_5_eq));  // open: gt, lt
  Hex_Digit_Display hex_digit_display_2 (.value(LedData[23:20]));  // open: dp
  Hex_Digit_Display hex_digit_display_3 (.value(LedData[27:24]));  // open: dp
  or or_1 (or_1_out, comparator_1_eq, comparator_2_eq);
  assign IRA = or_1_out ? ~CLK : 1'bz;  // Controlled_Inverter controlled_inverter_1
  assign IRB = comparator_3_eq ? ~CLK : 1'bz;  // Controlled_Inverter controlled_inverter_2
  or or_2 (or_2_out, comparator_4_eq, comparator_5_eq);
  assign IRC = or_2_out ? ~CLK : 1'bz;  // Controlled_Inverter controlled_inverter_3
  Hex_Digit_Display hex_digit_display_4 (.value(LedData[19:16]));  // open: dp
  Hex_Digit_Display hex_digit_display_5 (.value(LedData[15:12]));  // open: dp
  Pull_Resistor #(.pull(0)) pull_resistor_1 (.node(IRA));
  Pull_Resistor #(.pull(0)) pull_resistor_2 (.node(IRB));
  Pull_Resistor #(.pull(0)) pull_resistor_3 (.node(IRC));
  Hex_Digit_Display hex_digit_display_6 (.value(LedData[11:8]));  // open: dp
  Hex_Digit_Display hex_digit_display_7 (.value(LedData[7:4]));  // open: dp
  // Probe on \总周期数 
  or or_3 (W1, d_ff_4_q, d_ff_1_q);
  or or_4 (W2, d_ff_5_q, d_ff_2_q);
  or or_5 (W3, d_ff_6_q, d_ff_3_q);
  Hex_Digit_Display hex_digit_display_8 (.value(LedData[3:0]));  // open: dp
  D_Flip_Flop #(.trigger("rising"), .Pre_Clr_Positions("LEGACY"), .NegatePresetClear("false"), .enable("true"), .NewFFLayout("false")) d_ff_1 (
    .clk(IR1_t), .D(1'b1), .Q(d_ff_1_q), .reset(d_ff_4_q));  // open: Qn, preset, en
  D_Flip_Flop #(.trigger("rising"), .Pre_Clr_Positions("LEGACY"), .NegatePresetClear("false"), .enable("true"), .NewFFLayout("false")) d_ff_2 (
    .clk(IR2_t), .D(1'b1), .Q(d_ff_2_q), .reset(d_ff_5_q));  // open: Qn, preset, en
  D_Flip_Flop #(.trigger("rising"), .Pre_Clr_Positions("LEGACY"), .NegatePresetClear("false"), .enable("true"), .NewFFLayout("false")) d_ff_3 (
    .clk(IR3_t), .D(1'b1), .Q(d_ff_3_q), .reset(d_ff_6_q));  // open: Qn, preset, en
  not not_1 (not_1_out, halt);
  not not_2 (not_2_out, halt);
  Counter #(.width(16), .max('hffff), .ongoal("wrap"), .trigger("rising"), .behavior("new")) counter_1 (
    .D({16{1'b0}}), .count(not_2_out), .Q(\总周期数 ), .clk(CLK));  // open: load, carry, clr, preset, down
  or or_6 (or_6_out, d_ff_1_q, d_ff_4_q);
  not not_3 (not_3_out, IR1_reset);
  or or_7 (or_7_out, d_ff_2_q, d_ff_5_q);
  not not_4 (not_4_out, IR2_reset);
  or or_8 (or_8_out, d_ff_3_q, d_ff_6_q);
  not not_5 (not_5_out, IR3_reset);
  or or_9 (IR1_t, IR1, IRA);
  Register #(.width(32), .trigger("rising"), .Select("low")) u_PC (
    .D(PCnextnew), .en(not_1_out), .Q(PC), .clk(CLK), .clr(RST));
  Clock #(.highDuration(1), .lowDuration(1)) clock_1 (.out(clock_1_out));
  and and_1 (and_1_out, or_6_out, not_3_out);
  Clock #(.highDuration(1), .lowDuration(1)) clock_2 (.out(clock_2_out));
  and and_2 (and_2_out, or_7_out, not_4_out);
  Clock #(.highDuration(1), .lowDuration(1)) clock_3 (.out(clock_3_out));
  and and_3 (and_3_out, or_8_out, not_5_out);
  or or_10 (IR2_t, IR2, IRB);
  Adder #(.width(32)) adder_1 (.a(PC), .b(32'h4), .out(PCP4));  // open: cin, cout
  D_Flip_Flop #(.trigger("rising"), .Pre_Clr_Positions("LEGACY"), .NegatePresetClear("false"), .enable("true"), .NewFFLayout("false")) d_ff_4 (
    .clk(clock_1_out), .D(and_1_out), .Q(d_ff_4_q));  // open: Qn, preset, en, reset
  D_Flip_Flop #(.trigger("rising"), .Pre_Clr_Positions("LEGACY"), .NegatePresetClear("false"), .enable("true"), .NewFFLayout("false")) d_ff_5 (
    .clk(clock_2_out), .D(and_2_out), .Q(d_ff_5_q));  // open: Qn, preset, en, reset
  D_Flip_Flop #(.trigger("rising"), .Pre_Clr_Positions("LEGACY"), .NegatePresetClear("false"), .enable("true"), .NewFFLayout("false")) d_ff_6 (
    .clk(clock_3_out), .D(and_3_out), .Q(d_ff_6_q));  // open: Qn, preset, en, reset
  Demultiplexer #(.select(2), .width(1), .tristate("false"), .disabled("Z"), .enable("false")) demultiplexer_1 (
    .out1(demultiplexer_1_out1), .out2(demultiplexer_1_out2), .out3(demultiplexer_1_out3), .in(interrupt),
    .sel(InterruptId));  // open: out0
  // RiscV_Probe riscv_probe_1: pin names not known; wires that end beside it: IR
  or or_11 (IR3_t, IR3, IRC);
  ROM #(.addrWidth(10), .dataWidth(32), .Select("high")) rom_1 (.addr(PC[11:2]), .data(IR));
  Multiplexer #(.select(2), .width(1), .disabled("Z"), .enable("false")) multiplexer_1 (
    .in0(1'b1), .in1(IR1_begin), .in2(IR2_begin), .in3(IR3_begin), .out(multiplexer_1_out), .sel(InterruptId));
  Register #(.width(1), .trigger("rising"), .Select("low")) register_1 (
    .D(1'b1), .en(demultiplexer_1_out1), .Q(IR1_begin), .clk(CLK), .clr(IR1_reset));
  Multiplexer #(.select(1), .width(5), .disabled("Z"), .enable("false")) multiplexer_2 (
    .in0(IR[19:15]), .in1(5'b10001), .out(multiplexer_2_out), .sel(ecall));
  Multiplexer #(.select(1), .width(5), .disabled("Z"), .enable("false")) multiplexer_3 (
    .in0(IR[24:20]), .in1(5'b01010), .out(multiplexer_3_out), .sel(ecall));
  Multiplexer #(.select(1), .width(12), .disabled("Z"), .enable("false")) multiplexer_4 (
    .in0(IR[31:20]), .in1({IR[31:25], IR[11:7]}), .out(multiplexer_4_out), .sel(Stype));
  Priority_Encoder #(.select(2), .disabled("Z")) priority_encoder_1 (
    .in0(1'b1), .in1(d_ff_4_q), .in2(d_ff_5_q), .in3(d_ff_6_q), .out(InterruptId), .gs(priority_encoder_1_gs));  // open: en_out, en_in
  not not_6 (not_6_out, multiplexer_1_out);
  \单周期硬布线控制器  \u_单周期硬布线控制器_1  (
    .Funct({IR[30], IR[25], IR[14:12]}), .OP(IR[6:2]), .ALU_OP(AluOPS), .MemToReg(MemToRegS),
    .MemWrite(MemWrite), .ALU_SRC(AluSrcBS), .ecall(ecall), .S_type(Stype), .Jalr(JALRS), .Beq(BEQS),
    .JAL(JALS), .Bne(BNES), .in_3(IR[21]), .uret(URETS), .LBU(LBUS), .BLTU(BLTUS), .RegWrite(RegWrite),
    .CSC(CSC));  // open: RSread, RTread
  and and_4 (interrupt, priority_encoder_1_gs, not_6_out, IE);
  Register #(.width(1), .trigger("rising"), .Select("low")) register_2 (
    .D(1'b1), .en(demultiplexer_1_out2), .Q(IR2_begin), .clk(CLK), .clr(IR2_reset));
  assign bit_extender_1_out = {{20{multiplexer_4_out[11]}}, multiplexer_4_out};  // Bit_Extender bit_extender_1
  assign bit_extender_2_out = {{20{IR[31]}}, {IR[31], IR[7], IR[30:25], IR[11:8]}};  // Bit_Extender bit_extender_2
  assign bit_extender_3_out = {{12{IR[31]}}, {IR[31], IR[19:12], IR[20], IR[30:21]}};  // Bit_Extender bit_extender_3
  Regifile regifile_1 (
    .Din(RDin), .Clk(CLK), .R1(R1), .R2(MDin), .WE(RegWrite), .W_num(IR[11:7]), .R1_num(multiplexer_2_out),
    .R2_num(multiplexer_3_out));
  or or_12 (or_12_out, CSC, URETS, interrupt);
  Register #(.width(1), .trigger("rising"), .Select("low")) register_3 (
    .D(1'b1), .en(demultiplexer_1_out3), .Q(IR3_begin), .clk(CLK), .clr(IR3_reset));
  Shifter #(.width(32), .shift("ll")) shifter_1 (.in(bit_extender_2_out), .\dist (5'b00001), .out(shifter_1_out));
  Shifter #(.width(32), .shift("ll")) shifter_2 (.in(bit_extender_3_out), .\dist (5'b00001), .out(shifter_2_out));
  T_Flip_Flop #(.trigger("rising"), .Pre_Clr_Positions("ABOVE_BELOW"), .NegatePresetClear("false"), .enable("false"), .NewFFLayout("true")) t_ff_1 (
    .clk(CLK), .T(or_12_out), .Qn(IE));  // open: Q, preset, reset
  Multiplexer #(.select(1), .width(32), .disabled("Z"), .enable("false")) multiplexer_5 (
    .in0(MDin), .in1(bit_extender_1_out), .out(multiplexer_5_out), .sel(AluSrcBS));
  Adder #(.width(32)) adder_2 (.a(shifter_1_out), .b(PC), .out(BEADDR), .cin(1'b0));  // open: cout
  Adder #(.width(32)) adder_3 (.a(shifter_2_out), .b(PC), .out(JALADDR), .cin(1'b0));  // open: cout
  Comparator #(.width(2), .mode("twosComplement")) comparator_6 (
    .a(InterruptId), .b(InterruptProcessing), .eq(comparator_6_eq));  // open: gt, lt
  not not_7 (not_7_out, comparator_6_eq);
  D_Flip_Flop #(.trigger("high"), .Pre_Clr_Positions("LEGACY"), .NegatePresetClear("false"), .enable("true"), .NewFFLayout("false")) d_ff_7 (.Q(d_ff_7_q));  // open: clk, D, Qn, preset, en, reset
  // Probe on 13'hcd
  not not_8 (not_8_out, ALUequal);
  ALU alu_1 (
    .X(R1), .Y(multiplexer_5_out), .AluOP(AluOPS), .Equal(ALUequal), .Result(ALURet), .out_6(ALUless));  // open: Result_2, out_4
  Register #(.width(2), .trigger("rising"), .Select("low")) register_4 (
    .D(InterruptId), .en(not_7_out), .Q(InterruptProcessing), .clk(CLK));  // open: clr
  Demultiplexer #(.select(2), .width(1), .tristate("false"), .disabled("Z"), .enable("false")) demultiplexer_2 (
    .out1(IR1_reset), .out2(IR2_reset), .out3(IR3_reset), .in(URETS), .sel(InterruptProcessing));  // open: out0
  Comparator #(.width(13), .mode("twosComplement")) comparator_7 (
    .a(CNT_num), .b(13'hcd), .eq(comparator_7_eq), .lt(comparator_7_lt));  // open: gt
  Clock #(.highDuration(1), .lowDuration(1)) clock_4 (.out(clock_4_out));
  and and_5 (and_5_out, ALUequal, BEQS);
  or or_13 (BES, and_5_out, and_6_out, and_7_out);
  and and_6 (and_6_out, not_8_out, BNES);
  and and_7 (and_7_out, ALUless, BLTUS);
  Counter #(.width(13), .max('h1fff), .ongoal("stay"), .trigger("rising"), .behavior("old")) counter_2 (
    .count(comparator_7_lt), .Q(CNT_num), .clk(clock_4_out));  // open: load, D, carry, clr, preset
  Demultiplexer #(.select(2), .width(1), .tristate("false"), .disabled("Z"), .enable("false")) demultiplexer_3 (
    .out1(demultiplexer_3_out1), .out2(demultiplexer_3_out2), .out3(demultiplexer_3_out3), .in(interrupt),
    .sel(InterruptId));  // open: out0
  nand nand_1 (nand_1_out, d_ff_7_q, comparator_7_eq);
  Comparator #(.width(32), .mode("twosComplement")) comparator_8 (
    .a(R1), .b(32'h22), .eq(comparator_8_eq));  // open: gt, lt
  assign CLK = nand_1_out ? clock_4_out : 1'bz;  // Controlled_Buffer controlled_buffer_1
  Pull_Resistor #(.pull(1)) pull_resistor_4 (.node(CLK));
  Multiplexer #(.select(1), .width(32), .disabled("Z"), .enable("false")) multiplexer_6 (
    .in0(PCP4), .in1(BEADDR), .out(multiplexer_6_out), .sel(BES));
  not not_9 (not_9_out, comparator_8_eq);
  and and_8 (and_8_out, comparator_8_eq, ecall);
  Register #(.width(32), .trigger("rising"), .Select("low")) register_5 (
    .D(PCADDR), .en(demultiplexer_3_out1), .Q(register_5_q), .clk(CLK));  // open: clr
  Register #(.width(32), .trigger("rising"), .Select("low")) register_6 (
    .D(PCADDR), .en(demultiplexer_3_out2), .Q(register_6_q), .clk(CLK));  // open: clr
  Register #(.width(32), .trigger("rising"), .Select("low")) register_7 (
    .D(PCADDR), .en(demultiplexer_3_out3), .Q(register_7_q), .clk(CLK));  // open: clr
  RAM #(.addrWidth(10), .dataWidth(32), .bus("separate"), .Select("high")) ram_1 (
    .addr(ALURet[11:2]), .din(MDin), .data(ram_1_data), .str(MemWrite), .clk(CLK));  // open: sel, ld, clr
  Multiplexer #(.select(1), .width(32), .disabled("Z"), .enable("false")) multiplexer_7 (
    .in0(multiplexer_6_out), .in1(JALADDR), .out(multiplexer_7_out), .sel(JALS));
  and and_9 (and_9_out, not_9_out, ecall);
  Register #(.width(32), .trigger("rising"), .Select("low")) register_8 (
    .D(MDin), .en(and_8_out), .Q(LedData), .clk(CLK));  // open: clr
  Multiplexer #(.select(2), .width(8), .disabled("Z"), .enable("false")) multiplexer_8 (
    .in0(ram_1_data[7:0]), .in1(ram_1_data[15:8]), .in2(ram_1_data[23:16]), .in3(ram_1_data[31:24]),
    .out(multiplexer_8_out), .sel(ALURet[1:0]));
  Multiplexer #(.select(1), .width(32), .disabled("Z"), .enable("false")) multiplexer_9 (
    .in0(multiplexer_7_out), .in1(ALURet), .out(PCADDR), .sel(JALRS));
  Multiplexer #(.select(1), .width(1), .disabled("Z"), .enable("false")) multiplexer_10 (
    .in0(and_9_out), .in1(1'b0), .out(halt), .sel(Go));
  Multiplexer #(.select(2), .width(32), .disabled("Z"), .enable("false")) multiplexer_11 (
    .in1(register_5_q), .in2(register_6_q), .in3(register_7_q), .out(EPC), .sel(InterruptId));  // open: in0
  assign bit_extender_4_out = {{24{1'b0}}, multiplexer_8_out};  // Bit_Extender bit_extender_4
  Multiplexer #(.select(2), .width(32), .disabled("Z"), .enable("false")) multiplexer_12 (
    .in1(32'h30ac), .in2(32'h3158), .in3(32'h3204), .out(multiplexer_12_out), .sel(InterruptId));  // open: in0
  Multiplexer #(.select(1), .width(32), .disabled("Z"), .enable("false")) multiplexer_13 (
    .in0(ram_1_data), .in1(bit_extender_4_out), .out(multiplexer_13_out), .sel(LBUS));
  Multiplexer #(.select(1), .width(32), .disabled("Z"), .enable("false")) multiplexer_14 (
    .in0(ALURet), .in1(multiplexer_13_out), .out(multiplexer_14_out), .sel(MemToRegS));
  Multiplexer #(.select(1), .width(32), .disabled("Z"), .enable("false")) multiplexer_15 (
    .in0(PCADDR), .in1(multiplexer_12_out), .out(multiplexer_15_out), .sel(interrupt));
  or or_14 (or_14_out, JALS, JALRS);
  Multiplexer #(.select(1), .width(32), .disabled("Z"), .enable("false")) multiplexer_16 (
    .in0(multiplexer_14_out), .in1(PCP4), .out(RDin), .sel(or_14_out));
  Multiplexer #(.select(1), .width(32), .disabled("Z"), .enable("false")) multiplexer_17 (
    .in0(multiplexer_15_out), .in1(EPC), .out(PCnextnew), .sel(URETS));

  // Other names for the same wires on the sheet: flag = ALURet[1]; R2[31:0] = MDin

  // Notes on the sheet:
  //   中断源
  //   中断等待指示
  //   总复位信号应将除ROM以外所有存储组件全部清零
  //   多级中断测试信号模拟器
  //   数码管输出
  //   数码管输出应该用寄存器锁存，否则显示数据只能一闪而过
  //   指令探针
  //   指令存储器
  //   contents of rom_1 (hex, n*v repeats v):
  //   7d000113 100413 1f41993 41f9d993 433 c00913 800b13 140413 f47413 800293 100313 499993 89e9b3 1300533
  //   2200893 73 406282b3 fe0294e3 140413 f00f93 1f47433 1c41413 800293 100313 49d993 89e9b3 1300533
  //   2200893 73 406282b3 fe0294e3 1c45413 406b0b33 b0463 f95ff06f 2b3 fff2c293 1029293 fff2e293 500533
  //   2200893 73 f5dff06f 1112023 410113 a12023 410113 812023 410113 1312023 410113 1412023 410113 1512023
  //   410113 1612023 410113 40e073 100b13 300a13 100a93 1600433 441413 14469b3 1300533 2200893 73 fe0416e3
  //   415a0a33 fe0a10e3 40f073 ffc10113 12b03 ffc10113 12a83 ffc10113 12a03 ffc10113 12983 ffc10113 12403
  //   ffc10113 12503 ffc10113 12883 200073 1112023 410113 a12023 410113 812023 410113 1312023 410113
  //   1412023 410113 1512023 410113 1612023 410113 40e073 200b13 300a13 100a93 1600433 441413 14469b3
  //   1300533 2200893 73 fe0416e3 415a0a33 fe0a10e3 40f073 ffc10113 12b03 ffc10113 12a83 ffc10113 12a03
  //   ffc10113 12983 ffc10113 12403 ffc10113 12503 ffc10113 12883 200073 1112023 410113 a12023 410113
  //   812023 410113 1312023 410113 1412023 410113 1512023 410113 1612023 410113 40e073 300b13 300a13
  //   100a93 1600433 441413 14469b3 1300533 2200893 73 fe0416e3 415a0a33 fe0a10e3 40f073 ffc10113 12b03
  //   ffc10113 12a83 ffc10113 12a03 ffc10113 12983 ffc10113 12403 ffc10113 12503 ffc10113 12883 200073
  //   指令字
  //   JAL
  //   JALR
  //   URET
  //   Beq
  //   Bne
  //   MemToReg
  //   MemWrite
  //   AluOP
  //   AluSrcB
  //   RegWrite
  //   为方便自动评测，需要输出PC，IR，寄存器堆写如数据RDin
  //   RAM写使能MemWrite、RAM写入数据MDin等信号
  //   控制位
  //   暂停节拍，不能为0
  //   戳工具置1进入计数暂停模式，ctrl+k时钟自动运行到对应节拍暂停
  //   ctrl+k关闭时钟连续运行，将控制位置零，进入单步调试模式调试
  //   可计数暂停的时钟源
endmodule

module \封装正确性测试  (
);

  wire IR1, IR2, IR3, MemW, RegW;
  wire [31:0] EX_PC, ID_PC, IF_PC, IR, LED, MDin, MDinr, MEM_PC, PC, RDin, RDinr, WB_PC;

  \单周期RISC_V  \u_单周期risc_v_1  (
    .IR1(IR1), .IR2(IR2), .IR3(IR3), .RegWrite(RegW), .MemWrite(MemW), .PC(PC), .IR(IR), .RDin(RDin),
    .MDin(MDin), .LedData(LED));  // open: out_11
  \气泡流水线  \u_气泡流水线_1  (
    .RegWrite(RegW), .MemWrite(MemW), .IF_PC(IF_PC), .ID_PC(ID_PC), .EX_PC(EX_PC), .M_PC(MEM_PC),
    .WB_PC(WB_PC), .RDin(RDinr), .MDin(MDinr), .LedData(LED));
  \单周期_单级中断  \u_单周期_单级中断_1  (
    .IR1(IR1), .IR2(IR2), .IR3(IR3), .RegWrite(RegW), .MemWrite(MemW), .PC(PC), .IR(IR), .RDin(RDin),
    .MDin(MDin), .LedData(LED));
  \理想流水线  \u_理想流水线_1  (
    .RegWrite(RegW), .MemWrite(MemW), .IF_PC(IF_PC), .ID_PC(ID_PC), .EX_PC(EX_PC), .M_PC(MEM_PC),
    .WB_PC(WB_PC), .RDin(RDinr), .MDin(MDinr), .LedData(LED));
  \重定向流水线  \u_重定向流水线_1  (
    .RegWrite(RegW), .MemWrite(MemW), .IF_PC(IF_PC), .ID_PC(ID_PC), .EX_PC(EX_PC), .M_PC(MEM_PC),
    .WB_PC(WB_PC), .RDin(RDinr), .MDin(MDinr), .LedData(LED));
  \单周期_多级中断  \u_单周期_多级中断_1  (
    .IR1(IR1), .IR2(IR2), .IR3(IR3), .RegWrite(RegW), .MemWrite(MemW), .PC(PC), .IR(IR), .RDin(RDin),
    .MDin(MDin), .LedData(LED));

  // Notes on the sheet:
  //   单周期封装测试
  //   气泡流水封装测试
  //   单周期+单级中断封装测试
  //   请检查上面封装有无位宽不匹配，引脚标签是否和连接的标签相对应，否则无法在educoder平台上正确测试
  //   理想流水封装测试
  //   重定向流水封装测试
  //   单周期+多级中断封装测试
endmodule

module IF_ID (
  input  [31:0] PCin,
  input  [31:0] PCP4in,
  input  [31:0] IRin,
  input  EN,
  input  CLK,
  input  RESET,
  output [31:0] PCout,
  output [31:0] PCP4out,
  output [31:0] IRout
);

  wire [31:0] multiplexer_1_out, multiplexer_2_out, multiplexer_3_out;

  Multiplexer #(.select(1), .width(32), .disabled("Z"), .enable("false")) multiplexer_1 (
    .in0(PCin), .in1({32{1'b0}}), .out(multiplexer_1_out), .sel(RESET));
  Multiplexer #(.select(1), .width(32), .disabled("Z"), .enable("false")) multiplexer_2 (
    .in0(PCP4in), .in1({32{1'b0}}), .out(multiplexer_2_out), .sel(RESET));
  Multiplexer #(.select(1), .width(32), .disabled("Z"), .enable("false")) multiplexer_3 (
    .in0(IRin), .in1({32{1'b0}}), .out(multiplexer_3_out), .sel(RESET));
  Register #(.width(32), .trigger("rising"), .Select("low")) register_1 (
    .D(multiplexer_1_out), .en(EN), .Q(PCout), .clk(CLK));  // open: clr
  Register #(.width(32), .trigger("rising"), .Select("low")) register_2 (
    .D(multiplexer_2_out), .en(EN), .Q(PCP4out), .clk(CLK));  // open: clr
  Register #(.width(32), .trigger("rising"), .Select("low")) register_3 (
    .D(multiplexer_3_out), .en(EN), .Q(IRout), .clk(CLK));  // open: clr

  // Notes on the sheet:
  //   使能-时钟-异步重置
endmodule

module ID_EX (
  input  CLK,
  input  EN,
  input  RESET,
  input  RegWritein,
  input  MemToRegin,
  input  MemWritein,
  input  [3:0] ALUOPin,
  input  ALUSrcin,
  input  ecallin,
  input  Stypein,
  input  BEQin,
  input  BNEin,
  input  JALin,
  input  JALRin,
  input  LBUin,
  input  BLTUin,
  input  [31:0] R1in,
  input  [31:0] R2in,
  input  [4:0] W_in,
  input  [31:0] Immin,
  input  [31:0] BEADDRin,
  input  [31:0] PCin,
  input  [31:0] PCP4in,
  input  [31:0] JALADDrin,
  input  [31:0] IRin,
  input  [1:0] RSGOin,
  input  [1:0] RTGOin,
  output RegWriteout,
  output MemToRegout,
  output MemWriteout,
  output [3:0] ALUOPout,
  output ALUSrcout,
  output ecallout,
  output Stypeout,
  output BEQout,
  output BNEout,
  output JALout,
  output JALRout,
  output LBUout,
  output BLTUout,
  output [31:0] R1out,
  output [31:0] R2out,
  output [4:0] W_out,
  output [31:0] Immout,
  output [31:0] BEADDRout,
  output [31:0] PCout,
  output [31:0] PCP4out,
  output [31:0] JALADDRout,
  output [31:0] IRout,
  output [1:0] RSGOout,
  output [1:0] RTGOout
);

  wire multiplexer_1_out, multiplexer_2_out, multiplexer_3_out, multiplexer_5_out, multiplexer_6_out,
       multiplexer_7_out, multiplexer_8_out, multiplexer_9_out, multiplexer_10_out, multiplexer_11_out,
       multiplexer_12_out, multiplexer_13_out;
  wire [1:0] multiplexer_23_out, multiplexer_24_out;
  wire [3:0] multiplexer_4_out;
  wire [4:0] multiplexer_16_out;
  wire [31:0] multiplexer_14_out, multiplexer_15_out, multiplexer_17_out, multiplexer_18_out,
       multiplexer_19_out, multiplexer_20_out, multiplexer_21_out, multiplexer_22_out;

  Multiplexer #(.select(1), .width(1), .disabled("Z"), .enable("false")) multiplexer_1 (
    .in0(RegWritein), .in1(1'b0), .out(multiplexer_1_out), .sel(RESET));
  Multiplexer #(.select(1), .width(1), .disabled("Z"), .enable("false")) multiplexer_2 (
    .in0(MemToRegin), .in1(1'b0), .out(multiplexer_2_out), .sel(RESET));
  Multiplexer #(.select(1), .width(1), .disabled("Z"), .enable("false")) multiplexer_3 (
    .in0(MemWritein), .in1(1'b0), .out(multiplexer_3_out), .sel(RESET));
  Multiplexer #(.select(1), .width(4), .disabled("Z"), .enable("false")) multiplexer_4 (
    .in0(ALUOPin), .in1(4'b0000), .out(multiplexer_4_out), .sel(RESET));
  Multiplexer #(.select(1), .width(1), .disabled("Z"), .enable("false")) multiplexer_5 (
    .in0(ALUSrcin), .in1(1'b0), .out(multiplexer_5_out), .sel(RESET));
  Multiplexer #(.select(1), .width(1), .disabled("Z"), .enable("false")) multiplexer_6 (
    .in0(ecallin), .in1(1'b0), .out(multiplexer_6_out), .sel(RESET));
  Multiplexer #(.select(1), .width(1), .disabled("Z"), .enable("false")) multiplexer_7 (
    .in0(Stypein), .in1(1'b0), .out(multiplexer_7_out), .sel(RESET));
  Multiplexer #(.select(1), .width(1), .disabled("Z"), .enable("false")) multiplexer_8 (
    .in0(BEQin), .in1(1'b0), .out(multiplexer_8_out), .sel(RESET));
  Multiplexer #(.select(1), .width(1), .disabled("Z"), .enable("false")) multiplexer_9 (
    .in0(BNEin), .in1(1'b0), .out(multiplexer_9_out), .sel(RESET));
  Multiplexer #(.select(1), .width(1), .disabled("Z"), .enable("false")) multiplexer_10 (
    .in0(JALin), .in1(1'b0), .out(multiplexer_10_out), .sel(RESET));
  Multiplexer #(.select(1), .width(1), .disabled("Z"), .enable("false")) multiplexer_11 (
    .in0(JALRin), .in1(1'b0), .out(multiplexer_11_out), .sel(RESET));
  Multiplexer #(.select(1), .width(1), .disabled("Z"), .enable("false")) multiplexer_12 (
    .in0(LBUin), .in1(1'b0), .out(multiplexer_12_out), .sel(RESET));
  Multiplexer #(.select(1), .width(1), .disabled("Z"), .enable("false")) multiplexer_13 (
    .in0(BLTUin), .in1(1'b0), .out(multiplexer_13_out), .sel(RESET));
  Multiplexer #(.select(1), .width(32), .disabled("Z"), .enable("false")) multiplexer_14 (
    .in0(R1in), .in1({32{1'b0}}), .out(multiplexer_14_out), .sel(RESET));
  Multiplexer #(.select(1), .width(32), .disabled("Z"), .enable("false")) multiplexer_15 (
    .in0(R2in), .in1({32{1'b0}}), .out(multiplexer_15_out), .sel(RESET));
  Multiplexer #(.select(1), .width(5), .disabled("Z"), .enable("false")) multiplexer_16 (
    .in0(W_in), .in1({5{1'b0}}), .out(multiplexer_16_out), .sel(RESET));
  Multiplexer #(.select(1), .width(32), .disabled("Z"), .enable("false")) multiplexer_17 (
    .in0(Immin), .in1({32{1'b0}}), .out(multiplexer_17_out), .sel(RESET));
  Multiplexer #(.select(1), .width(32), .disabled("Z"), .enable("false")) multiplexer_18 (
    .in0(BEADDRin), .in1({32{1'b0}}), .out(multiplexer_18_out), .sel(RESET));
  Multiplexer #(.select(1), .width(32), .disabled("Z"), .enable("false")) multiplexer_19 (
    .in0(PCin), .in1({32{1'b0}}), .out(multiplexer_19_out), .sel(RESET));
  Multiplexer #(.select(1), .width(32), .disabled("Z"), .enable("false")) multiplexer_20 (
    .in0(PCP4in), .in1({32{1'b0}}), .out(multiplexer_20_out), .sel(RESET));
  Multiplexer #(.select(1), .width(32), .disabled("Z"), .enable("false")) multiplexer_21 (
    .in0(JALADDrin), .in1({32{1'b0}}), .out(multiplexer_21_out), .sel(RESET));
  Multiplexer #(.select(1), .width(32), .disabled("Z"), .enable("false")) multiplexer_22 (
    .in0(IRin), .in1({32{1'b0}}), .out(multiplexer_22_out), .sel(RESET));
  Multiplexer #(.select(1), .width(2), .disabled("Z"), .enable("false")) multiplexer_23 (
    .in0(RSGOin), .in1(2'b00), .out(multiplexer_23_out), .sel(RESET));
  Multiplexer #(.select(1), .width(2), .disabled("Z"), .enable("false")) multiplexer_24 (
    .in0(RTGOin), .in1(2'b00), .out(multiplexer_24_out), .sel(RESET));
  Register #(.width(1), .trigger("rising"), .Select("low")) register_1 (
    .D(multiplexer_1_out), .en(EN), .Q(RegWriteout), .clk(CLK));  // open: clr
  Register #(.width(1), .trigger("rising"), .Select("low")) register_2 (
    .D(multiplexer_2_out), .en(EN), .Q(MemToRegout), .clk(CLK));  // open: clr
  Register #(.width(1), .trigger("rising"), .Select("low")) register_3 (
    .D(multiplexer_3_out), .en(EN), .Q(MemWriteout), .clk(CLK));  // open: clr
  Register #(.width(4), .trigger("rising"), .Select("low")) register_4 (
    .D(multiplexer_4_out), .en(EN), .Q(ALUOPout), .clk(CLK));  // open: clr
  Register #(.width(1), .trigger("rising"), .Select("low")) register_5 (
    .D(multiplexer_5_out), .en(EN), .Q(ALUSrcout), .clk(CLK));  // open: clr
  Register #(.width(1), .trigger("rising"), .Select("low")) register_6 (
    .D(multiplexer_6_out), .en(EN), .Q(ecallout), .clk(CLK));  // open: clr
  Register #(.width(1), .trigger("rising"), .Select("low")) register_7 (
    .D(multiplexer_7_out), .en(EN), .Q(Stypeout), .clk(CLK));  // open: clr
  Register #(.width(1), .trigger("rising"), .Select("low")) register_8 (
    .D(multiplexer_8_out), .en(EN), .Q(BEQout), .clk(CLK));  // open: clr
  Register #(.width(1), .trigger("rising"), .Select("low")) register_9 (
    .D(multiplexer_9_out), .en(EN), .Q(BNEout), .clk(CLK));  // open: clr
  Register #(.width(1), .trigger("rising"), .Select("low")) register_10 (
    .D(multiplexer_10_out), .en(EN), .Q(JALout), .clk(CLK));  // open: clr
  Register #(.width(1), .trigger("rising"), .Select("low")) register_11 (
    .D(multiplexer_11_out), .en(EN), .Q(JALRout), .clk(CLK));  // open: clr
  Register #(.width(1), .trigger("rising"), .Select("low")) register_12 (
    .D(multiplexer_12_out), .en(EN), .Q(LBUout), .clk(CLK));  // open: clr
  Register #(.width(1), .trigger("rising"), .Select("low")) register_13 (
    .D(multiplexer_13_out), .en(EN), .Q(BLTUout), .clk(CLK));  // open: clr
  Register #(.width(32), .trigger("rising"), .Select("low")) register_14 (
    .D(multiplexer_14_out), .en(EN), .Q(R1out), .clk(CLK));  // open: clr
  Register #(.width(32), .trigger("rising"), .Select("low")) register_15 (
    .D(multiplexer_15_out), .en(EN), .Q(R2out), .clk(CLK));  // open: clr
  Register #(.width(5), .trigger("rising"), .Select("low")) register_16 (
    .D(multiplexer_16_out), .en(EN), .Q(W_out), .clk(CLK));  // open: clr
  Register #(.width(32), .trigger("rising"), .Select("low")) register_17 (
    .D(multiplexer_17_out), .en(EN), .Q(Immout), .clk(CLK));  // open: clr
  Register #(.width(32), .trigger("rising"), .Select("low")) register_18 (
    .D(multiplexer_18_out), .en(EN), .Q(BEADDRout), .clk(CLK));  // open: clr
  Register #(.width(32), .trigger("rising"), .Select("low")) register_19 (
    .D(multiplexer_19_out), .en(EN), .Q(PCout), .clk(CLK));  // open: clr
  Register #(.width(32), .trigger("rising"), .Select("low")) register_20 (
    .D(multiplexer_20_out), .en(EN), .Q(PCP4out), .clk(CLK));  // open: clr
  Register #(.width(32), .trigger("rising"), .Select("low")) register_21 (
    .D(multiplexer_21_out), .en(EN), .Q(JALADDRout), .clk(CLK));  // open: clr
  Register #(.width(32), .trigger("rising"), .Select("low")) register_22 (
    .D(multiplexer_22_out), .en(EN), .Q(IRout), .clk(CLK));  // open: clr
  Register #(.width(2), .trigger("rising"), .Select("low")) register_23 (
    .D(multiplexer_23_out), .en(EN), .Q(RSGOout), .clk(CLK));  // open: clr
  Register #(.width(2), .trigger("rising"), .Select("low")) register_24 (
    .D(multiplexer_24_out), .en(EN), .Q(RTGOout), .clk(CLK));  // open: clr

  // Notes on the sheet:
  //   重置-使能-时钟
endmodule

module EX_MEM (
  input  CLK,
  input  EN,
  input  RESET,
  input  RegWritein,
  input  MemToRegin,
  input  MemWritein,
  input  [3:0] ALUOPin,
  input  ALUSrcin,
  input  ecallin,
  input  Stypein,
  input  BEQin,
  input  BNEin,
  input  JALin,
  input  JALRin,
  input  LBUin,
  input  BLTUin,
  input  [31:0] R1in,
  input  [31:0] R2in,
  input  [4:0] W_in,
  input  [31:0] Immin,
  input  [31:0] BEADDRin,
  input  [31:0] PCin,
  input  [31:0] PCP4in,
  input  [31:0] JALADDrin,
  input  BEin,
  input  [31:0] ALUResultin,
  input  [31:0] IRin,
  output RegWriteout,
  output MemToRegout,
  output MemWriteout,
  output [3:0] ALUOPout,
  output ALUSrcout,
  output ecallout,
  output Stypeout,
  output BEQout,
  output BNEout,
  output JALout,
  output JALRout,
  output LBUout,
  output BLTUout,
  output [31:0] R1out,
  output [31:0] R2out,
  output [4:0] W_out,
  output [31:0] Immout,
  output [31:0] BEADDRout,
  output [31:0] PCout,
  output [31:0] PCP4out,
  output [31:0] JALADDRout,
  output BEout,
  output [31:0] ALUResultout,
  output [31:0] IRout
);

  wire multiplexer_1_out, multiplexer_2_out, multiplexer_3_out, multiplexer_5_out, multiplexer_6_out,
       multiplexer_7_out, multiplexer_8_out, multiplexer_9_out, multiplexer_10_out, multiplexer_11_out,
       multiplexer_12_out, multiplexer_13_out, multiplexer_22_out;
  wire [3:0] multiplexer_4_out;
  wire [4:0] multiplexer_16_out;
  wire [31:0] multiplexer_14_out, multiplexer_15_out, multiplexer_17_out, multiplexer_18_out,
       multiplexer_19_out, multiplexer_20_out, multiplexer_21_out, multiplexer_23_out, multiplexer_24_out;

  Multiplexer #(.select(1), .width(1), .disabled("Z"), .enable("false")) multiplexer_1 (
    .in0(RegWritein), .in1(1'b0), .out(multiplexer_1_out), .sel(RESET));
  Multiplexer #(.select(1), .width(1), .disabled("Z"), .enable("false")) multiplexer_2 (
    .in0(MemToRegin), .in1(1'b0), .out(multiplexer_2_out), .sel(RESET));
  Multiplexer #(.select(1), .width(1), .disabled("Z"), .enable("false")) multiplexer_3 (
    .in0(MemWritein), .in1(1'b0), .out(multiplexer_3_out), .sel(RESET));
  Multiplexer #(.select(1), .width(4), .disabled("Z"), .enable("false")) multiplexer_4 (
    .in0(ALUOPin), .in1(4'b0000), .out(multiplexer_4_out), .sel(RESET));
  Multiplexer #(.select(1), .width(1), .disabled("Z"), .enable("false")) multiplexer_5 (
    .in0(ALUSrcin), .in1(1'b0), .out(multiplexer_5_out), .sel(RESET));
  Multiplexer #(.select(1), .width(1), .disabled("Z"), .enable("false")) multiplexer_6 (
    .in0(ecallin), .in1(1'b0), .out(multiplexer_6_out), .sel(RESET));
  Multiplexer #(.select(1), .width(1), .disabled("Z"), .enable("false")) multiplexer_7 (
    .in0(Stypein), .in1(1'b0), .out(multiplexer_7_out), .sel(RESET));
  Multiplexer #(.select(1), .width(1), .disabled("Z"), .enable("false")) multiplexer_8 (
    .in0(BEQin), .in1(1'b0), .out(multiplexer_8_out), .sel(RESET));
  Multiplexer #(.select(1), .width(1), .disabled("Z"), .enable("false")) multiplexer_9 (
    .in0(BNEin), .in1(1'b0), .out(multiplexer_9_out), .sel(RESET));
  Multiplexer #(.select(1), .width(1), .disabled("Z"), .enable("false")) multiplexer_10 (
    .in0(JALin), .in1(1'b0), .out(multiplexer_10_out), .sel(RESET));
  Multiplexer #(.select(1), .width(1), .disabled("Z"), .enable("false")) multiplexer_11 (
    .in0(JALRin), .in1(1'b0), .out(multiplexer_11_out), .sel(RESET));
  Multiplexer #(.select(1), .width(1), .disabled("Z"), .enable("false")) multiplexer_12 (
    .in0(LBUin), .in1(1'b0), .out(multiplexer_12_out), .sel(RESET));
  Multiplexer #(.select(1), .width(1), .disabled("Z"), .enable("false")) multiplexer_13 (
    .in0(BLTUin), .in1(1'b0), .out(multiplexer_13_out), .sel(RESET));
  Multiplexer #(.select(1), .width(32), .disabled("Z"), .enable("false")) multiplexer_14 (
    .in0(R1in), .in1({32{1'b0}}), .out(multiplexer_14_out), .sel(RESET));
  Multiplexer #(.select(1), .width(32), .disabled("Z"), .enable("false")) multiplexer_15 (
    .in0(R2in), .in1({32{1'b0}}), .out(multiplexer_15_out), .sel(RESET));
  Multiplexer #(.select(1), .width(5), .disabled("Z"), .enable("false")) multiplexer_16 (
    .in0(W_in), .in1({5{1'b0}}), .out(multiplexer_16_out), .sel(RESET));
  Multiplexer #(.select(1), .width(32), .disabled("Z"), .enable("false")) multiplexer_17 (
    .in0(Immin), .in1({32{1'b0}}), .out(multiplexer_17_out), .sel(RESET));
  Multiplexer #(.select(1), .width(32), .disabled("Z"), .enable("false")) multiplexer_18 (
    .in0(BEADDRin), .in1({32{1'b0}}), .out(multiplexer_18_out), .sel(RESET));
  Multiplexer #(.select(1), .width(32), .disabled("Z"), .enable("false")) multiplexer_19 (
    .in0(PCin), .in1({32{1'b0}}), .out(multiplexer_19_out), .sel(RESET));
  Multiplexer #(.select(1), .width(32), .disabled("Z"), .enable("false")) multiplexer_20 (
    .in0(PCP4in), .in1({32{1'b0}}), .out(multiplexer_20_out), .sel(RESET));
  Multiplexer #(.select(1), .width(32), .disabled("Z"), .enable("false")) multiplexer_21 (
    .in0(JALADDrin), .in1({32{1'b0}}), .out(multiplexer_21_out), .sel(RESET));
  Multiplexer #(.select(1), .width(1), .disabled("Z"), .enable("false")) multiplexer_22 (
    .in0(BEin), .in1(1'b0), .out(multiplexer_22_out), .sel(RESET));
  Multiplexer #(.select(1), .width(32), .disabled("Z"), .enable("false")) multiplexer_23 (
    .in0(ALUResultin), .in1({32{1'b0}}), .out(multiplexer_23_out), .sel(RESET));
  Multiplexer #(.select(1), .width(32), .disabled("Z"), .enable("false")) multiplexer_24 (
    .in0(IRin), .in1({32{1'b0}}), .out(multiplexer_24_out), .sel(RESET));
  Register #(.width(1), .trigger("rising"), .Select("low")) register_1 (
    .D(multiplexer_1_out), .en(EN), .Q(RegWriteout), .clk(CLK));  // open: clr
  Register #(.width(1), .trigger("rising"), .Select("low")) register_2 (
    .D(multiplexer_2_out), .en(EN), .Q(MemToRegout), .clk(CLK));  // open: clr
  Register #(.width(1), .trigger("rising"), .Select("low")) register_3 (
    .D(multiplexer_3_out), .en(EN), .Q(MemWriteout), .clk(CLK));  // open: clr
  Register #(.width(4), .trigger("rising"), .Select("low")) register_4 (
    .D(multiplexer_4_out), .en(EN), .Q(ALUOPout), .clk(CLK));  // open: clr
  Register #(.width(1), .trigger("rising"), .Select("low")) register_5 (
    .D(multiplexer_5_out), .en(EN), .Q(ALUSrcout), .clk(CLK));  // open: clr
  Register #(.width(1), .trigger("rising"), .Select("low")) register_6 (
    .D(multiplexer_6_out), .en(EN), .Q(ecallout), .clk(CLK));  // open: clr
  Register #(.width(1), .trigger("rising"), .Select("low")) register_7 (
    .D(multiplexer_7_out), .en(EN), .Q(Stypeout), .clk(CLK));  // open: clr
  Register #(.width(1), .trigger("rising"), .Select("low")) register_8 (
    .D(multiplexer_8_out), .en(EN), .Q(BEQout), .clk(CLK));  // open: clr
  Register #(.width(1), .trigger("rising"), .Select("low")) register_9 (
    .D(multiplexer_9_out), .en(EN), .Q(BNEout), .clk(CLK));  // open: clr
  Register #(.width(1), .trigger("rising"), .Select("low")) register_10 (
    .D(multiplexer_10_out), .en(EN), .Q(JALout), .clk(CLK));  // open: clr
  Register #(.width(1), .trigger("rising"), .Select("low")) register_11 (
    .D(multiplexer_11_out), .en(EN), .Q(JALRout), .clk(CLK));  // open: clr
  Register #(.width(1), .trigger("rising"), .Select("low")) register_12 (
    .D(multiplexer_12_out), .en(EN), .Q(LBUout), .clk(CLK));  // open: clr
  Register #(.width(1), .trigger("rising"), .Select("low")) register_13 (
    .D(multiplexer_13_out), .en(EN), .Q(BLTUout), .clk(CLK));  // open: clr
  Register #(.width(32), .trigger("rising"), .Select("low")) register_14 (
    .D(multiplexer_14_out), .en(EN), .Q(R1out), .clk(CLK));  // open: clr
  Register #(.width(32), .trigger("rising"), .Select("low")) register_15 (
    .D(multiplexer_15_out), .en(EN), .Q(R2out), .clk(CLK));  // open: clr
  Register #(.width(5), .trigger("rising"), .Select("low")) register_16 (
    .D(multiplexer_16_out), .en(EN), .Q(W_out), .clk(CLK));  // open: clr
  Register #(.width(32), .trigger("rising"), .Select("low")) register_17 (
    .D(multiplexer_17_out), .en(EN), .Q(Immout), .clk(CLK));  // open: clr
  Register #(.width(32), .trigger("rising"), .Select("low")) register_18 (
    .D(multiplexer_18_out), .en(EN), .Q(BEADDRout), .clk(CLK));  // open: clr
  Register #(.width(32), .trigger("rising"), .Select("low")) register_19 (
    .D(multiplexer_19_out), .en(EN), .Q(PCout), .clk(CLK));  // open: clr
  Register #(.width(32), .trigger("rising"), .Select("low")) register_20 (
    .D(multiplexer_20_out), .en(EN), .Q(PCP4out), .clk(CLK));  // open: clr
  Register #(.width(32), .trigger("rising"), .Select("low")) register_21 (
    .D(multiplexer_21_out), .en(EN), .Q(JALADDRout), .clk(CLK));  // open: clr
  Register #(.width(1), .trigger("rising"), .Select("low")) register_22 (
    .D(multiplexer_22_out), .en(EN), .Q(BEout), .clk(CLK));  // open: clr
  Register #(.width(32), .trigger("rising"), .Select("low")) register_23 (
    .D(multiplexer_23_out), .en(EN), .Q(ALUResultout), .clk(CLK));  // open: clr
  Register #(.width(32), .trigger("rising"), .Select("low")) register_24 (
    .D(multiplexer_24_out), .en(EN), .Q(IRout), .clk(CLK));  // open: clr

  // Notes on the sheet:
  //   重置-使能-时钟
endmodule

module MEM_WB (
  input  CLK,
  input  EN,
  input  RESET,
  input  RegWritein,
  input  MemToRegin,
  input  MemWritein,
  input  [3:0] ALUOPin,
  input  ALUSrcin,
  input  ecallin,
  input  Stypein,
  input  BEQin,
  input  BNEin,
  input  JALin,
  input  JALRin,
  input  LBUin,
  input  BLTUin,
  input  [31:0] IRin,
  input  [4:0] W_in,
  input  [31:0] Memin,
  input  [31:0] BEADDRin,
  input  [31:0] PCin,
  input  [31:0] PCP4in,
  input  [31:0] JALADDrin,
  input  BEin,
  input  [31:0] ALUResultin,
  input  [31:0] R1in,
  input  [31:0] R2in,
  output RegWriteout,
  output MemToRegout,
  output MemWriteout,
  output [3:0] ALUOPout,
  output ALUSrcout,
  output ecallout,
  output Stypeout,
  output BEQout,
  output BNEout,
  output JALout,
  output JALRout,
  output LBUout,
  output BLTUout,
  output [31:0] IRout,
  output [4:0] W_out,
  output [31:0] Memout,
  output [31:0] BEADDRout,
  output [31:0] PCout,
  output [31:0] PCP4out,
  output [31:0] JALADDRout,
  output BEout,
  output [31:0] ALUResultout,
  output [31:0] R1out,
  output [31:0] R2out
);

  wire multiplexer_1_out, multiplexer_2_out, multiplexer_3_out, multiplexer_5_out, multiplexer_6_out,
       multiplexer_7_out, multiplexer_8_out, multiplexer_9_out, multiplexer_10_out, multiplexer_11_out,
       multiplexer_12_out, multiplexer_13_out, multiplexer_21_out;
  wire [3:0] multiplexer_4_out;
  wire [4:0] multiplexer_15_out;
  wire [31:0] multiplexer_14_out, multiplexer_16_out, multiplexer_17_out, multiplexer_18_out,
       multiplexer_19_out, multiplexer_20_out, multiplexer_22_out, multiplexer_23_out, multiplexer_24_out;

  Multiplexer #(.select(1), .width(1), .disabled("Z"), .enable("false")) multiplexer_1 (
    .in0(RegWritein), .in1(1'b0), .out(multiplexer_1_out), .sel(RESET));
  Multiplexer #(.select(1), .width(1), .disabled("Z"), .enable("false")) multiplexer_2 (
    .in0(MemToRegin), .in1(1'b0), .out(multiplexer_2_out), .sel(RESET));
  Multiplexer #(.select(1), .width(1), .disabled("Z"), .enable("false")) multiplexer_3 (
    .in0(MemWritein), .in1(1'b0), .out(multiplexer_3_out), .sel(RESET));
  Multiplexer #(.select(1), .width(4), .disabled("Z"), .enable("false")) multiplexer_4 (
    .in0(ALUOPin), .in1(4'b0000), .out(multiplexer_4_out), .sel(RESET));
  Multiplexer #(.select(1), .width(1), .disabled("Z"), .enable("false")) multiplexer_5 (
    .in0(ALUSrcin), .in1(1'b0), .out(multiplexer_5_out), .sel(RESET));
  Multiplexer #(.select(1), .width(1), .disabled("Z"), .enable("false")) multiplexer_6 (
    .in0(ecallin), .in1(1'b0), .out(multiplexer_6_out), .sel(RESET));
  Multiplexer #(.select(1), .width(1), .disabled("Z"), .enable("false")) multiplexer_7 (
    .in0(Stypein), .in1(1'b0), .out(multiplexer_7_out), .sel(RESET));
  Multiplexer #(.select(1), .width(1), .disabled("Z"), .enable("false")) multiplexer_8 (
    .in0(BEQin), .in1(1'b0), .out(multiplexer_8_out), .sel(RESET));
  Multiplexer #(.select(1), .width(1), .disabled("Z"), .enable("false")) multiplexer_9 (
    .in0(BNEin), .in1(1'b0), .out(multiplexer_9_out), .sel(RESET));
  Multiplexer #(.select(1), .width(1), .disabled("Z"), .enable("false")) multiplexer_10 (
    .in0(JALin), .in1(1'b0), .out(multiplexer_10_out), .sel(RESET));
  Multiplexer #(.select(1), .width(1), .disabled("Z"), .enable("false")) multiplexer_11 (
    .in0(JALRin), .in1(1'b0), .out(multiplexer_11_out), .sel(RESET));
  Multiplexer #(.select(1), .width(1), .disabled("Z"), .enable("false")) multiplexer_12 (
    .in0(LBUin), .in1(1'b0), .out(multiplexer_12_out), .sel(RESET));
  Multiplexer #(.select(1), .width(1), .disabled("Z"), .enable("false")) multiplexer_13 (
    .in0(BLTUin), .in1(1'b0), .out(multiplexer_13_out), .sel(RESET));
  Multiplexer #(.select(1), .width(32), .disabled("Z"), .enable("false")) multiplexer_14 (
    .in0(IRin), .in1({32{1'b0}}), .out(multiplexer_14_out), .sel(RESET));
  Multiplexer #(.select(1), .width(5), .disabled("Z"), .enable("false")) multiplexer_15 (
    .in0(W_in), .in1({5{1'b0}}), .out(multiplexer_15_out), .sel(RESET));
  Multiplexer #(.select(1), .width(32), .disabled("Z"), .enable("false")) multiplexer_16 (
    .in0(Memin), .in1({32{1'b0}}), .out(multiplexer_16_out), .sel(RESET));
  Multiplexer #(.select(1), .width(32), .disabled("Z"), .enable("false")) multiplexer_17 (
    .in0(BEADDRin), .in1({32{1'b0}}), .out(multiplexer_17_out), .sel(RESET));
  Multiplexer #(.select(1), .width(32), .disabled("Z"), .enable("false")) multiplexer_18 (
    .in0(PCin), .in1({32{1'b0}}), .out(multiplexer_18_out), .sel(RESET));
  Multiplexer #(.select(1), .width(32), .disabled("Z"), .enable("false")) multiplexer_19 (
    .in0(PCP4in), .in1({32{1'b0}}), .out(multiplexer_19_out), .sel(RESET));
  Multiplexer #(.select(1), .width(32), .disabled("Z"), .enable("false")) multiplexer_20 (
    .in0(JALADDrin), .in1({32{1'b0}}), .out(multiplexer_20_out), .sel(RESET));
  Multiplexer #(.select(1), .width(1), .disabled("Z"), .enable("false")) multiplexer_21 (
    .in0(BEin), .in1(1'b0), .out(multiplexer_21_out), .sel(RESET));
  Multiplexer #(.select(1), .width(32), .disabled("Z"), .enable("false")) multiplexer_22 (
    .in0(ALUResultin), .in1({32{1'b0}}), .out(multiplexer_22_out), .sel(RESET));
  Multiplexer #(.select(1), .width(32), .disabled("Z"), .enable("false")) multiplexer_23 (
    .in0(R1in), .in1({32{1'b0}}), .out(multiplexer_23_out), .sel(RESET));
  Multiplexer #(.select(1), .width(32), .disabled("Z"), .enable("false")) multiplexer_24 (
    .in0(R2in), .in1({32{1'b0}}), .out(multiplexer_24_out), .sel(RESET));
  Register #(.width(1), .trigger("rising"), .Select("low")) register_1 (
    .D(multiplexer_1_out), .en(EN), .Q(RegWriteout), .clk(CLK));  // open: clr
  Register #(.width(1), .trigger("rising"), .Select("low")) register_2 (
    .D(multiplexer_2_out), .en(EN), .Q(MemToRegout), .clk(CLK));  // open: clr
  Register #(.width(1), .trigger("rising"), .Select("low")) register_3 (
    .D(multiplexer_3_out), .en(EN), .Q(MemWriteout), .clk(CLK));  // open: clr
  Register #(.width(4), .trigger("rising"), .Select("low")) register_4 (
    .D(multiplexer_4_out), .en(EN), .Q(ALUOPout), .clk(CLK));  // open: clr
  Register #(.width(1), .trigger("rising"), .Select("low")) register_5 (
    .D(multiplexer_5_out), .en(EN), .Q(ALUSrcout), .clk(CLK));  // open: clr
  Register #(.width(1), .trigger("rising"), .Select("low")) register_6 (
    .D(multiplexer_6_out), .en(EN), .Q(ecallout), .clk(CLK));  // open: clr
  Register #(.width(1), .trigger("rising"), .Select("low")) register_7 (
    .D(multiplexer_7_out), .en(EN), .Q(Stypeout), .clk(CLK));  // open: clr
  Register #(.width(1), .trigger("rising"), .Select("low")) register_8 (
    .D(multiplexer_8_out), .en(EN), .Q(BEQout), .clk(CLK));  // open: clr
  Register #(.width(1), .trigger("rising"), .Select("low")) register_9 (
    .D(multiplexer_9_out), .en(EN), .Q(BNEout), .clk(CLK));  // open: clr
  Register #(.width(1), .trigger("rising"), .Select("low")) register_10 (
    .D(multiplexer_10_out), .en(EN), .Q(JALout), .clk(CLK));  // open: clr
  Register #(.width(1), .trigger("rising"), .Select("low")) register_11 (
    .D(multiplexer_11_out), .en(EN), .Q(JALRout), .clk(CLK));  // open: clr
  Register #(.width(1), .trigger("rising"), .Select("low")) register_12 (
    .D(multiplexer_12_out), .en(EN), .Q(LBUout), .clk(CLK));  // open: clr
  Register #(.width(1), .trigger("rising"), .Select("low")) register_13 (
    .D(multiplexer_13_out), .en(EN), .Q(BLTUout), .clk(CLK));  // open: clr
  Register #(.width(32), .trigger("rising"), .Select("low")) register_14 (
    .D(multiplexer_14_out), .en(EN), .Q(IRout), .clk(CLK));  // open: clr
  Register #(.width(5), .trigger("rising"), .Select("low")) register_15 (
    .D(multiplexer_15_out), .en(EN), .Q(W_out), .clk(CLK));  // open: clr
  Register #(.width(32), .trigger("rising"), .Select("low")) register_16 (
    .D(multiplexer_16_out), .en(EN), .Q(Memout), .clk(CLK));  // open: clr
  Register #(.width(32), .trigger("rising"), .Select("low")) register_17 (
    .D(multiplexer_17_out), .en(EN), .Q(BEADDRout), .clk(CLK));  // open: clr
  Register #(.width(32), .trigger("rising"), .Select("low")) register_18 (
    .D(multiplexer_18_out), .en(EN), .Q(PCout), .clk(CLK));  // open: clr
  Register #(.width(32), .trigger("rising"), .Select("low")) register_19 (
    .D(multiplexer_19_out), .en(EN), .Q(PCP4out), .clk(CLK));  // open: clr
  Register #(.width(32), .trigger("rising"), .Select("low")) register_20 (
    .D(multiplexer_20_out), .en(EN), .Q(JALADDRout), .clk(CLK));  // open: clr
  Register #(.width(1), .trigger("rising"), .Select("low")) register_21 (
    .D(multiplexer_21_out), .en(EN), .Q(BEout), .clk(CLK));  // open: clr
  Register #(.width(32), .trigger("rising"), .Select("low")) register_22 (
    .D(multiplexer_22_out), .en(EN), .Q(ALUResultout), .clk(CLK));  // open: clr
  Register #(.width(32), .trigger("rising"), .Select("low")) register_23 (
    .D(multiplexer_23_out), .en(EN), .Q(R1out), .clk(CLK));  // open: clr
  Register #(.width(32), .trigger("rising"), .Select("low")) register_24 (
    .D(multiplexer_24_out), .en(EN), .Q(R2out), .clk(CLK));  // open: clr

  // Notes on the sheet:
  //   重置-使能-时钟
endmodule

module \流水判决  (
  input  RSU,
  input  RTU,
  input  [4:0] RSid,
  input  [4:0] RTid,
  input  EX_regwrite,
  input  MEM_regwrite,
  input  [4:0] EX_WID,
  input  [4:0] MEM_WID,
  output bubble
);

  wire and_1_out, and_2_out, and_3_out, and_4_out, comparator_1_eq, comparator_2_eq, comparator_3_eq,
       comparator_4_eq, comparator_5_eq, comparator_6_eq, comparator_7_eq, comparator_8_eq, not_1_out,
       not_2_out, not_3_out, not_4_out;

  Comparator #(.width(5), .mode("twosComplement")) comparator_1 (
    .a({5{1'b0}}), .b(RSid), .eq(comparator_1_eq));  // open: gt, lt
  Comparator #(.width(5), .mode("twosComplement")) comparator_2 (
    .a(RSid), .b(EX_WID), .eq(comparator_2_eq));  // open: gt, lt
  Comparator #(.width(5), .mode("twosComplement")) comparator_3 (
    .a({5{1'b0}}), .b(RSid), .eq(comparator_3_eq));  // open: gt, lt
  Comparator #(.width(5), .mode("twosComplement")) comparator_4 (
    .a(RSid), .b(MEM_WID), .eq(comparator_4_eq));  // open: gt, lt
  Comparator #(.width(5), .mode("twosComplement")) comparator_5 (
    .a({5{1'b0}}), .b(RTid), .eq(comparator_5_eq));  // open: gt, lt
  Comparator #(.width(5), .mode("twosComplement")) comparator_6 (
    .a(RTid), .b(EX_WID), .eq(comparator_6_eq));  // open: gt, lt
  Comparator #(.width(5), .mode("twosComplement")) comparator_7 (
    .a({5{1'b0}}), .b(RTid), .eq(comparator_7_eq));  // open: gt, lt
  Comparator #(.width(5), .mode("twosComplement")) comparator_8 (
    .a(RTid), .b(MEM_WID), .eq(comparator_8_eq));  // open: gt, lt
  not not_1 (not_1_out, comparator_1_eq);
  not not_2 (not_2_out, comparator_3_eq);
  not not_3 (not_3_out, comparator_5_eq);
  not not_4 (not_4_out, comparator_7_eq);
  and and_1 (and_1_out, RSU, EX_regwrite, not_1_out, comparator_2_eq);
  and and_2 (and_2_out, RSU, MEM_regwrite, not_2_out, comparator_4_eq);
  and and_3 (and_3_out, RTU, EX_regwrite, not_3_out, comparator_6_eq);
  and and_4 (and_4_out, RTU, MEM_regwrite, not_4_out, comparator_8_eq);
  or or_1 (bubble, and_1_out, and_2_out, and_3_out, and_4_out);

  // Other names for the same wires on the sheet: EX_reg = EX_regwrite; EX_W_num[4:0] = EX_WID; MEM_reg = MEM_regwrite;
  //   MEM_W_num[4:0] = MEM_WID; RS[4:0] = RSid; RSread = RSU; RT[4:0] = RTid; RTread = RTU
endmodule

module \重定向判决  (
  input  RSU,
  input  RTU,
  input  [4:0] RSid,
  input  [4:0] RTid,
  input  EX_reg_write,
  input  MEM_reg_write,
  input  [4:0] EX_Wid,
  input  [4:0] MEM_Wid,
  input  EX_memtoreg,
  output [1:0] RSGO,
  output [1:0] RTGO,
  output load
);

  wire and_1_out, and_2_out, and_3_out, and_4_out, and_5_out, and_6_out, comparator_1_eq, comparator_2_eq,
       comparator_3_eq, comparator_4_eq, comparator_5_eq, comparator_6_eq, comparator_7_eq, comparator_8_eq,
       comparator_9_eq, comparator_10_eq, comparator_11_eq, comparator_12_eq, not_1_out, not_2_out,
       not_3_out, not_4_out, not_5_out, not_6_out;
  wire [1:0] multiplexer_1_out, multiplexer_2_out;

  Comparator #(.width(5), .mode("twosComplement")) comparator_1 (
    .a({5{1'b0}}), .b(RSid), .eq(comparator_1_eq));  // open: gt, lt
  Comparator #(.width(5), .mode("twosComplement")) comparator_2 (
    .a(RSid), .b(EX_Wid), .eq(comparator_2_eq));  // open: gt, lt
  Comparator #(.width(5), .mode("twosComplement")) comparator_3 (
    .a({5{1'b0}}), .b(RTid), .eq(comparator_3_eq));  // open: gt, lt
  Comparator #(.width(5), .mode("twosComplement")) comparator_4 (
    .a(RTid), .b(EX_Wid), .eq(comparator_4_eq));  // open: gt, lt
  not not_1 (not_1_out, comparator_1_eq);
  not not_2 (not_2_out, comparator_3_eq);
  and and_1 (and_1_out, RSU, EX_memtoreg, not_1_out, comparator_2_eq);
  and and_2 (and_2_out, RTU, EX_memtoreg, not_2_out, comparator_4_eq);
  or or_1 (load, and_1_out, and_2_out);
  not not_3 (not_3_out, comparator_5_eq);
  Comparator #(.width(5), .mode("twosComplement")) comparator_5 (
    .a({5{1'b0}}), .b(RSid), .eq(comparator_5_eq));  // open: gt, lt
  Comparator #(.width(5), .mode("twosComplement")) comparator_6 (
    .a(RSid), .b(EX_Wid), .eq(comparator_6_eq));  // open: gt, lt
  Comparator #(.width(5), .mode("twosComplement")) comparator_7 (
    .a({5{1'b0}}), .b(RSid), .eq(comparator_7_eq));  // open: gt, lt
  not not_4 (not_4_out, comparator_7_eq);
  Comparator #(.width(5), .mode("twosComplement")) comparator_8 (
    .a(RSid), .b(MEM_Wid), .eq(comparator_8_eq));  // open: gt, lt
  Comparator #(.width(5), .mode("twosComplement")) comparator_9 (
    .a({5{1'b0}}), .b(RTid), .eq(comparator_9_eq));  // open: gt, lt
  not not_5 (not_5_out, comparator_9_eq);
  Comparator #(.width(5), .mode("twosComplement")) comparator_10 (
    .a(RTid), .b(EX_Wid), .eq(comparator_10_eq));  // open: gt, lt
  not not_6 (not_6_out, comparator_11_eq);
  Comparator #(.width(5), .mode("twosComplement")) comparator_11 (
    .a({5{1'b0}}), .b(RTid), .eq(comparator_11_eq));  // open: gt, lt
  Comparator #(.width(5), .mode("twosComplement")) comparator_12 (
    .a(RTid), .b(MEM_Wid), .eq(comparator_12_eq));  // open: gt, lt
  and and_3 (and_3_out, RSU, EX_reg_write, not_3_out, comparator_6_eq);
  and and_4 (and_4_out, RSU, MEM_reg_write, not_4_out, comparator_8_eq);
  and and_5 (and_5_out, RTU, EX_reg_write, not_5_out, comparator_10_eq);
  and and_6 (and_6_out, RTU, MEM_reg_write, not_6_out, comparator_12_eq);
  Multiplexer #(.select(1), .width(2), .disabled("Z"), .enable("false")) multiplexer_1 (
    .in0(2'b00), .in1(2'b01), .out(multiplexer_1_out), .sel(and_4_out));
  Multiplexer #(.select(1), .width(2), .disabled("Z"), .enable("false")) multiplexer_2 (
    .in0(2'b00), .in1(2'b01), .out(multiplexer_2_out), .sel(and_6_out));
  Multiplexer #(.select(1), .width(2), .disabled("Z"), .enable("false")) multiplexer_3 (
    .in0(multiplexer_1_out), .in1(2'b10), .out(RSGO), .sel(and_3_out));
  Multiplexer #(.select(1), .width(2), .disabled("Z"), .enable("false")) multiplexer_4 (
    .in0(multiplexer_2_out), .in1(2'b10), .out(RTGO), .sel(and_5_out));

  // Other names for the same wires on the sheet: EX_mtr = EX_memtoreg; EX_reg = EX_reg_write; EX_W_num[4:0] = EX_Wid;
  //   MEM_reg = MEM_reg_write; MEM_W_num[4:0] = MEM_Wid; RS[4:0] = RSid; RSread = RSU; RT[4:0] = RTid; RTread = RTU
endmodule

module \双位预测状态转换图  (
  input  \val_高位 ,
  input  \val_低位 ,
  input  IsJump,
  output \输出_高位 ,
  output \输出_低位 
);

  wire and_1_out, and_2_out, and_3_out, and_4_out, not_1_out, not_2_out, not_3_out, not_4_out, not_5_out;

  not not_1 (not_1_out, \val_低位 );
  not not_2 (not_2_out, \val_高位 );
  not not_3 (not_3_out, \val_低位 );
  not not_4 (not_4_out, \val_低位 );
  not not_5 (not_5_out, IsJump);
  and and_1 (and_1_out, \val_低位 , IsJump);
  and and_2 (and_2_out, \val_高位 , not_1_out);
  and and_3 (and_3_out, not_2_out, not_3_out, IsJump);
  and and_4 (and_4_out, \val_高位 , not_4_out, not_5_out);
  or or_1 (\输出_高位 , and_1_out, and_2_out);
  or or_2 (\输出_低位 , and_3_out, and_4_out);
endmodule

module \传递最大值  (
  input  [2:0] X,
  input  [2:0] Y,
  input  [31:0] XVal,
  input  [31:0] YVal,
  output [2:0] ID,
  output [31:0] Val
);

  wire comparator_1_eq, comparator_1_gt, or_1_out;

  Comparator #(.width(32), .mode("unsigned")) comparator_1 (
    .a(XVal), .b(YVal), .gt(comparator_1_gt), .eq(comparator_1_eq));  // open: lt
  or or_1 (or_1_out, comparator_1_gt, comparator_1_eq);
  Multiplexer #(.select(1), .width(3), .disabled("Z"), .enable("false")) multiplexer_1 (
    .in0(Y), .in1(X), .out(ID), .sel(or_1_out));
  Multiplexer #(.select(1), .width(32), .disabled("Z"), .enable("false")) multiplexer_2 (
    .in0(YVal), .in1(XVal), .out(Val), .sel(or_1_out));
endmodule

module BTB (
  input  CLK,
  input  EX_IsBranchIR,
  input  EX_BranchTaken,
  input  [31:0] PC,
  input  [31:0] EX_PC,
  input  [31:0] EX_BranchAddr,
  output PredictIJump,
  output [31:0] JumpAddr
);

  wire and_1_out, and_2_out, and_3_out, and_4_out, and_5_out, and_6_out, and_7_out, and_8_out, and_25_out,
       and_26_out, and_27_out, and_28_out, and_29_out, and_30_out, and_31_out, and_32_out, branch_HitErr,
       comparator_1_eq, comparator_2_eq, comparator_3_eq, comparator_4_eq, comparator_5_eq, comparator_6_eq,
       comparator_7_eq, comparator_8_eq, comparator_9_gt, comparator_10_gt, comparator_11_gt,
       comparator_12_gt, comparator_13_gt, comparator_14_gt, comparator_15_gt, comparator_16_gt,
       comparator_17_eq, comparator_18_eq, comparator_19_eq, comparator_20_eq, comparator_21_eq,
       comparator_22_eq, comparator_23_eq, comparator_24_eq, d_ff_1_q, d_ff_2_q, d_ff_3_q, d_ff_4_q,
       d_ff_5_q, d_ff_6_q, d_ff_7_q, d_ff_8_q, full, not_1_out, not_2_out, not_3_out, or_1_out, or_2_out,
       or_3_out, or_4_out, or_5_out, or_6_out, or_7_out, or_8_out, read0, read1, read2, read3, read4, read5,
       read6, read7, ReadHit, valid0, valid1, valid2, valid3, valid4, valid5, valid6, valid7, write0,
       write01, write1, write02, write2, write3, write4, write5, write6, write7, write11, write12, write21,
       write22, write31, write32, write41, write42, write51, write52, write61, write62, write71, write72,
       WriteHit;
  wire [1:0] multiplexer_2_out, multiplexer_3_out, multiplexer_4_out, multiplexer_6_out, multiplexer_8_out,
       multiplexer_10_out, multiplexer_12_out, multiplexer_15_out, \next状态0 , \next状态1 , \next状态2 ,
       \next状态3 , \next状态4 , \next状态5 , \next状态6 , \next状态7 , \双位预测状态转换图_1_输出_低位 , \双位预测状态转换图_2_输出_低位 ,
       \双位预测状态转换图_3_输出_低位 , \双位预测状态转换图_4_输出_低位 , \双位预测状态转换图_5_输出_低位 , \双位预测状态转换图_6_输出_低位 ,
       \双位预测状态转换图_7_输出_低位 , \双位预测状态转换图_8_输出_低位 , \预测历史位0 , \预测历史位1 , \预测历史位2 , \预测历史位3 , \预测历史位4 , \预测历史位5 ,
       \预测历史位6 , \预测历史位7 ;
  wire [2:0] multiplexer_1_out, priority_encoder_1_out, \传递最大值_1_id , \传递最大值_2_id , \传递最大值_3_id ,
       \传递最大值_4_id , \传递最大值_5_id , \传递最大值_6_id , \传递最大值_7_id ;
  wire [31:0] LruCnt0, LruCnt1, LruCnt2, LruCnt3, LruCnt4, LruCnt5, LruCnt6, LruCnt7, LruCntMax, PC_Key0,
       PC_Key1, PC_Key2, PC_Key3, PC_Key4, PC_Key5, PC_Key6, PC_Key7, \传递最大值_1_val , \传递最大值_2_val ,
       \传递最大值_3_val , \传递最大值_4_val , \传递最大值_5_val , \传递最大值_6_val , \分支目标地址0 , \分支目标地址1 , \分支目标地址2 ,
       \分支目标地址3 , \分支目标地址4 , \分支目标地址5 , \分支目标地址6 , \分支目标地址7 ;

  Register #(.width(1), .trigger("rising"), .Select("low")) register_1 (
    .D(1'b1), .en(write0), .Q(valid0), .clk(CLK));  // open: clr
  Register #(.width(1), .trigger("rising"), .Select("low")) register_2 (
    .D(1'b1), .en(write1), .Q(valid1), .clk(CLK));  // open: clr
  Register #(.width(1), .trigger("rising"), .Select("low")) register_3 (
    .D(1'b1), .en(write2), .Q(valid2), .clk(CLK));  // open: clr
  Register #(.width(1), .trigger("rising"), .Select("low")) register_4 (
    .D(1'b1), .en(write3), .Q(valid3), .clk(CLK));  // open: clr
  Register #(.width(1), .trigger("rising"), .Select("low")) register_5 (
    .D(1'b1), .en(write4), .Q(valid4), .clk(CLK));  // open: clr
  Register #(.width(1), .trigger("rising"), .Select("low")) register_6 (
    .D(1'b1), .en(write5), .Q(valid5), .clk(CLK));  // open: clr
  Register #(.width(1), .trigger("rising"), .Select("low")) register_7 (
    .D(1'b1), .en(write6), .Q(valid6), .clk(CLK));  // open: clr
  Register #(.width(1), .trigger("rising"), .Select("low")) register_8 (
    .D(1'b1), .en(write7), .Q(valid7), .clk(CLK));  // open: clr
  // Probe on valid1
  and and_1 (and_1_out, branch_HitErr, write0);
  and and_2 (and_2_out, branch_HitErr, write1);
  and and_3 (and_3_out, branch_HitErr, write2);
  and and_4 (and_4_out, branch_HitErr, write3);
  and and_5 (and_5_out, branch_HitErr, write4);
  and and_6 (and_6_out, branch_HitErr, write5);
  and and_7 (and_7_out, branch_HitErr, write6);
  and and_8 (and_8_out, branch_HitErr, write7);
  Register #(.width(32), .trigger("rising"), .Select("low")) register_9 (
    .D(EX_PC), .en(and_1_out), .Q(PC_Key0), .clk(CLK));  // open: clr
  Register #(.width(32), .trigger("rising"), .Select("low")) register_10 (
    .D(EX_PC), .en(and_2_out), .Q(PC_Key1), .clk(CLK));  // open: clr
  Register #(.width(32), .trigger("rising"), .Select("low")) register_11 (
    .D(EX_PC), .en(and_3_out), .Q(PC_Key2), .clk(CLK));  // open: clr
  Register #(.width(32), .trigger("rising"), .Select("low")) register_12 (
    .D(EX_PC), .en(and_4_out), .Q(PC_Key3), .clk(CLK));  // open: clr
  Register #(.width(32), .trigger("rising"), .Select("low")) register_13 (
    .D(EX_PC), .en(and_5_out), .Q(PC_Key4), .clk(CLK));  // open: clr
  Register #(.width(32), .trigger("rising"), .Select("low")) register_14 (
    .D(EX_PC), .en(and_6_out), .Q(PC_Key5), .clk(CLK));  // open: clr
  Register #(.width(32), .trigger("rising"), .Select("low")) register_15 (
    .D(EX_PC), .en(and_7_out), .Q(PC_Key6), .clk(CLK));  // open: clr
  Register #(.width(32), .trigger("rising"), .Select("low")) register_16 (
    .D(EX_PC), .en(and_8_out), .Q(PC_Key7), .clk(CLK));  // open: clr
  Register #(.width(32), .trigger("rising"), .Select("low")) register_17 (
    .D(EX_BranchAddr), .en(write0), .Q(\分支目标地址0 ), .clk(CLK));  // open: clr
  Register #(.width(32), .trigger("rising"), .Select("low")) register_18 (
    .D(EX_BranchAddr), .en(write1), .Q(\分支目标地址1 ), .clk(CLK));  // open: clr
  Register #(.width(32), .trigger("rising"), .Select("low")) register_19 (
    .D(EX_BranchAddr), .en(write2), .Q(\分支目标地址2 ), .clk(CLK));  // open: clr
  Register #(.width(32), .trigger("rising"), .Select("low")) register_20 (
    .D(EX_BranchAddr), .en(write3), .Q(\分支目标地址3 ), .clk(CLK));  // open: clr
  Register #(.width(32), .trigger("rising"), .Select("low")) register_21 (
    .D(EX_BranchAddr), .en(write4), .Q(\分支目标地址4 ), .clk(CLK));  // open: clr
  Register #(.width(32), .trigger("rising"), .Select("low")) register_22 (
    .D(EX_BranchAddr), .en(write5), .Q(\分支目标地址5 ), .clk(CLK));  // open: clr
  Register #(.width(32), .trigger("rising"), .Select("low")) register_23 (
    .D(EX_BranchAddr), .en(write6), .Q(\分支目标地址6 ), .clk(CLK));  // open: clr
  Register #(.width(32), .trigger("rising"), .Select("low")) register_24 (
    .D(EX_BranchAddr), .en(write7), .Q(\分支目标地址7 ), .clk(CLK));  // open: clr
  Register #(.width(2), .trigger("rising"), .Select("low")) register_25 (
    .D(\next状态6 ), .en(write6), .Q(\预测历史位6 ), .clk(CLK));  // open: clr
  Register #(.width(2), .trigger("rising"), .Select("low")) register_26 (
    .D(\next状态0 ), .en(write0), .Q(\预测历史位0 ), .clk(CLK));  // open: clr
  Register #(.width(2), .trigger("rising"), .Select("low")) register_27 (
    .D(\next状态1 ), .en(write1), .Q(\预测历史位1 ), .clk(CLK));  // open: clr
  Register #(.width(2), .trigger("rising"), .Select("low")) register_28 (
    .D(\next状态2 ), .en(write2), .Q(\预测历史位2 ), .clk(CLK));  // open: clr
  Register #(.width(2), .trigger("rising"), .Select("low")) register_29 (
    .D(\next状态3 ), .en(write3), .Q(\预测历史位3 ), .clk(CLK));  // open: clr
  Register #(.width(2), .trigger("rising"), .Select("low")) register_30 (
    .D(\next状态4 ), .en(write4), .Q(\预测历史位4 ), .clk(CLK));  // open: clr
  Register #(.width(2), .trigger("rising"), .Select("low")) register_31 (
    .D(\next状态5 ), .en(write5), .Q(\预测历史位5 ), .clk(CLK));  // open: clr
  Register #(.width(2), .trigger("rising"), .Select("low")) register_32 (
    .D(\next状态7 ), .en(write7), .Q(\预测历史位7 ), .clk(CLK));  // open: clr
  Counter #(.width(32), .max('hffffffff), .ongoal("wrap"), .trigger("rising"), .behavior("new")) counter_1 (
    .D({32{1'b0}}), .Q(LruCnt0), .clk(CLK), .clr(d_ff_1_q));  // open: load, count, carry, preset, down
  Counter #(.width(32), .max('hffffffff), .ongoal("wrap"), .trigger("rising"), .behavior("new")) counter_2 (
    .D({32{1'b0}}), .Q(LruCnt1), .clk(CLK), .clr(d_ff_2_q));  // open: load, count, carry, preset, down
  Counter #(.width(32), .max('hffffffff), .ongoal("wrap"), .trigger("rising"), .behavior("new")) counter_3 (
    .D({32{1'b0}}), .Q(LruCnt2), .clk(CLK), .clr(d_ff_3_q));  // open: load, count, carry, preset, down
  Counter #(.width(32), .max('hffffffff), .ongoal("wrap"), .trigger("rising"), .behavior("new")) counter_4 (
    .D({32{1'b0}}), .Q(LruCnt3), .clk(CLK), .clr(d_ff_4_q));  // open: load, count, carry, preset, down
  Counter #(.width(32), .max('hffffffff), .ongoal("wrap"), .trigger("rising"), .behavior("new")) counter_5 (
    .D({32{1'b0}}), .Q(LruCnt4), .clk(CLK), .clr(d_ff_5_q));  // open: load, count, carry, preset, down
  Counter #(.width(32), .max('hffffffff), .ongoal("wrap"), .trigger("rising"), .behavior("new")) counter_6 (
    .D({32{1'b0}}), .Q(LruCnt5), .clk(CLK), .clr(d_ff_6_q));  // open: load, count, carry, preset, down
  Counter #(.width(32), .max('hffffffff), .ongoal("wrap"), .trigger("rising"), .behavior("new")) counter_7 (
    .D({32{1'b0}}), .Q(LruCnt6), .clk(CLK), .clr(d_ff_7_q));  // open: load, count, carry, preset, down
  Counter #(.width(32), .max('hffffffff), .ongoal("wrap"), .trigger("rising"), .behavior("new")) counter_8 (
    .D({32{1'b0}}), .Q(LruCnt7), .clk(CLK), .clr(d_ff_8_q));  // open: load, count, carry, preset, down
  or or_1 (or_1_out, read0, write0);
  or or_2 (or_2_out, read1, write1);
  or or_3 (or_3_out, read2, write2);
  or or_4 (or_4_out, read3, write3);
  or or_5 (or_5_out, read4, write4);
  or or_6 (or_6_out, read5, write5);
  or or_7 (or_7_out, read6, write6);
  or or_8 (or_8_out, read7, write7);
  D_Flip_Flop #(.trigger("rising"), .Pre_Clr_Positions("LEGACY"), .NegatePresetClear("false"), .enable("true"), .NewFFLayout("false")) d_ff_1 (
    .clk(CLK), .D(or_1_out), .Q(d_ff_1_q));  // open: Qn, preset, en, reset
  D_Flip_Flop #(.trigger("rising"), .Pre_Clr_Positions("LEGACY"), .NegatePresetClear("false"), .enable("true"), .NewFFLayout("false")) d_ff_2 (
    .clk(CLK), .D(or_2_out), .Q(d_ff_2_q));  // open: Qn, preset, en, reset
  D_Flip_Flop #(.trigger("rising"), .Pre_Clr_Positions("LEGACY"), .NegatePresetClear("false"), .enable("true"), .NewFFLayout("false")) d_ff_3 (
    .clk(CLK), .D(or_3_out), .Q(d_ff_3_q));  // open: Qn, preset, en, reset
  D_Flip_Flop #(.trigger("rising"), .Pre_Clr_Positions("LEGACY"), .NegatePresetClear("false"), .enable("true"), .NewFFLayout("false")) d_ff_4 (
    .clk(CLK), .D(or_4_out), .Q(d_ff_4_q));  // open: Qn, preset, en, reset
  D_Flip_Flop #(.trigger("rising"), .Pre_Clr_Positions("LEGACY"), .NegatePresetClear("false"), .enable("true"), .NewFFLayout("false")) d_ff_5 (
    .clk(CLK), .D(or_5_out), .Q(d_ff_5_q));  // open: Qn, preset, en, reset
  D_Flip_Flop #(.trigger("rising"), .Pre_Clr_Positions("LEGACY"), .NegatePresetClear("false"), .enable("true"), .NewFFLayout("false")) d_ff_6 (
    .clk(CLK), .D(or_6_out), .Q(d_ff_6_q));  // open: Qn, preset, en, reset
  D_Flip_Flop #(.trigger("rising"), .Pre_Clr_Positions("LEGACY"), .NegatePresetClear("false"), .enable("true"), .NewFFLayout("false")) d_ff_7 (
    .clk(CLK), .D(or_7_out), .Q(d_ff_7_q));  // open: Qn, preset, en, reset
  D_Flip_Flop #(.trigger("rising"), .Pre_Clr_Positions("LEGACY"), .NegatePresetClear("false"), .enable("true"), .NewFFLayout("false")) d_ff_8 (
    .clk(CLK), .D(or_8_out), .Q(d_ff_8_q));  // open: Qn, preset, en, reset
  Comparator #(.width(32), .mode("twosComplement")) comparator_1 (
    .a(PC), .b(PC_Key0), .eq(comparator_1_eq));  // open: gt, lt
  Comparator #(.width(32), .mode("unsigned")) comparator_2 (.a(PC), .b(PC_Key1), .eq(comparator_2_eq));  // open: gt, lt
  Comparator #(.width(32), .mode("unsigned")) comparator_3 (.a(PC), .b(PC_Key2), .eq(comparator_3_eq));  // open: gt, lt
  Comparator #(.width(32), .mode("unsigned")) comparator_4 (.a(PC), .b(PC_Key3), .eq(comparator_4_eq));  // open: gt, lt
  Comparator #(.width(32), .mode("unsigned")) comparator_5 (.a(PC), .b(PC_Key4), .eq(comparator_5_eq));  // open: gt, lt
  Comparator #(.width(32), .mode("unsigned")) comparator_6 (.a(PC), .b(PC_Key5), .eq(comparator_6_eq));  // open: gt, lt
  Comparator #(.width(32), .mode("unsigned")) comparator_7 (.a(PC), .b(PC_Key6), .eq(comparator_7_eq));  // open: gt, lt
  Comparator #(.width(32), .mode("unsigned")) comparator_8 (.a(PC), .b(PC_Key7), .eq(comparator_8_eq));  // open: gt, lt
  assign JumpAddr = not_1_out ? {32{1'b0}} : 32'bz;  // Controlled_Buffer controlled_buffer_1
  not not_1 (not_1_out, ReadHit);
  assign JumpAddr = read0 ? \分支目标地址0  : 32'bz;  // Controlled_Buffer controlled_buffer_2
  assign JumpAddr = read1 ? \分支目标地址1  : 32'bz;  // Controlled_Buffer controlled_buffer_3
  assign JumpAddr = read2 ? \分支目标地址2  : 32'bz;  // Controlled_Buffer controlled_buffer_4
  assign JumpAddr = read3 ? \分支目标地址3  : 32'bz;  // Controlled_Buffer controlled_buffer_5
  assign JumpAddr = read4 ? \分支目标地址4  : 32'bz;  // Controlled_Buffer controlled_buffer_6
  assign JumpAddr = read5 ? \分支目标地址5  : 32'bz;  // Controlled_Buffer controlled_buffer_7
  assign JumpAddr = read6 ? \分支目标地址6  : 32'bz;  // Controlled_Buffer controlled_buffer_8
  assign JumpAddr = read7 ? \分支目标地址7  : 32'bz;  // Controlled_Buffer controlled_buffer_9
  and and_9 (read0, valid0, comparator_1_eq);
  and and_10 (read1, valid1, comparator_2_eq);
  and and_11 (read2, valid2, comparator_3_eq);
  and and_12 (read3, valid3, comparator_4_eq);
  and and_13 (read4, valid4, comparator_5_eq);
  and and_14 (read5, valid5, comparator_6_eq);
  and and_15 (read6, valid6, comparator_7_eq);
  and and_16 (read7, valid7, comparator_8_eq);
  or or_9 (ReadHit, read7, read6, read5, read4, read3, read2, read1, read0);
  not not_2 (not_2_out, ReadHit);
  assign PredictIJump = not_2_out ? 1'b0 : 1'bz;  // Controlled_Buffer controlled_buffer_10
  assign PredictIJump = read0 ? comparator_9_gt : 1'bz;  // Controlled_Buffer controlled_buffer_11
  Comparator #(.width(2), .mode("unsigned")) comparator_9 (
    .a(\预测历史位0 ), .b(2'b01), .gt(comparator_9_gt));  // open: eq, lt
  assign PredictIJump = read1 ? comparator_10_gt : 1'bz;  // Controlled_Buffer controlled_buffer_12
  Comparator #(.width(2), .mode("unsigned")) comparator_10 (
    .a(\预测历史位1 ), .b(2'b01), .gt(comparator_10_gt));  // open: eq, lt
  assign PredictIJump = read2 ? comparator_11_gt : 1'bz;  // Controlled_Buffer controlled_buffer_13
  Comparator #(.width(2), .mode("unsigned")) comparator_11 (
    .a(\预测历史位2 ), .b(2'b01), .gt(comparator_11_gt));  // open: eq, lt
  assign PredictIJump = read3 ? comparator_12_gt : 1'bz;  // Controlled_Buffer controlled_buffer_14
  Comparator #(.width(2), .mode("unsigned")) comparator_12 (
    .a(\预测历史位3 ), .b(2'b01), .gt(comparator_12_gt));  // open: eq, lt
  assign PredictIJump = read4 ? comparator_13_gt : 1'bz;  // Controlled_Buffer controlled_buffer_15
  Comparator #(.width(2), .mode("unsigned")) comparator_13 (
    .a(\预测历史位4 ), .b(2'b01), .gt(comparator_13_gt));  // open: eq, lt
  assign PredictIJump = read5 ? comparator_14_gt : 1'bz;  // Controlled_Buffer controlled_buffer_16
  Comparator #(.width(2), .mode("unsigned")) comparator_14 (
    .a(\预测历史位5 ), .b(2'b01), .gt(comparator_14_gt));  // open: eq, lt
  assign PredictIJump = read6 ? comparator_15_gt : 1'bz;  // Controlled_Buffer controlled_buffer_17
  Comparator #(.width(2), .mode("unsigned")) comparator_15 (
    .a(\预测历史位6 ), .b(2'b01), .gt(comparator_15_gt));  // open: eq, lt
  assign PredictIJump = read7 ? comparator_16_gt : 1'bz;  // Controlled_Buffer controlled_buffer_18
  Comparator #(.width(2), .mode("unsigned")) comparator_16 (
    .a(\预测历史位7 ), .b(2'b01), .gt(comparator_16_gt));  // open: eq, lt
  Comparator #(.width(32), .mode("unsigned")) comparator_17 (
    .a(EX_PC), .b(PC_Key0), .eq(comparator_17_eq));  // open: gt, lt
  Comparator #(.width(32), .mode("unsigned")) comparator_18 (
    .a(EX_PC), .b(PC_Key1), .eq(comparator_18_eq));  // open: gt, lt
  Comparator #(.width(32), .mode("unsigned")) comparator_19 (
    .a(EX_PC), .b(PC_Key2), .eq(comparator_19_eq));  // open: gt, lt
  Comparator #(.width(32), .mode("unsigned")) comparator_20 (
    .a(EX_PC), .b(PC_Key3), .eq(comparator_20_eq));  // open: gt, lt
  Comparator #(.width(32), .mode("unsigned")) comparator_21 (
    .a(EX_PC), .b(PC_Key4), .eq(comparator_21_eq));  // open: gt, lt
  Comparator #(.width(32), .mode("unsigned")) comparator_22 (
    .a(EX_PC), .b(PC_Key5), .eq(comparator_22_eq));  // open: gt, lt
  Comparator #(.width(32), .mode("unsigned")) comparator_23 (
    .a(EX_PC), .b(PC_Key6), .eq(comparator_23_eq));  // open: gt, lt
  Comparator #(.width(32), .mode("unsigned")) comparator_24 (
    .a(EX_PC), .b(PC_Key7), .eq(comparator_24_eq));  // open: gt, lt
  and and_17 (write01, valid0, comparator_17_eq);
  and and_18 (write11, valid1, comparator_18_eq);
  and and_19 (write21, valid2, comparator_19_eq);
  and and_20 (write31, valid3, comparator_20_eq);
  and and_21 (write41, valid4, comparator_21_eq);
  and and_22 (write51, valid5, comparator_22_eq);
  and and_23 (write61, valid6, comparator_23_eq);
  and and_24 (write71, valid7, comparator_24_eq);
  or or_10 (WriteHit, write71, write61, write51, write41, write31, write21, write11, write01);
  Priority_Encoder #(.select(3), .disabled("Z")) priority_encoder_1 (
    .in0(1'b1), .in1(valid0), .in2(valid1), .in3(valid2), .in4(valid3), .in5(valid4), .in6(valid5),
    .in7(valid6), .out(priority_encoder_1_out));  // open: gs, en_out, en_in
  \传递最大值  \u_传递最大值_1  (.X(3'b000), .Y(3'b001), .XVal(LruCnt0), .YVal(LruCnt1), .ID(\传递最大值_1_id ), .Val(\传递最大值_1_val ));
  \传递最大值  \u_传递最大值_2  (.X(3'b010), .Y(3'b011), .XVal(LruCnt2), .YVal(LruCnt3), .ID(\传递最大值_2_id ), .Val(\传递最大值_2_val ));
  \传递最大值  \u_传递最大值_3  (.X(3'b100), .Y(3'b101), .XVal(LruCnt4), .YVal(LruCnt5), .ID(\传递最大值_3_id ), .Val(\传递最大值_3_val ));
  \传递最大值  \u_传递最大值_4  (.X(3'b110), .Y(3'b111), .XVal(LruCnt6), .YVal(LruCnt7), .ID(\传递最大值_4_id ), .Val(\传递最大值_4_val ));
  and and_25 (and_25_out, branch_HitErr, write02);
  and and_26 (and_26_out, branch_HitErr, write12);
  and and_27 (and_27_out, branch_HitErr, write22);
  and and_28 (and_28_out, branch_HitErr, write32);
  and and_29 (and_29_out, branch_HitErr, write42);
  and and_30 (and_30_out, branch_HitErr, write52);
  and and_31 (and_31_out, branch_HitErr, write62);
  and and_32 (and_32_out, branch_HitErr, write72);
  // Probe on priority_encoder_1_out
  \传递最大值  \u_传递最大值_5  (
    .X(\传递最大值_1_id ), .Y(\传递最大值_2_id ), .XVal(\传递最大值_1_val ), .YVal(\传递最大值_2_val ), .ID(\传递最大值_5_id ),
    .Val(\传递最大值_5_val ));
  \传递最大值  \u_传递最大值_6  (
    .X(\传递最大值_3_id ), .Y(\传递最大值_4_id ), .XVal(\传递最大值_3_val ), .YVal(\传递最大值_4_val ), .ID(\传递最大值_6_id ),
    .Val(\传递最大值_6_val ));
  and and_33 (full, valid0, valid1, valid2, valid3, valid4, valid5, valid6, valid7);
  \传递最大值  \u_传递最大值_7  (
    .X(\传递最大值_5_id ), .Y(\传递最大值_6_id ), .XVal(\传递最大值_5_val ), .YVal(\传递最大值_6_val ), .ID(\传递最大值_7_id ),
    .Val(LruCntMax));
  or or_11 (write0, write01, and_25_out);
  or or_12 (write1, write11, and_26_out);
  or or_13 (write2, write21, and_27_out);
  or or_14 (write3, write31, and_28_out);
  or or_15 (write4, write41, and_29_out);
  or or_16 (write5, write51, and_30_out);
  or or_17 (write6, write61, and_31_out);
  or or_18 (write7, write71, and_32_out);
  // Probe on full
  Multiplexer #(.select(1), .width(3), .disabled("Z"), .enable("false")) multiplexer_1 (
    .in0(priority_encoder_1_out), .in1(\传递最大值_7_id ), .out(multiplexer_1_out), .sel(full));
  // Probe on multiplexer_1_out
  Decoder #(.select(3), .tristate("false"), .disabled("Z"), .enable("false")) decoder_1 (
    .out0(write02), .out1(write12), .out2(write22), .out3(write32), .out4(write42), .out5(write52),
    .out6(write62), .out7(write72), .sel(multiplexer_1_out));
  not not_3 (not_3_out, WriteHit);
  and and_34 (branch_HitErr, not_3_out, EX_IsBranchIR);
  \双位预测状态转换图  \u_双位预测状态转换图_1  (
    .\val_高位 (\预测历史位1 [1]), .\val_低位 (\预测历史位1 [0]), .IsJump(EX_BranchTaken),
    .\输出_高位 (\双位预测状态转换图_1_输出_低位 [1]), .\输出_低位 (\双位预测状态转换图_1_输出_低位 [0]));
  \双位预测状态转换图  \u_双位预测状态转换图_2  (
    .\val_高位 (\预测历史位3 [1]), .\val_低位 (\预测历史位3 [0]), .IsJump(EX_BranchTaken),
    .\输出_高位 (\双位预测状态转换图_2_输出_低位 [1]), .\输出_低位 (\双位预测状态转换图_2_输出_低位 [0]));
  \双位预测状态转换图  \u_双位预测状态转换图_3  (
    .\val_高位 (\预测历史位4 [1]), .\val_低位 (\预测历史位4 [0]), .IsJump(EX_BranchTaken),
    .\输出_高位 (\双位预测状态转换图_3_输出_低位 [1]), .\输出_低位 (\双位预测状态转换图_3_输出_低位 [0]));
  \双位预测状态转换图  \u_双位预测状态转换图_4  (
    .\val_高位 (\预测历史位5 [1]), .\val_低位 (\预测历史位5 [0]), .IsJump(EX_BranchTaken),
    .\输出_高位 (\双位预测状态转换图_4_输出_低位 [1]), .\输出_低位 (\双位预测状态转换图_4_输出_低位 [0]));
  \双位预测状态转换图  \u_双位预测状态转换图_5  (
    .\val_高位 (\预测历史位6 [1]), .\val_低位 (\预测历史位6 [0]), .IsJump(EX_BranchTaken),
    .\输出_高位 (\双位预测状态转换图_5_输出_低位 [1]), .\输出_低位 (\双位预测状态转换图_5_输出_低位 [0]));
  \双位预测状态转换图  \u_双位预测状态转换图_6  (
    .\val_高位 (\预测历史位7 [1]), .\val_低位 (\预测历史位7 [0]), .IsJump(EX_BranchTaken),
    .\输出_高位 (\双位预测状态转换图_6_输出_低位 [1]), .\输出_低位 (\双位预测状态转换图_6_输出_低位 [0]));
  \双位预测状态转换图  \u_双位预测状态转换图_7  (
    .\val_高位 (\预测历史位0 [1]), .\val_低位 (\预测历史位0 [0]), .IsJump(EX_BranchTaken),
    .\输出_高位 (\双位预测状态转换图_7_输出_低位 [1]), .\输出_低位 (\双位预测状态转换图_7_输出_低位 [0]));
  \双位预测状态转换图  \u_双位预测状态转换图_8  (
    .\val_高位 (\预测历史位2 [1]), .\val_低位 (\预测历史位2 [0]), .IsJump(EX_BranchTaken),
    .\输出_高位 (\双位预测状态转换图_8_输出_低位 [1]), .\输出_低位 (\双位预测状态转换图_8_输出_低位 [0]));
  Multiplexer #(.select(1), .width(2), .disabled("Z"), .enable("false")) multiplexer_2 (
    .in0(2'b00), .in1(2'b10), .out(multiplexer_2_out), .sel(EX_BranchTaken));
  Multiplexer #(.select(1), .width(2), .disabled("Z"), .enable("false")) multiplexer_3 (
    .in0(2'b00), .in1(2'b10), .out(multiplexer_3_out), .sel(EX_BranchTaken));
  Multiplexer #(.select(1), .width(2), .disabled("Z"), .enable("false")) multiplexer_4 (
    .in0(2'b00), .in1(2'b10), .out(multiplexer_4_out), .sel(EX_BranchTaken));
  Multiplexer #(.select(1), .width(2), .disabled("Z"), .enable("false")) multiplexer_5 (
    .in0(multiplexer_4_out), .in1(\双位预测状态转换图_7_输出_低位 ), .out(\next状态0 ), .sel(WriteHit));
  Multiplexer #(.select(1), .width(2), .disabled("Z"), .enable("false")) multiplexer_6 (
    .in0(2'b00), .in1(2'b10), .out(multiplexer_6_out), .sel(EX_BranchTaken));
  Multiplexer #(.select(1), .width(2), .disabled("Z"), .enable("false")) multiplexer_7 (
    .in0(multiplexer_6_out), .in1(\双位预测状态转换图_1_输出_低位 ), .out(\next状态1 ), .sel(WriteHit));
  Multiplexer #(.select(1), .width(2), .disabled("Z"), .enable("false")) multiplexer_8 (
    .in0(2'b00), .in1(2'b10), .out(multiplexer_8_out), .sel(EX_BranchTaken));
  Multiplexer #(.select(1), .width(2), .disabled("Z"), .enable("false")) multiplexer_9 (
    .in0(multiplexer_8_out), .in1(\双位预测状态转换图_8_输出_低位 ), .out(\next状态2 ), .sel(WriteHit));
  Multiplexer #(.select(1), .width(2), .disabled("Z"), .enable("false")) multiplexer_10 (
    .in0(2'b00), .in1(2'b10), .out(multiplexer_10_out), .sel(EX_BranchTaken));
  Multiplexer #(.select(1), .width(2), .disabled("Z"), .enable("false")) multiplexer_11 (
    .in0(multiplexer_10_out), .in1(\双位预测状态转换图_2_输出_低位 ), .out(\next状态3 ), .sel(WriteHit));
  Multiplexer #(.select(1), .width(2), .disabled("Z"), .enable("false")) multiplexer_12 (
    .in0(2'b00), .in1(2'b10), .out(multiplexer_12_out), .sel(EX_BranchTaken));
  Multiplexer #(.select(1), .width(2), .disabled("Z"), .enable("false")) multiplexer_13 (
    .in0(multiplexer_12_out), .in1(\双位预测状态转换图_3_输出_低位 ), .out(\next状态4 ), .sel(WriteHit));
  Multiplexer #(.select(1), .width(2), .disabled("Z"), .enable("false")) multiplexer_14 (
    .in0(multiplexer_2_out), .in1(\双位预测状态转换图_4_输出_低位 ), .out(\next状态5 ), .sel(WriteHit));
  Multiplexer #(.select(1), .width(2), .disabled("Z"), .enable("false")) multiplexer_15 (
    .in0(2'b00), .in1(2'b10), .out(multiplexer_15_out), .sel(EX_BranchTaken));
  Multiplexer #(.select(1), .width(2), .disabled("Z"), .enable("false")) multiplexer_16 (
    .in0(multiplexer_15_out), .in1(\双位预测状态转换图_5_输出_低位 ), .out(\next状态6 ), .sel(WriteHit));
  Multiplexer #(.select(1), .width(2), .disabled("Z"), .enable("false")) multiplexer_17 (
    .in0(multiplexer_3_out), .in1(\双位预测状态转换图_6_输出_低位 ), .out(\next状态7 ), .sel(WriteHit));

  // Other names for the same wires on the sheet: PredictJump = PredictIJump

  // Notes on the sheet:
  //   EX_PC: pull=down
  //   输入信息
  //   输出信息
  //   命中返回对应目标分支地址，否则返回0
  //   读命中检测
  //   命中则假设可以直接跳转，否则直接返回0不跳转
  //   写逻辑1
  //   写命中检测，命中了则直接进入命中了的
  //   写未命中，基于lru策略写入空cache或者替换
  //   写逻辑2
endmodule
module \动态分支预测  (
  output RegWrite,
  output MemWrite,
  output [31:0] IF_PC,
  output [31:0] ID_PC,
  output [31:0] EX_PC,
  output [31:0] M_PC,
  output [31:0] WB_PC,
  output [31:0] RDin,
  output [31:0] MDin,
  output [31:0] LedData
);

  wire and_1_out, and_2_out, and_3_out, and_5_out, and_6_out, and_7_out, btb_1_predictijump, CLK,
       clock_1_out, comparator_1_eq, comparator_2_eq, comparator_2_lt, comparator_3_eq, d_ff_1_q, ENS,
       EX_ALUequal, EX_ALUless, EX_AluSrcB, EX_BE, EX_BEQ, EX_BLTU, EX_BNE, EX_branch, EX_ecall,
       EX_IsBranchIR, EX_JAL, EX_JALR, EX_JUMP, EX_LBU, EX_MemToReg, EX_MemWrite, EX_RegWrite, EX_Stype, Go,
       halt, ID_AluSrcB, ID_BEQ, ID_BLTU, ID_BNE, ID_ecall, ID_JAL, ID_JALR, ID_LBU, ID_MemToReg,
       ID_MemWrite, ID_RegWrite, ID_Stype, ID_URET, IR1, IR2, IR3, load, locker_1_1_output,
       locker_1_2_output, MEM_AluSrcB, MEM_BE, MEM_BEQ, MEM_BLTU, MEM_BNE, MEM_ecall, MEM_JAL, MEM_JALR,
       MEM_LBU, MEM_MemToReg, MEM_RegWrite, MEM_Stype, nand_1_out, nor_1_out, not_1_out, not_3_out,
       not_4_out, not_5_out, not_6_out, or_1_out, or_2_out, or_7_out, PredictError, RST, W1, W2, W3,
       WB_AluSrcB, WB_BE, WB_BEQ, WB_BLTU, WB_BNE, WB_ecall, WB_JAL, WB_JALR, WB_LBU, WB_MemToReg,
       WB_MemWrite, WB_Stype, \单周期硬布线控制器_1_rsread , \单周期硬布线控制器_1_rtread ;
  wire [1:0] EX_RSGO, EX_RTGO, ID_RSGO, ID_RTGO;
  wire [3:0] EX_AluOP, ID_AluOP, MEM_AluOP, WB_AluOP;
  wire [4:0] EX_W_num, MEM_W_num, RS_id, RT_id, WB_W_num;
  wire [7:0] multiplexer_12_out;
  wire [11:0] multiplexer_6_out;
  wire [12:0] CNT_num;
  wire [15:0] \LoadUse次数 , \总周期数 , \插入气泡数 , \无条件分支数 , \条件分支成功数 ;
  wire [31:0] bit_extender_2_out, bit_extender_3_out, bit_extender_4_out, btb_1_jumpaddr, EX_BEADDR, EX_IMM,
       EX_IR, EX_JALADDR, EX_NEXTADDR, EX_PCP4, EX_R1, EX_R2, EX_Result, ID_BEADDR, id_ex_1_r1out,
       id_ex_1_r2out, ID_IMM, ID_IR, ID_JALADDR, ID_PCP4, ID_R1, ID_R2, IF_IR, IF_PCP4, MEM_ALUOUT,
       MEM_BEADDR, MEM_IMM, MEM_IR, MEM_JALADDR, MEM_PCP4, MEM_R1, mem_wb_1_aluresultout, mem_wb_1_memout,
       multiplexer_1_out, multiplexer_2_out, multiplexer_9_out, multiplexer_10_out, multiplexer_13_out,
       multiplexer_14_out, PCnext, ram_1_data, shifter_1_out, shifter_2_out, WB_BEADDR, WB_IR, WB_JALADDR,
       WB_PCP4, WB_R1, WB_R2;

  Button \u_总复位  (.out(RST));
  Button _1 (.out(IR1));
  Button _2 (.out(IR2));
  Button _3 (.out(IR3));
  // Probe on \总周期数 
  // Probe on \总周期数 
  Button \u_继续运行  (.out(Go));
  LED #(.active("true")) led_1 (.in(W1));
  LED #(.active("true")) led_2 (.in(W2));
  LED #(.active("true")) led_3 (.in(W3));
  and and_1 (and_1_out, not_1_out, CLK);
  not not_1 (not_1_out, WB_ecall);
  Hex_Digit_Display hex_digit_display_1 (.value(LedData[31:28]));  // open: dp
  // Probe on IF_PC[19:0]
  // RiscV_Probe riscv_probe_1: pin names not known; wires that end beside it: IF_IR
  not not_2 (ENS, halt);
  Counter #(.width(16), .max('hffff), .ongoal("wrap"), .trigger("rising"), .behavior("new")) counter_1 (
    .D({16{1'b0}}), .Q(\总周期数 ), .clk(and_1_out));  // open: load, count, carry, clr, preset, down
  Hex_Digit_Display hex_digit_display_2 (.value(LedData[23:20]));  // open: dp
  Hex_Digit_Display hex_digit_display_3 (.value(LedData[27:24]));  // open: dp
  // Probe on ID_PC[19:0]
  // RiscV_Probe riscv_probe_2: pin names not known; wires that end beside it: ID_IR
  Register #(.width(32), .trigger("rising"), .Select("low")) PC (
    .D(PCnext), .en(not_3_out), .Q(IF_PC), .clk(CLK), .clr(RST));
  not not_3 (not_3_out, or_1_out);
  or or_1 (or_1_out, load, halt);
  Hex_Digit_Display hex_digit_display_4 (.value(LedData[15:12]));  // open: dp
  Hex_Digit_Display hex_digit_display_5 (.value(LedData[19:16]));  // open: dp
  Adder #(.width(32)) adder_1 (.a(IF_PC), .b(32'h4), .out(IF_PCP4));  // open: cin, cout
  Hex_Digit_Display hex_digit_display_6 (.value(LedData[11:8]));  // open: dp
  Hex_Digit_Display hex_digit_display_7 (.value(LedData[7:4]));  // open: dp
  // Probe on EX_PC[19:0]
  // RiscV_Probe riscv_probe_3: pin names not known; wires that end beside it: EX_IR
  Hex_Digit_Display hex_digit_display_8 (.value(LedData[3:0]));  // open: dp
  ROM #(.addrWidth(10), .dataWidth(32), .Select("high")) rom_1 (.addr(IF_PC[11:2]), .data(IF_IR));
  BTB btb_1 (
    .CLK(CLK), .EX_IsBranchIR(EX_IsBranchIR), .EX_BranchTaken(EX_branch), .PredictIJump(btb_1_predictijump),
    .PC(IF_PC), .EX_PC(EX_PC), .EX_BranchAddr(EX_NEXTADDR), .JumpAddr(btb_1_jumpaddr));
  Multiplexer #(.select(1), .width(32), .disabled("Z"), .enable("false")) multiplexer_1 (
    .in0(IF_PCP4), .in1(btb_1_jumpaddr), .out(multiplexer_1_out), .sel(btb_1_predictijump));
  Multiplexer #(.select(1), .width(32), .disabled("Z"), .enable("false")) multiplexer_2 (
    .in0(EX_PCP4), .in1(EX_NEXTADDR), .out(multiplexer_2_out), .sel(EX_branch));
  // Probe on \总周期数 
  // Probe on M_PC[19:0]
  // RiscV_Probe riscv_probe_4: pin names not known; wires that end beside it: MEM_IR
  // RiscV_Probe riscv_probe_5: pin names not known; wires that end beside it: IF_IR
  Comparator #(.width(32), .mode("twosComplement")) comparator_1 (
    .a(WB_R1), .b(32'h22), .eq(comparator_1_eq));  // open: gt, lt
  // Probe on \总周期数 
  // Probe on \无条件分支数 
  // Probe on \条件分支成功数 
  // Probe on \插入气泡数 
  // Probe on \LoadUse次数 
  IF_ID if_id_1 (
    .CLK(CLK), .IRin(IF_IR), .IRout(ID_IR), .PCP4in(IF_PCP4), .PCP4out(ID_PCP4), .EN(nor_1_out),
    .RESET(PredictError), .PCin(IF_PC), .PCout(ID_PC));
  nor nor_1 (nor_1_out, halt, load);
  Locker_1 locker_1_1 (
    .CLK(CLK), .EN(nor_1_out), .RST(PredictError), .\input (btb_1_predictijump), .\output (locker_1_1_output));
  Multiplexer #(.select(1), .width(32), .disabled("Z"), .enable("false")) multiplexer_3 (
    .in0(multiplexer_1_out), .in1(multiplexer_2_out), .out(PCnext), .sel(PredictError));
  not not_4 (not_4_out, comparator_1_eq);
  // Probe on IF_PC[11:0]
  // Probe on WB_PC[19:0]
  // RiscV_Probe riscv_probe_6: pin names not known; wires that end beside it: WB_IR
  // RiscV_Probe riscv_probe_7: pin names not known; wires that end beside it: ID_IR
  not not_5 (not_5_out, Go);
  and and_2 (and_2_out, not_4_out, WB_ecall);
  and and_3 (and_3_out, comparator_1_eq, WB_ecall);
  // Probe on ID_PC[11:0]
  // Probe on EX_PC[11:0]
  and and_4 (halt, not_5_out, and_2_out);
  // Probe on M_PC[11:0]
  D_Flip_Flop #(.trigger("high"), .Pre_Clr_Positions("LEGACY"), .NegatePresetClear("false"), .enable("true"), .NewFFLayout("false")) d_ff_1 (.Q(d_ff_1_q));  // open: clk, D, Qn, preset, en, reset
  // Probe on 13'hc
  Register #(.width(32), .trigger("rising"), .Select("low")) register_1 (
    .D(WB_R2), .en(and_3_out), .Q(LedData), .clk(CLK));  // open: clr
  // Probe on WB_PC[11:0]
  Comparator #(.width(13), .mode("twosComplement")) comparator_2 (
    .a(CNT_num), .b(13'hc), .eq(comparator_2_eq), .lt(comparator_2_lt));  // open: gt
  Clock #(.highDuration(1), .lowDuration(1)) clock_1 (.out(clock_1_out));
  nand nand_1 (nand_1_out, d_ff_1_q, comparator_2_eq);
  Counter #(.width(13), .max('h1fff), .ongoal("stay"), .trigger("rising"), .behavior("old")) counter_2 (
    .count(comparator_2_lt), .Q(CNT_num), .clk(clock_1_out));  // open: load, D, carry, clr, preset
  assign CLK = nand_1_out ? clock_1_out : 1'bz;  // Controlled_Buffer controlled_buffer_1
  \重定向判决  \u_重定向判决_1  (
    .RSU(\单周期硬布线控制器_1_rsread ), .RTU(\单周期硬布线控制器_1_rtread ), .RSid(RS_id), .RTid(RT_id),
    .EX_reg_write(EX_RegWrite), .MEM_reg_write(MEM_RegWrite), .EX_Wid(EX_W_num), .MEM_Wid(MEM_W_num),
    .EX_memtoreg(EX_MemToReg), .RSGO(ID_RSGO), .RTGO(ID_RTGO), .load(load));
  \单周期硬布线控制器  \u_单周期硬布线控制器_1  (
    .Funct({ID_IR[30], ID_IR[25], ID_IR[14:12]}), .OP(ID_IR[6:2]), .ALU_OP(ID_AluOP), .MemToReg(ID_MemToReg),
    .MemWrite(ID_MemWrite), .ALU_SRC(ID_AluSrcB), .ecall(ID_ecall), .S_type(ID_Stype), .Jalr(ID_JALR),
    .Beq(ID_BEQ), .JAL(ID_JAL), .Bne(ID_BNE), .in_3(ID_IR[21]), .uret(ID_URET), .LBU(ID_LBU), .BLTU(ID_BLTU),
    .RSread(\单周期硬布线控制器_1_rsread ), .RTread(\单周期硬布线控制器_1_rtread ), .RegWrite(ID_RegWrite));  // open: CSC
  Multiplexer #(.select(1), .width(5), .disabled("Z"), .enable("false")) multiplexer_4 (
    .in0(ID_IR[19:15]), .in1(5'b10001), .out(RS_id), .sel(ID_ecall));
  Multiplexer #(.select(1), .width(5), .disabled("Z"), .enable("false")) multiplexer_5 (
    .in0(ID_IR[24:20]), .in1(5'b01010), .out(RT_id), .sel(ID_ecall));
  Multiplexer #(.select(1), .width(12), .disabled("Z"), .enable("false")) multiplexer_6 (
    .in0(ID_IR[31:20]), .in1({ID_IR[31:25], ID_IR[11:7]}), .out(multiplexer_6_out), .sel(ID_Stype));
  Pull_Resistor #(.pull(1)) pull_resistor_1 (.node(CLK));
  assign ID_IMM = {{20{multiplexer_6_out[11]}}, multiplexer_6_out};  // Bit_Extender bit_extender_1
  assign bit_extender_2_out = {{20{ID_IR[31]}}, {ID_IR[31], ID_IR[7], ID_IR[30:25], ID_IR[11:8]}};  // Bit_Extender bit_extender_2
  assign bit_extender_3_out = {{12{ID_IR[31]}}, {ID_IR[31], ID_IR[19:12], ID_IR[20], ID_IR[30:21]}};  // Bit_Extender bit_extender_3
  Shifter #(.width(32), .shift("ll")) shifter_1 (.in(bit_extender_2_out), .\dist (5'b00001), .out(shifter_1_out));
  Shifter #(.width(32), .shift("ll")) shifter_2 (.in(bit_extender_3_out), .\dist (5'b00001), .out(shifter_2_out));
  Regifile regifile_1 (
    .Din(RDin), .Clk(CLK), .R1(ID_R1), .R2(ID_R2), .WE(RegWrite), .W_num(WB_W_num), .R1_num(RS_id),
    .R2_num(RT_id));
  Adder #(.width(32)) adder_2 (.a(shifter_1_out), .b(ID_PC), .out(ID_BEADDR), .cin(1'b0));  // open: cout
  Adder #(.width(32)) adder_3 (.a(shifter_2_out), .b(ID_PC), .out(ID_JALADDR), .cin(1'b0));  // open: cout
  ID_EX id_ex_1 (
    .CLK(CLK), .EN(ENS), .RESET(or_2_out), .RegWritein(ID_RegWrite), .MemToRegin(ID_MemToReg),
    .MemWritein(ID_MemWrite), .ALUOPin(ID_AluOP), .ALUSrcin(ID_AluSrcB), .ecallin(ID_ecall),
    .Stypein(ID_Stype), .BEQin(ID_BEQ), .BNEin(ID_BNE), .JALRin(ID_JALR), .BLTUin(ID_BLTU), .JALin(ID_JAL),
    .RegWriteout(EX_RegWrite), .MemToRegout(EX_MemToReg), .MemWriteout(EX_MemWrite), .ALUOPout(EX_AluOP),
    .ALUSrcout(EX_AluSrcB), .ecallout(EX_ecall), .Stypeout(EX_Stype), .BEQout(EX_BEQ), .BNEout(EX_BNE),
    .JALout(EX_JAL), .JALRout(EX_JALR), .LBUin(ID_LBU), .LBUout(EX_LBU), .BLTUout(EX_BLTU), .R1in(ID_R1),
    .R1out(id_ex_1_r1out), .R2in(ID_R2), .R2out(id_ex_1_r2out), .W_in(ID_IR[11:7]), .W_out(EX_W_num),
    .Immin(ID_IMM), .Immout(EX_IMM), .BEADDRin(ID_BEADDR), .BEADDRout(EX_BEADDR), .PCin(ID_PC),
    .PCout(EX_PC), .PCP4in(ID_PCP4), .PCP4out(EX_PCP4), .JALADDrin(ID_JALADDR), .JALADDRout(EX_JALADDR),
    .IRin(ID_IR), .IRout(EX_IR), .RSGOin(ID_RSGO), .RSGOout(EX_RSGO), .RTGOin(ID_RTGO), .RTGOout(EX_RTGO));
  or or_2 (or_2_out, PredictError, load);
  Locker_1 locker_1_2 (.CLK(CLK), .EN(ENS), .RST(or_2_out), .\input (locker_1_1_output), .\output (locker_1_2_output));
  or or_3 (EX_IsBranchIR, EX_BEQ, EX_BNE, EX_JAL, EX_JALR, EX_BLTU);
  Multiplexer #(.select(2), .width(32), .disabled("Z"), .enable("false")) multiplexer_7 (
    .in0(id_ex_1_r1out), .in1(RDin), .in2(MEM_ALUOUT), .out(EX_R1), .sel(EX_RSGO));  // open: in3
  Multiplexer #(.select(2), .width(32), .disabled("Z"), .enable("false")) multiplexer_8 (
    .in0(id_ex_1_r2out), .in1(RDin), .in2(MEM_ALUOUT), .out(EX_R2), .sel(EX_RTGO));  // open: in3
  not not_6 (not_6_out, EX_ALUequal);
  Multiplexer #(.select(1), .width(32), .disabled("Z"), .enable("false")) multiplexer_9 (
    .in0(EX_BEADDR), .in1(EX_JALADDR), .out(multiplexer_9_out), .sel(EX_JAL));
  Multiplexer #(.select(1), .width(32), .disabled("Z"), .enable("false")) multiplexer_10 (
    .in0(EX_R2), .in1(EX_IMM), .out(multiplexer_10_out), .sel(EX_AluSrcB));
  and and_5 (and_5_out, EX_ALUequal, EX_BEQ);
  and and_6 (and_6_out, not_6_out, EX_BNE);
  or or_4 (EX_BE, and_5_out, and_6_out, and_7_out);
  and and_7 (and_7_out, EX_ALUless, EX_BLTU);
  or or_5 (EX_JUMP, EX_JAL, EX_JALR);
  Multiplexer #(.select(1), .width(32), .disabled("Z"), .enable("false")) multiplexer_11 (
    .in0(multiplexer_9_out), .in1(EX_Result), .out(EX_NEXTADDR), .sel(EX_JALR));
  or or_6 (EX_branch, EX_BE, EX_JUMP);
  ALU alu_1 (
    .X(EX_R1), .Y(multiplexer_10_out), .AluOP(EX_AluOP), .Equal(EX_ALUequal), .Result(EX_Result),
    .out_6(EX_ALUless));  // open: Result_2, out_4
  Comparator #(.width(1), .mode("twosComplement")) comparator_3 (
    .a(locker_1_2_output), .b(EX_branch), .eq(comparator_3_eq));  // open: gt, lt
  not not_7 (PredictError, comparator_3_eq);
  EX_MEM ex_mem_1 (
    .CLK(CLK), .EN(ENS), .RESET(1'b0), .RegWritein(EX_RegWrite), .MemToRegin(EX_MemToReg),
    .MemWritein(EX_MemWrite), .ALUOPin(EX_AluOP), .ALUSrcin(EX_AluSrcB), .ecallin(EX_ecall),
    .Stypein(EX_Stype), .BEQin(EX_BEQ), .BNEin(EX_BNE), .JALin(EX_JAL), .JALRin(EX_JALR), .LBUin(EX_LBU),
    .BLTUin(EX_BLTU), .W_in(EX_W_num), .Immin(EX_IMM), .BEADDRin(EX_BEADDR), .PCin(EX_PC), .PCP4in(EX_PCP4),
    .JALADDrin(EX_JALADDR), .RegWriteout(MEM_RegWrite), .MemToRegout(MEM_MemToReg), .MemWriteout(MemWrite),
    .ALUOPout(MEM_AluOP), .ALUSrcout(MEM_AluSrcB), .ecallout(MEM_ecall), .Stypeout(MEM_Stype),
    .BEQout(MEM_BEQ), .BNEout(MEM_BNE), .JALout(MEM_JAL), .JALRout(MEM_JALR), .LBUout(MEM_LBU),
    .BLTUout(MEM_BLTU), .W_out(MEM_W_num), .Immout(MEM_IMM), .BEADDRout(MEM_BEADDR), .PCout(M_PC),
    .PCP4out(MEM_PCP4), .JALADDRout(MEM_JALADDR), .BEin(EX_BE), .BEout(MEM_BE), .ALUResultin(EX_Result),
    .ALUResultout(MEM_ALUOUT), .R1in(EX_R1), .R1out(MEM_R1), .R2in(EX_R2), .R2out(MDin), .IRin(EX_IR),
    .IRout(MEM_IR));
  RAM #(.addrWidth(10), .dataWidth(32), .bus("separate"), .Select("high")) ram_1 (
    .addr(MEM_ALUOUT[11:2]), .din(MDin), .data(ram_1_data), .str(MemWrite), .clk(CLK));  // open: sel, ld, clr
  Multiplexer #(.select(2), .width(8), .disabled("Z"), .enable("false")) multiplexer_12 (
    .in0(ram_1_data[7:0]), .in1(ram_1_data[15:8]), .in2(ram_1_data[23:16]), .in3(ram_1_data[31:24]),
    .out(multiplexer_12_out), .sel(MEM_ALUOUT[1:0]));
  assign bit_extender_4_out = {{24{1'b0}}, multiplexer_12_out};  // Bit_Extender bit_extender_4
  Multiplexer #(.select(1), .width(32), .disabled("Z"), .enable("false")) multiplexer_13 (
    .in0(ram_1_data), .in1(bit_extender_4_out), .out(multiplexer_13_out), .sel(MEM_LBU));
  MEM_WB mem_wb_1 (
    .CLK(CLK), .EN(ENS), .RESET(1'b0), .RegWritein(MEM_RegWrite), .RegWriteout(RegWrite),
    .MemToRegin(MEM_MemToReg), .MemToRegout(WB_MemToReg), .MemWritein(MemWrite), .MemWriteout(WB_MemWrite),
    .ALUOPin(MEM_AluOP), .ALUOPout(WB_AluOP), .ALUSrcin(MEM_AluSrcB), .ALUSrcout(WB_AluSrcB),
    .ecallin(MEM_ecall), .ecallout(WB_ecall), .Stypein(MEM_Stype), .Stypeout(WB_Stype), .BEQin(MEM_BEQ),
    .BEQout(WB_BEQ), .BNEin(MEM_BNE), .BNEout(WB_BNE), .JALin(MEM_JAL), .JALout(WB_JAL), .JALRin(MEM_JALR),
    .JALRout(WB_JALR), .LBUin(MEM_LBU), .LBUout(WB_LBU), .BLTUin(MEM_BLTU), .BLTUout(WB_BLTU),
    .W_in(MEM_W_num), .W_out(WB_W_num), .Memin(multiplexer_13_out), .Memout(mem_wb_1_memout),
    .BEADDRin(MEM_BEADDR), .BEADDRout(WB_BEADDR), .PCin(M_PC), .PCout(WB_PC), .PCP4in(MEM_PCP4),
    .PCP4out(WB_PCP4), .JALADDrin(MEM_JALADDR), .JALADDRout(WB_JALADDR), .BEin(MEM_BE), .BEout(WB_BE),
    .ALUResultin(MEM_ALUOUT), .ALUResultout(mem_wb_1_aluresultout), .IRin(MEM_IR), .IRout(WB_IR),
    .R1in(MEM_R1), .R1out(WB_R1), .R2in(MDin), .R2out(WB_R2));
  Multiplexer #(.select(1), .width(32), .disabled("Z"), .enable("false")) multiplexer_14 (
    .in0(mem_wb_1_aluresultout), .in1(mem_wb_1_memout), .out(multiplexer_14_out), .sel(WB_MemToReg));
  or or_7 (or_7_out, WB_JAL, WB_JALR);
  Multiplexer #(.select(1), .width(32), .disabled("Z"), .enable("false")) multiplexer_15 (
    .in0(multiplexer_14_out), .in1(WB_PCP4), .out(RDin), .sel(or_7_out));

  // Other names for the same wires on the sheet: ID_W_num[4:0] = ID_IR[11:7]; MEM_MemWrite = MemWrite;
  //   MEM_PC[31:0] = M_PC; MEM_R2[31:0] = MDin; WB_RegWrite = RegWrite

  // Notes on the sheet:
  //   中断源
  //   时空图监测，可删除
  //   中断等待指示
  //   数码管输出
  //   指令存储器
  //   contents of rom_1 (hex, n*v repeats v):
  //   100493 100006f 100493 200913 300993 100006f 100493 200913 300993 100006f 100493 200913 300993
  //   100006f 100493 200913 300993 41c000ef 100413 100493 1f49493 900533 2200893 73 24d493 48463 fedff06f
  //   900533 2200893 73 100493 249493 900533 2200893 73 48463 fedff06f 100493 1f49493 900533 2200893 73
  //   4034d493 900533 2200893 73 4044d493 900533 2200893 73 4044d493 900533 2200893 73 4044d493 900533
  //   2200893 73 4044d493 900533 2200893 73 4044d493 900533 2200893 73 4044d493 900533 2200893 73 4044d493
  //   900533 2200893 73 100413 1f41993 41f9d993 433 c00913 300b13 140413 f47413 800293 100313 499993
  //   89e9b3 1300533 2200893 73 406282b3 fe0294e3 140413 f00f93 1f47433 1c41413 800293 100313 49d993
  //   89e9b3 1300533 2200893 73 406282b3 fe0294e3 1c45413 406b0b33 b0463 f95ff06f 2b3 fff2c293 829293
  //   ff2e293 500533 2200893 73 fff00413 493 84a023 140413 448493 84a023 140413 448493 84a023 140413
  //   448493 84a023 140413 448493 84a023 140413 448493 84a023 140413 448493 84a023 140413 448493 84a023
  //   140413 448493 84a023 140413 448493 84a023 140413 448493 84a023 140413 448493 84a023 140413 448493
  //   84a023 140413 448493 84a023 140413 448493 84a023 140413 448493 84a023 140413 448493 140413 433
  //   3c00493 42983 4aa03 149a2b3 28663 134a023 1442023 ffc48493 fe9412e3 800533 2200893 73 440413 3c00493
  //   fc9416e3 3200893 73 100293 300313 800493 849493 7648493 1449493 900533 2200893 73 800e13 4054d4b3
  //   4064d4b3 900533 2200893 73 fffe0e13 fe0e14e3 a00893 73 13 430497 900533 2200893 73 430497 900533
  //   2200893 73 430497 900533 2200893 73 430497 900533 2200893 73 430497 900533 2200893 73 430497 900533
  //   2200893 73 430497 900533 2200893 73 430497 900533 2200893 73 a00893 73 313 1000e13 8400493 849493
  //   8348493 400913 891913 490913 849493 8248493 849493 8148493 891913 490913 891913 490913 932023
  //   12484b3 430313 fffe0e13 fe0e18e3 2000e13 313 35483 900533 2200893 73 230313 fffe0e13 fe0e14e3 a00893
  //   73 ff100493 900533 2200893 73 148493 fe04c8e3 a00893 73 a00893 73 413 140413 800533 2200893 73
  //   240413 800533 2200893 73 340413 800533 2200893 73 440413 800533 2200893 73 540413 800533 2200893 73
  //   640413 800533 2200893 73 740413 800533 2200893 73 840413 800533 2200893 2200893 73 8067
  //   IR
  //   PC
  //   PC+4
  //   控制位
  //   流水调试日志用
  //   暂停节拍，不能为0
  //   戳工具置1进入计数暂停模式，ctrl+k时钟自动运行到对应节拍暂停
  //   ctrl+k关闭时钟连续运行，将控制位置零，进入单步调试模式调试
  //   JAL
  //   JALR
  //   URET
  //   可计数暂停的时钟源
  //   Beq
  //   Bne
  //   MemToReg
  //   MemWrite
  //   AluOP
  //   AluSrcB
  //   RegWrite
  //   为方便自动评测，需要输出流水线各段保存的PC值，注意是PC不是PC+4，另外ID段寄存器写入信息，Mem段内存写入信息也要输出
  //   险象，70周期，预期锁存器先传过去，使得 PredictError 不会变成1，但这里 PredictError先变为1，导致被清零了
endmodule

module Locker_1 (
  input  CLK,
  input  EN,
  input  RST,
  input  \input ,
  output \output 
);

  wire multiplexer_1_out;

  Multiplexer #(.select(1), .width(1), .disabled("Z"), .enable("false")) multiplexer_1 (
    .in0(\input ), .in1(1'b0), .out(multiplexer_1_out), .sel(RST));
  Register #(.width(1), .trigger("rising"), .Select("low")) register_1 (
    .D(multiplexer_1_out), .en(EN), .Q(\output ), .clk(CLK));  // open: clr
endmodule
